// Logisim project CPU.circ as structural Verilog: 27 circuits, main circuit stepper
module PC (
  input  HALT,
  input  RESUME,
  input  RESET
);

  wire and_1_out, and_2_out, and_3_out, and_4_out, buffer_1_out_2, cpu_1_out_5, cpu_1_out_8, cpu_1_out_9,
       cpu_1_out_10, cpu_1_out_13, cpu_1_out_14, cpu_1_out_15, d_ff_1_q, keyboard_1_avail, keyboard_3_out_5,
       nor_1_out, not_1_out, not_2_out, not_3_out, not_4_out, not_5_out, or_1_out, ram_1_raise_error;
  wire [3:0] cpu_1_out_7, cpu_1_out_17, number_display_1_out_3, number_display_1_out_4,
       number_display_1_out_5, number_display_1_out_6, number_display_1_out_7, number_display_1_out_8,
       number_display_1_out_9, number_display_1_out_10;
  wire [6:0] keyboard_1_data, keyboard_2_data;
  wire [31:0] rom_1_out_4;

  Keyboard keyboard_1 (.clk(buffer_1_out_2), .avail(keyboard_1_avail), .data(keyboard_1_data));  // open: re, clr
  nor nor_1 (nor_1_out, ~keyboard_1_avail, buffer_1_out_2);  // NOR_Gate
  buffer buffer_1 (.in_1(nor_1_out), .out_2(buffer_1_out_2));
  ROM rom_1 (.in_1(rom_1_out_4), .in_3(cpu_1_out_5), .out_4(rom_1_out_4), .in_2(cpu_1_out_15));
  or or_1 (or_1_out, HALT, ram_1_raise_error);
  CPU cpu_1 (
    .in_1(rom_1_out_4), .out_5(cpu_1_out_5), .out_13(cpu_1_out_13), .out_14(cpu_1_out_14),
    .out_15(cpu_1_out_15), .out_6(rom_1_out_4), .in_2(or_1_out), .in_4(RESET), .out_17(cpu_1_out_17[0]),
    .out_16(cpu_1_out_17[1]), .out_11(cpu_1_out_17[2]), .out_12(cpu_1_out_17[3]), .out_7(cpu_1_out_7),
    .out_8(cpu_1_out_8), .out_9(cpu_1_out_9), .out_10(cpu_1_out_10), .in_3(RESUME));
  RAM ram_1 (
    .in_6(cpu_1_out_5), .in_5(cpu_1_out_13), .in_7(cpu_1_out_14), .in_2(cpu_1_out_7), .in_3(cpu_1_out_9),
    .in_8(cpu_1_out_8), .out_9(rom_1_out_4), .in_4(rom_1_out_4), .in_1(cpu_1_out_10),
    .RAISE_ERROR(ram_1_raise_error));
  not not_1 (not_1_out, rom_1_out_4[0]);
  not not_2 (not_2_out, rom_1_out_4[1]);
  not not_3 (not_3_out, rom_1_out_4[5]);
  not not_4 (not_4_out, rom_1_out_4[7]);
  Keyboard keyboard_2 (.clk(keyboard_3_out_5), .data(keyboard_2_data));  // open: re, clr, avail
  NUMBER_DISPLAY number_display_1 (
    .in_1(rom_1_out_4), .in_2(cpu_1_out_17), .out_3(number_display_1_out_3), .out_4(number_display_1_out_4),
    .out_5(number_display_1_out_5), .out_6(number_display_1_out_6), .out_7(number_display_1_out_7),
    .out_8(number_display_1_out_8), .out_9(number_display_1_out_9), .out_10(number_display_1_out_10));
  Hex_Digit_Display hex_digit_display_1 (.value(number_display_1_out_3));  // open: dp
  TTY tty_1 (.data(keyboard_1_data), .clk(buffer_1_out_2));  // open: we, clr
  TTY tty_2 (.data(rom_1_out_4[6:0]), .clk(and_4_out));  // open: we, clr
  and and_1 (and_1_out, 1'b1, not_1_out, not_2_out, rom_1_out_4[2], rom_1_out_4[3], rom_1_out_4[4], not_3_out, rom_1_out_4[6], not_4_out);
  not not_5 (not_5_out, cpu_1_out_17[2]);
  KEYBOARD keyboard_3 (
    .out_4(rom_1_out_4), .in_1(keyboard_2_data), .in_2(rom_1_out_4), .in_3(cpu_1_out_17),
    .out_5(keyboard_3_out_5));
  Hex_Digit_Display hex_digit_display_2 (.value(number_display_1_out_5));  // open: dp
  Hex_Digit_Display hex_digit_display_3 (.value(number_display_1_out_4));  // open: dp
  D_Flip_Flop d_ff_1 (.clk(and_2_out), .D(and_1_out), .Q(d_ff_1_q));  // open: Qn, preset, en, reset
  and and_2 (and_2_out, cpu_1_out_17[0], cpu_1_out_17[2], cpu_1_out_17[3]);
  and and_3 (and_3_out, cpu_1_out_17[0], cpu_1_out_17[3], not_5_out);
  Hex_Digit_Display hex_digit_display_4 (.value(number_display_1_out_6));  // open: dp
  Hex_Digit_Display hex_digit_display_5 (.value(number_display_1_out_7));  // open: dp
  and and_4 (and_4_out, d_ff_1_q, and_3_out);
  Hex_Digit_Display hex_digit_display_6 (.value(number_display_1_out_8));  // open: dp
  Hex_Digit_Display hex_digit_display_7 (.value(number_display_1_out_9));  // open: dp
  Hex_Digit_Display hex_digit_display_8 (.value(number_display_1_out_10));  // open: dp

  // Notes on the sheet:
  //   CLOCK S
  //   CLK E
  //   D/A
  //   I/O
endmodule

module CPU (
  input  [31:0] in_1,
  input  in_2,
  input  in_3,
  input  in_4,
  output out_5,
  output [31:0] out_6,
  output [3:0] out_7,
  output out_8,
  output out_9,
  output out_10,
  output out_11,
  output out_12,
  output out_13,
  output out_14,
  output out_15,
  output out_16,
  output out_17
);

  wire alu_1_out_5, alu_1_out_6, alu_1_out_7, alu_1_out_8, clock_1_out, control_section_1_acc,
       control_section_1_acc_2, control_section_1_bus_1, control_section_1_flag, control_section_1_iar,
       control_section_1_iar_2, control_section_1_iar_plus_plus, control_section_1_in, control_section_1_ir,
       control_section_1_out, control_section_1_out_12, control_section_1_tmp, flag_reg_1_out_6,
       flag_reg_1_out_7, flag_reg_1_out_8, flag_reg_1_out_9;
  wire [5:0] control_section_1_out_34;
  wire [15:0] control_section_1_out_31, control_section_1_out_32, intruction_register_ir_1_out_3;
  wire [31:0] alu_1_a_2, controlled_buffer_2_out, tmp_1_out_4;

  assign out_6 = control_section_1_out ? controlled_buffer_2_out : 32'bz;  // Controlled_Buffer controlled_buffer_1
  assign controlled_buffer_2_out = control_section_1_in ? in_1 : 32'bz;  // Controlled_Buffer controlled_buffer_2
  TMP tmp_1 (
    .in_1(controlled_buffer_2_out), .in_2(control_section_1_tmp), .in_3(control_section_1_bus_1),
    .out_4(tmp_1_out_4));
  ALU alu_1 (
    .A(controlled_buffer_2_out), .B(tmp_1_out_4), .in_4(control_section_1_out_34), .out_5(alu_1_out_5),
    .out_6(alu_1_out_6), .out_7(alu_1_out_7), .A_2(alu_1_a_2), .in_3(flag_reg_1_out_6), .out_8(alu_1_out_8));
  ACC acc_1 (
    .in_1(alu_1_a_2), .out_4(controlled_buffer_2_out), .in_2(control_section_1_acc_2),
    .in_3(control_section_1_acc));
  Clock clock_1 (.out(clock_1_out));
  FLAG_REG flag_reg_1 (
    .in_2(alu_1_out_5), .in_3(alu_1_out_6), .in_4(alu_1_out_7), .out_7(flag_reg_1_out_7),
    .out_8(flag_reg_1_out_8), .out_9(flag_reg_1_out_9), .in_5(control_section_1_flag), .in_1(alu_1_out_8),
    .out_6(flag_reg_1_out_6));
  CPU_REG cpu_reg_1 (
    .out_4(controlled_buffer_2_out), .in_1(controlled_buffer_2_out), .in_2(control_section_1_out_31),
    .in_3(control_section_1_out_32));
  CONTROL_SECTION control_section_1 (
    .CLK(clock_1_out), .bus_1(control_section_1_bus_1), .ACC(control_section_1_acc),
    .IAR_2(control_section_1_iar_2), .I_O_CLK_E(out_16), .RAM(out_13), .MAR(out_5),
    .IAR(control_section_1_iar), .IAR_plus_plus(control_section_1_iar_plus_plus), .IR(control_section_1_ir),
    .ACC_2(control_section_1_acc_2), .TMP(control_section_1_tmp), .I_O_CLK_S(out_17),
    .FLAG(control_section_1_flag), .ROM(out_15), .RAM_2(out_14), .out_31(control_section_1_out_31),
    .out_32(control_section_1_out_32), .in_5(flag_reg_1_out_6), .in_6(flag_reg_1_out_7),
    .in_7(flag_reg_1_out_8), .in_8(flag_reg_1_out_9), .in_9(intruction_register_ir_1_out_3),
    .out_34(control_section_1_out_34), .DATA_ADDRESS(out_11), .INPUT_OUTPUT(out_12), .HALT(in_2),
    .RESET(in_4), .out_12(control_section_1_out_12), .STACK_E(out_9), .STACK_S(out_8), .STACK_OP(out_7),
    .out(control_section_1_out), .in(control_section_1_in), .ARR_E(out_10), .RESUME(in_3));
  INTRUCTION_REGISTER_IR intruction_register_ir_1 (
    .in_1(controlled_buffer_2_out), .in_2(control_section_1_ir), .out_3(intruction_register_ir_1_out_3));
  IAR iar_1 (
    .clock(control_section_1_iar_plus_plus), .reset(control_section_1_out_12), .set(control_section_1_iar),
    .in_5(controlled_buffer_2_out), .out_6(controlled_buffer_2_out), .enable(control_section_1_iar_2));

  // Notes on the sheet:
  //   FPU
endmodule

module CONTROL_SECTION (
  input  CLK,
  input  HALT,
  input  RESET,
  input  RESUME,
  input  in_5,
  input  in_6,
  input  in_7,
  input  in_8,
  input  [15:0] in_9,
  output in,
  output out,
  output out_12,
  output RAM,
  output bus_1,
  output MAR,
  output ACC,
  output IAR,
  output IAR_plus_plus,
  output IAR_2,
  output IR,
  output STACK_E,
  output ARR_E,
  output I_O_CLK_E,
  output ACC_2,
  output TMP,
  output I_O_CLK_S,
  output FLAG,
  output ROM,
  output RAM_2,
  output STACK_S,
  output [15:0] out_31,
  output [15:0] out_32,
  output [3:0] STACK_OP,
  output [5:0] out_34,
  output DATA_ADDRESS,
  output INPUT_OUTPUT
);

  wire A_2_out, A_out, and_1_out, and_11_out, and_12_out, and_17_out, and_18_out, and_19_out, and_20_out,
       and_21_out, and_22_out, and_23_out, and_24_out, and_25_out, and_26_out, and_27_out, and_28_out,
       and_29_out, and_30_out, and_31_out, and_32_out, and_33_out, and_34_out, and_35_out, and_36_out,
       and_37_out, and_38_out, and_39_out, and_40_out, and_41_out, and_42_out, and_43_out, and_44_out,
       and_45_out, and_46_out, and_47_out, and_48_out, and_49_out, and_50_out, and_51_out, and_52_out,
       and_53_out, and_54_out, and_55_out, and_56_out, and_57_out, and_58_out, and_59_out, and_60_out,
       and_61_out, and_62_out, and_63_out, and_64_out, and_65_out, and_66_out, and_67_out, and_68_out,
       and_69_out, and_70_out, and_71_out, and_72_out, and_73_out, and_74_out, and_75_out, and_76_out,
       and_77_out, and_78_out, and_89_out, C_2_out, C_out, clock_1_out_2, clock_1_out_3, clock_1_out_4,
       d_ff_1_q, decoder_3_out0, decoder_3_out1, decoder_3_out2, decoder_3_out3, decoder_3_out4,
       decoder_3_out5, decoder_3_out6, decoder_3_out7, decoder_3_out8, decoder_3_out9, decoder_3_out10,
       decoder_3_out11, decoder_3_out12, decoder_3_out13, decoder_3_out14, decoder_3_out15, decoder_4_out0,
       decoder_4_out1, decoder_4_out2, decoder_4_out3, decoder_4_out4, decoder_4_out5, demultiplexer_1_out2,
       demultiplexer_2_out0, demultiplexer_2_out1, demultiplexer_2_out2, demultiplexer_2_out3,
       demultiplexer_2_out4, demultiplexer_2_out5, demultiplexer_3_out0, demultiplexer_3_out1,
       demultiplexer_3_out2, demultiplexer_3_out3, demultiplexer_3_out4, demultiplexer_3_out5, N_2_out,
       N_out, nand_1_out, nor_1_out, not_1_out, not_2_out, not_3_out, not_4_out, not_5_out, not_6_out,
       not_7_out, not_8_out, not_9_out, not_10_out, not_11_out, not_12_out, not_13_out, or_1_out, or_3_out,
       or_4_out, or_5_out, or_6_out, or_7_out, or_8_out, or_9_out, or_10_out, or_12_out, or_13_out,
       or_14_out, or_15_out, or_16_out, or_17_out, or_18_out, or_19_out, or_20_out, or_21_out, or_23_out,
       or_24_out, or_25_out, or_26_out, or_27_out, or_28_out, or_29_out, or_30_out, or_31_out, or_33_out,
       or_34_out, or_35_out, or_36_out, or_37_out, or_38_out, or_39_out, or_40_out, R0_2_out, R0_out,
       stepper_1_out_3, Z_2_out, Z_out;
  wire [3:0] stepper_1_out_4;
  wire [14:0] pull_resistor_5_node;
  wire [15:0] decoder_1_out0, decoder_2_out0, decoder_5_out0, or_2_out, pull_resistor_2_node,
       pull_resistor_3_node, pull_resistor_4_node;
  wire [15:1] pull_resistor_1_node;

  or or_1 (or_1_out, HALT, d_ff_1_q, RESET);
  not not_1 (not_1_out, CLK);
  nand nand_1 (nand_1_out, or_1_out, decoder_4_out0);
  not not_2 (not_2_out, and_1_out);
  and and_1 (and_1_out, not_1_out, nand_1_out);
  and and_2 (out_12, nand_1_out, RESET);
  CLOCK clock_1 (.in_1(not_2_out), .out_2(clock_1_out_2), .out_3(clock_1_out_3), .out_4(clock_1_out_4));
  and and_3 (bus_1, clock_1_out_4, and_35_out);
  and and_4 (ACC, clock_1_out_4, or_8_out);
  and and_5 (IAR_2, clock_1_out_4, or_3_out);
  and and_6 (STACK_E, clock_1_out_4, or_4_out);
  and and_7 (ARR_E, clock_1_out_4, or_18_out);
  and and_8 (I_O_CLK_E, clock_1_out_4, and_66_out);
  and and_9 (ROM, or_7_out, clock_1_out_4);
  and and_10 (RAM_2, or_7_out, clock_1_out_4);
  and R0 (R0_out, or_26_out, clock_1_out_4);
  assign or_2_out = pull_resistor_2_node | pull_resistor_3_node;  // OR_Gate or_2, 16 bits wide
  Multiplexer #(.width(16), .enable("false")) multiplexer_1 (
    .in0(or_2_out), .in1({pull_resistor_1_node, 1'b1}), .out(out_32), .sel(R0_out));
  Pull_Resistor pull_resistor_1 (.node(pull_resistor_1_node));
  or or_3 (or_3_out, or_9_out, and_27_out, and_38_out, or_14_out);
  or or_4 (or_4_out, and_67_out, demultiplexer_1_out2, and_42_out);
  and and_11 (and_11_out, clock_1_out_4, or_5_out);
  Pull_Resistor pull_resistor_2 (.node(pull_resistor_2_node));
  assign pull_resistor_2_node = and_11_out ? decoder_1_out0 : 16'bz;  // Controlled_Buffer controlled_buffer_1
  and and_12 (and_12_out, clock_1_out_4, or_6_out);
  Pull_Resistor pull_resistor_3 (.node(pull_resistor_3_node));
  assign pull_resistor_3_node = and_12_out ? decoder_2_out0 : 16'bz;  // Controlled_Buffer controlled_buffer_2
  D_Flip_Flop d_ff_1 (.Q(d_ff_1_q), .preset(and_50_out), .reset(RESUME));  // open: clk, D, Qn, en
  or or_5 (or_5_out, and_56_out, or_27_out, and_40_out, and_21_out, and_52_out, or_18_out);
  or or_6 (or_6_out, and_23_out, and_25_out, and_46_out, or_21_out, and_44_out, and_48_out);
  or or_7 (or_7_out, and_57_out, decoder_4_out1, and_55_out, or_17_out, and_53_out, and_75_out);
  Decoder #(.select(4), .enable("false")) decoder_1 (
    .out0(decoder_1_out0[0]), .out1(decoder_1_out0[1]), .out2(decoder_1_out0[2]), .out3(decoder_1_out0[3]),
    .out4(decoder_1_out0[4]), .out5(decoder_1_out0[5]), .out6(decoder_1_out0[6]), .out7(decoder_1_out0[7]),
    .out8(decoder_1_out0[8]), .out9(decoder_1_out0[9]), .out10(decoder_1_out0[10]),
    .out11(decoder_1_out0[11]), .out12(decoder_1_out0[12]), .out13(decoder_1_out0[13]),
    .out14(decoder_1_out0[14]), .out15(decoder_1_out0[15]), .sel(in_9[3:0]));
  Decoder #(.select(4), .enable("false")) decoder_2 (
    .out0(decoder_2_out0[0]), .out1(decoder_2_out0[1]), .out2(decoder_2_out0[2]), .out3(decoder_2_out0[3]),
    .out4(decoder_2_out0[4]), .out5(decoder_2_out0[5]), .out6(decoder_2_out0[6]), .out7(decoder_2_out0[7]),
    .out8(decoder_2_out0[8]), .out9(decoder_2_out0[9]), .out10(decoder_2_out0[10]),
    .out11(decoder_2_out0[11]), .out12(decoder_2_out0[12]), .out13(decoder_2_out0[13]),
    .out14(decoder_2_out0[14]), .out15(decoder_2_out0[15]), .sel(in_9[7:4]));
  stepper stepper_1 (.in_1(clock_1_out_3), .in_2(or_13_out), .out_4(stepper_1_out_4), .out_3(stepper_1_out_3));
  or or_8 (or_8_out, or_25_out, or_24_out);
  Decoder #(.select(4), .enable("false")) decoder_3 (
    .out0(decoder_3_out0), .out1(decoder_3_out1), .out2(decoder_3_out2), .out3(decoder_3_out3),
    .out4(decoder_3_out4), .out5(decoder_3_out5), .out6(decoder_3_out6), .out7(decoder_3_out7),
    .out8(decoder_3_out8), .out9(decoder_3_out9), .out10(decoder_3_out10), .out11(decoder_3_out11),
    .out12(decoder_3_out12), .out13(decoder_3_out13), .out14(decoder_3_out14), .out15(decoder_3_out15),
    .sel(in_9[11:8]));
  and and_13 (out_34[0], or_10_out, in_9[8], decoder_4_out3);
  and and_14 (out_34[1], or_10_out, in_9[9], decoder_4_out3);
  and and_15 (out_34[2], or_10_out, in_9[10], decoder_4_out3);
  and and_16 (out_34[3], or_10_out, in_9[11], decoder_4_out3);
  or or_9 (or_9_out, decoder_4_out0, and_19_out);
  not not_3 (not_3_out, in_9[14]);
  or or_10 (or_10_out, in_9[12], in_9[14]);
  or or_11 (out_34[5], or_10_out, or_17_out);
  not not_4 (not_4_out, not_5_out);
  not not_5 (not_5_out, or_10_out);
  Decoder #(.select(4), .disabled(0)) decoder_4 (
    .out0(decoder_4_out0), .out1(decoder_4_out1), .out2(decoder_4_out2), .out3(decoder_4_out3),
    .out4(decoder_4_out4), .out5(decoder_4_out5), .sel(stepper_1_out_4), .en(stepper_1_out_3));  // open: out6, out7, out8, out9, out10, out11, out12, out13, out14, out15
  or or_12 (or_12_out, decoder_4_out1, and_53_out);
  and and_17 (and_17_out, decoder_4_out2, and_18_out);
  and and_18 (and_18_out, decoder_3_out0, not_5_out);
  and and_19 (and_19_out, decoder_4_out2, and_20_out);
  and and_20 (and_20_out, not_4_out, in_9[14]);
  and and_21 (and_21_out, decoder_4_out2, and_22_out);
  and and_22 (and_22_out, not_3_out, not_4_out);
  and and_23 (and_23_out, decoder_4_out2, and_24_out);
  and and_24 (and_24_out, not_5_out, decoder_3_out1);
  and and_25 (and_25_out, decoder_4_out2, and_26_out);
  and and_26 (and_26_out, not_5_out, decoder_3_out2);
  and and_27 (and_27_out, decoder_4_out2, and_28_out);
  and and_28 (and_28_out, not_5_out, decoder_3_out3);
  and and_29 (and_29_out, decoder_4_out2, and_30_out);
  and and_30 (and_30_out, not_5_out, decoder_3_out4);
  and and_31 (and_31_out, decoder_4_out2, and_32_out);
  and and_32 (and_32_out, not_5_out, decoder_3_out5);
  and and_33 (and_33_out, decoder_4_out2, and_34_out);
  and and_34 (and_34_out, not_5_out, decoder_3_out6);
  and and_35 (and_35_out, decoder_4_out2, and_36_out);
  and and_36 (and_36_out, not_5_out, decoder_3_out7);
  and and_37 (and_37_out, not_5_out, decoder_3_out8);
  and and_38 (and_38_out, decoder_4_out2, and_39_out);
  and and_39 (and_39_out, not_5_out, decoder_3_out9);
  and and_40 (and_40_out, decoder_4_out2, and_41_out);
  and and_41 (and_41_out, not_5_out, decoder_3_out10);
  and and_42 (and_42_out, decoder_4_out2, and_43_out);
  and and_43 (and_43_out, not_5_out, decoder_3_out11);
  and and_44 (and_44_out, decoder_4_out2, and_45_out);
  and and_45 (and_45_out, not_5_out, decoder_3_out12);
  and and_46 (and_46_out, decoder_4_out2, and_47_out);
  and and_47 (and_47_out, not_5_out, decoder_3_out13);
  and and_48 (and_48_out, decoder_4_out2, and_49_out);
  and and_49 (and_49_out, not_5_out, decoder_3_out14);
  and and_50 (and_50_out, decoder_4_out2, and_51_out);
  and and_51 (and_51_out, not_5_out, decoder_3_out15);
  or or_13 (or_13_out, or_23_out, or_16_out, or_15_out, and_50_out, and_48_out);
  or or_14 (or_14_out, and_29_out, and_31_out, and_33_out);
  and and_52 (and_52_out, decoder_4_out2, in_9[5], and_37_out);
  not not_6 (not_6_out, in_5);
  not not_7 (not_7_out, in_6);
  not not_8 (not_8_out, in_7);
  not not_9 (not_9_out, in_8);
  or or_15 (or_15_out, and_35_out, and_40_out, and_38_out);
  and and_53 (and_53_out, decoder_4_out3, and_20_out);
  and and_54 (and_54_out, decoder_4_out3, and_22_out);
  and and_55 (and_55_out, decoder_4_out3, and_24_out);
  and and_56 (and_56_out, decoder_4_out3, and_26_out);
  and and_57 (and_57_out, decoder_4_out3, and_28_out);
  and and_58 (and_58_out, decoder_4_out3, and_30_out);
  and and_59 (and_59_out, decoder_4_out3, and_32_out);
  and and_60 (and_60_out, decoder_4_out3, and_34_out);
  not not_10 (not_10_out, in_9[5]);
  and and_61 (and_61_out, decoder_4_out3, and_43_out);
  and and_62 (and_62_out, decoder_4_out3, and_45_out);
  and and_63 (and_63_out, decoder_4_out3, and_47_out);
  and C (C_out, in_9[3], in_5);
  and A (A_out, in_9[2], in_6);
  and N (N_out, in_9[1], in_7);
  and Z (Z_out, in_9[0], in_8);
  and C_2 (C_2_out, in_9[3], not_6_out);
  and A_2 (A_2_out, in_9[2], not_7_out);
  and N_2 (N_2_out, in_9[1], not_8_out);
  and Z_2 (Z_2_out, in_9[0], not_9_out);
  and and_64 (and_64_out, in_9[8], in_9[9], in_9[10], in_9[11]);
  not not_11 (not_11_out, and_64_out);
  or or_16 (or_16_out, and_56_out, and_17_out, and_66_out, and_55_out, and_65_out);
  and and_65 (and_65_out, and_67_out, not_13_out);
  or or_17 (or_17_out, and_58_out, and_59_out, and_60_out);
  and and_66 (and_66_out, decoder_4_out3, not_10_out, and_37_out);
  and and_67 (and_67_out, and_61_out, not_12_out);
  or or_18 (or_18_out, and_62_out, and_63_out);
  or or_19 (or_19_out, C_out, A_out, N_out, Z_out);
  or or_20 (or_20_out, C_2_out, A_2_out, N_2_out, Z_2_out);
  or or_21 (or_21_out, and_54_out, and_68_out);
  not not_12 (not_12_out, or_26_out);
  Demultiplexer #(.select(3), .enable("false")) demultiplexer_1 (
    .out2(demultiplexer_1_out2), .in(and_74_out), .sel(in_9[6:4]));  // open: out0, out1, out3, out4, out5, out6, out7
  Demultiplexer #(.select(3), .enable("false")) demultiplexer_2 (
    .out0(demultiplexer_2_out0), .out1(demultiplexer_2_out1), .out2(demultiplexer_2_out2),
    .out3(demultiplexer_2_out3), .out4(demultiplexer_2_out4), .out5(demultiplexer_2_out5), .in(and_61_out),
    .sel(in_9[6:4]));  // open: out6, out7
  Demultiplexer #(.select(3), .enable("false")) demultiplexer_3 (
    .out0(demultiplexer_3_out0), .out1(demultiplexer_3_out1), .out2(demultiplexer_3_out2),
    .out3(demultiplexer_3_out3), .out4(demultiplexer_3_out4), .out5(demultiplexer_3_out5), .in(and_42_out),
    .sel(in_9[6:4]));  // open: out6, out7
  or or_22 (out, or_18_out, or_28_out, or_26_out, or_27_out, and_52_out);
  or or_23 (or_23_out, or_24_out, and_74_out, and_70_out, or_25_out, or_29_out, and_75_out, or_26_out);
  or or_24 (or_24_out, and_69_out, and_78_out);
  and and_68 (and_68_out, decoder_4_out4, and_20_out);
  and and_69 (and_69_out, decoder_4_out4, and_22_out, not_11_out);
  and and_70 (and_70_out, decoder_4_out4, and_28_out);
  and and_71 (and_71_out, decoder_4_out4, and_30_out);
  or or_25 (or_25_out, and_71_out, and_72_out, and_73_out);
  and and_72 (and_72_out, decoder_4_out4, or_19_out, and_32_out);
  and and_73 (and_73_out, decoder_4_out4, or_20_out, and_34_out);
  not not_13 (not_13_out, demultiplexer_2_out2);
  and and_74 (and_74_out, decoder_4_out4, and_43_out);
  and and_75 (and_75_out, decoder_4_out4, and_45_out);
  and and_76 (and_76_out, decoder_4_out4, and_47_out);
  or or_26 (or_26_out, and_76_out, demultiplexer_2_out4);
  or or_27 (or_27_out, demultiplexer_3_out0, demultiplexer_3_out4, demultiplexer_3_out5);
  or or_28 (or_28_out, or_9_out, and_23_out, and_25_out, and_27_out, or_14_out, and_44_out, and_46_out);
  or or_29 (or_29_out, demultiplexer_2_out0, or_30_out, demultiplexer_2_out3);
  or or_30 (or_30_out, demultiplexer_2_out1, demultiplexer_2_out5);
  and and_77 (and_77_out, nor_1_out, or_39_out);
  nor nor_1 (nor_1_out, and_38_out, and_48_out);
  or or_31 (or_31_out, and_42_out, and_67_out, demultiplexer_1_out2, or_18_out);
  and and_78 (and_78_out, decoder_4_out5, and_20_out);
  Decoder #(.select(4), .enable("false")) decoder_5 (
    .out0(decoder_5_out0[0]), .out1(decoder_5_out0[1]), .out2(decoder_5_out0[2]), .out3(decoder_5_out0[3]),
    .out4(decoder_5_out0[4]), .out5(decoder_5_out0[5]), .out6(decoder_5_out0[6]), .out7(decoder_5_out0[7]),
    .out8(decoder_5_out0[8]), .out9(decoder_5_out0[9]), .out10(decoder_5_out0[10]),
    .out11(decoder_5_out0[11]), .out12(decoder_5_out0[12]), .out13(decoder_5_out0[13]),
    .out14(decoder_5_out0[14]), .out15(decoder_5_out0[15]), .sel(in_9[3:0]));
  or or_32 (in, or_17_out, and_53_out, and_77_out, or_34_out, decoder_4_out1);
  or or_33 (or_33_out, and_56_out, or_26_out);
  or or_34 (or_34_out, or_25_out, and_40_out);
  or or_35 (or_35_out, or_12_out, and_70_out, or_17_out);
  or or_36 (or_36_out, or_21_out, or_17_out);
  or or_37 (or_37_out, and_53_out, or_14_out, and_21_out);
  or or_38 (or_38_out, and_35_out, or_21_out);
  or or_39 (or_39_out, and_48_out, and_38_out, and_57_out, or_24_out, and_55_out, and_66_out, or_30_out);
  or or_40 (or_40_out, or_24_out, and_75_out, demultiplexer_2_out5);
  or or_41 (STACK_OP[0], demultiplexer_2_out1, demultiplexer_3_out1, demultiplexer_2_out5, demultiplexer_3_out2, demultiplexer_3_out3);
  or or_42 (STACK_OP[1], demultiplexer_2_out2, demultiplexer_3_out0, demultiplexer_3_out2, demultiplexer_3_out3);
  or or_43 (STACK_OP[2], demultiplexer_1_out2, demultiplexer_2_out0, demultiplexer_2_out2, demultiplexer_3_out1, demultiplexer_3_out3);
  or or_44 (STACK_OP[3], demultiplexer_3_out4, demultiplexer_2_out1, demultiplexer_3_out5);
  and and_79 (RAM, clock_1_out_2, or_33_out);
  and and_80 (MAR, clock_1_out_2, or_28_out);
  and and_81 (IAR, clock_1_out_2, or_34_out);
  and and_82 (IAR_plus_plus, clock_1_out_2, or_35_out);
  and and_83 (IR, clock_1_out_2, decoder_4_out1);
  and and_84 (ACC_2, clock_1_out_2, or_36_out);
  and and_85 (TMP, clock_1_out_2, or_37_out);
  and and_86 (I_O_CLK_S, and_52_out, clock_1_out_2);
  and and_87 (FLAG, clock_1_out_2, or_38_out);
  and and_88 (STACK_S, clock_1_out_2, or_31_out);
  and and_89 (and_89_out, clock_1_out_2, or_39_out);
  and R0_2 (R0_2_out, clock_1_out_2, or_40_out);
  Pull_Resistor pull_resistor_4 (.node(pull_resistor_4_node));
  assign pull_resistor_4_node = and_89_out ? decoder_5_out0 : 16'bz;  // Controlled_Buffer controlled_buffer_3
  Pull_Resistor pull_resistor_5 (.node(pull_resistor_5_node));
  Multiplexer #(.width(16), .enable("false")) multiplexer_2 (
    .in0(pull_resistor_4_node), .in1({pull_resistor_5_node, 1'b1}), .out(out_31), .sel(R0_2_out));

  assign DATA_ADDRESS = in_9[4];
  assign INPUT_OUTPUT = in_9[5];
  assign out_34[4] = in_9[13];

  // Notes on the sheet:
  //   reg B
  //   reg A
endmodule

module ROM (
  input  [31:0] in_1,
  input  in_2,
  input  in_3,
  output [31:0] out_4
);

  wire and_1_out, not_1_out;
  wire [16:0] register_1_q;
  wire [31:0] rom_1_data;

  Register #(.width(17)) register_1 (.D(in_1[16:0]), .Q(register_1_q), .clk(in_3));  // open: en, clr
  not not_1 (not_1_out, register_1_q[16]);
  Pull_Resistor pull_resistor_1 (.node(register_1_q[16]));
  ROM_part #(.addrWidth(16), .dataWidth(32)) rom_1 (.addr(register_1_q[15:0]), .data(rom_1_data));  // open: sel
  and and_1 (and_1_out, not_1_out, in_2);
  assign out_4 = and_1_out ? rom_1_data : 32'bz;  // Controlled_Buffer controlled_buffer_1

  // Notes on the sheet:
  //   contents of rom_1 (hex, n*v repeats v):
  //   301 10 301 10 301 10 400 10
endmodule

module RAM (
  input  in_1,
  input  [3:0] in_2,
  input  in_3,
  input  [31:0] in_4,
  input  in_5,
  input  in_6,
  input  in_7,
  input  in_8,
  output [31:0] out_9,
  output RAISE_ERROR
);

  wire and_1_out, and_2_out, and_3_out, and_4_out, and_6_out, demultiplexer_1_out0, demultiplexer_1_out1,
       demultiplexer_1_out2, demultiplexer_1_out3, demultiplexer_1_out4, demultiplexer_1_out5,
       demultiplexer_1_out6, demultiplexer_1_out7, demultiplexer_1_out8, demultiplexer_1_out9, nor_1_out,
       or_1_out, or_2_out, or_3_out, or_4_out, or_5_out, or_6_out, or_7_out, or_8_out, or_9_out;
  wire [13:0] controlled_buffer_7_out, controlled_buffer_11_out, pull_resistor_3_node, pull_resistor_5_node,
       ram_1_data, register_2_q, register_3_q, subtractor_1_out;
  wire [15:0] controlled_buffer_4_out, register_1_q;
  wire [16:0] adder_1_out, controlled_buffer_1_out, controlled_buffer_10_out;
  wire [16:16] register_1_q_2;
  wire [31:14] ram_1_data_2;

  Demultiplexer #(.select(4), .disabled(0), .enable("false")) demultiplexer_1 (
    .out0(demultiplexer_1_out0), .out1(demultiplexer_1_out1), .out2(demultiplexer_1_out2),
    .out3(demultiplexer_1_out3), .out4(demultiplexer_1_out4), .out5(demultiplexer_1_out5),
    .out6(demultiplexer_1_out6), .out7(demultiplexer_1_out7), .out8(demultiplexer_1_out8),
    .out9(demultiplexer_1_out9), .in(in_3), .sel(in_2));  // open: out10, out11, out12, out13, out14, out15
  or or_1 (or_1_out, in_1, demultiplexer_1_out8);
  or or_2 (or_2_out, demultiplexer_1_out1, demultiplexer_1_out9);
  assign controlled_buffer_1_out = or_1_out ? adder_1_out : 17'bz;  // Controlled_Buffer controlled_buffer_1
  assign controlled_buffer_1_out = in_6 ? in_4[16:0] : 17'bz;  // Controlled_Buffer controlled_buffer_2
  assign in_4 = demultiplexer_1_out3 ? {{18{1'b0}}, register_2_q} : 32'bz;  // Controlled_Buffer controlled_buffer_3
  and and_1 (and_1_out, or_1_out, in_8);
  Pull_Resistor pull_resistor_1 (.node(in_4));
  or or_3 (or_3_out, demultiplexer_1_out2, demultiplexer_1_out9, demultiplexer_1_out3);
  Register #(.width(17)) register_1 (
    .D(controlled_buffer_1_out), .Q({register_1_q_2[16], register_1_q}), .clk(or_4_out));  // open: en, clr
  or or_4 (or_4_out, and_1_out, in_6);
  assign controlled_buffer_4_out = demultiplexer_1_out0 ? {2'b00, register_2_q} : 16'bz;  // Controlled_Buffer controlled_buffer_4
  assign controlled_buffer_4_out = or_3_out ? {2'b00, register_3_q} : 16'bz;  // Controlled_Buffer controlled_buffer_5
  nor nor_1 (nor_1_out, demultiplexer_1_out0, or_3_out);
  assign controlled_buffer_4_out = nor_1_out ? register_1_q : 16'bz;  // Controlled_Buffer controlled_buffer_6
  Pull_Resistor pull_resistor_2 (.node(register_1_q_2[16]));
  or or_5 (or_5_out, demultiplexer_1_out0, demultiplexer_1_out6);
  assign controlled_buffer_7_out = demultiplexer_1_out7 ? register_2_q : 14'bz;  // Controlled_Buffer controlled_buffer_7
  assign controlled_buffer_7_out = demultiplexer_1_out5 ? subtractor_1_out : 14'bz;  // Controlled_Buffer controlled_buffer_8
  assign controlled_buffer_7_out = demultiplexer_1_out4 ? adder_1_out[13:0] : 14'bz;  // Controlled_Buffer controlled_buffer_9
  assign controlled_buffer_10_out = in_1 ? {register_1_q_2[16], register_1_q} : 17'bz;  // Controlled_Buffer controlled_buffer_10
  or or_6 (or_6_out, demultiplexer_1_out2, demultiplexer_1_out3);
  assign controlled_buffer_11_out = demultiplexer_1_out0 ? ram_1_data : 14'bz;  // Controlled_Buffer controlled_buffer_11
  Register #(.width(14)) register_2 (.D(controlled_buffer_11_out), .Q(register_2_q), .clk(and_2_out));  // open: en, clr
  assign controlled_buffer_11_out = demultiplexer_1_out6 ? register_3_q : 14'bz;  // Controlled_Buffer controlled_buffer_12
  and and_2 (and_2_out, or_5_out, in_8);
  Register #(.width(14)) register_3 (.D(controlled_buffer_7_out), .Q(register_3_q), .clk(and_3_out));  // open: en, clr
  and and_3 (and_3_out, or_7_out, in_8);
  or or_7 (or_7_out, demultiplexer_1_out4, demultiplexer_1_out5, demultiplexer_1_out7);
  or or_8 (or_8_out, and_4_out, in_5);
  and and_4 (and_4_out, in_8, or_6_out);
  assign controlled_buffer_10_out[13:0] = demultiplexer_1_out8 ? register_2_q : 14'bz;  // Controlled_Buffer controlled_buffer_13
  Pull_Resistor pull_resistor_3 (.node(pull_resistor_3_node));
  Pull_Resistor pull_resistor_4 (.node(controlled_buffer_10_out[16:14]));
  assign controlled_buffer_10_out[13:0] = demultiplexer_1_out4 ? register_3_q : 14'bz;  // Controlled_Buffer controlled_buffer_14
  Pull_Resistor pull_resistor_5 (.node(pull_resistor_5_node));
  assign pull_resistor_5_node = or_1_out ? in_4[13:0] : 14'bz;  // Controlled_Buffer controlled_buffer_15
  RAM_part #(.addrWidth(16), .dataWidth(32), .bus("separate")) ram_1 (
    .addr(controlled_buffer_4_out), .din(in_4), .data({ram_1_data_2, ram_1_data}), .clk(or_8_out));  // open: str, sel, ld, clr
  and and_5 (RAISE_ERROR, in_5, ~register_1_q_2[16]);  // AND_Gate
  Subtractor #(.width(14)) subtractor_1 (
    .a(register_3_q), .b(pull_resistor_3_node), .out(subtractor_1_out), .bin(1'b1));  // open: bout
  assign out_9 = or_9_out ? {ram_1_data_2, ram_1_data} : 32'bz;  // Controlled_Buffer controlled_buffer_16
  or or_9 (or_9_out, or_2_out, and_6_out);
  and and_6 (and_6_out, register_1_q_2[16], in_7);
  Adder #(.width(17)) adder_1 (
    .a(controlled_buffer_10_out), .b({3'b000, pull_resistor_5_node}), .out(adder_1_out),
    .cin(demultiplexer_1_out4));  // open: cout

  // Notes on the sheet:
  //   TRIED WRITING IN ROM
endmodule

module CPU_REG (
  input  [31:0] in_1,
  input  [15:0] in_2,
  input  [15:0] in_3,
  output [31:0] out_4
);

  wire or_1_out;
  wire [31:0] register_1_out_4;

  REGISTER register_1 (.in_1(in_1), .out_4(register_1_out_4), .in_2(in_2[0]), .in_3(in_3[0]));
  REGISTER register_2 (.in_1(in_1), .out_4(register_1_out_4), .in_2(in_2[1]), .in_3(in_3[1]));
  REGISTER register_3 (.in_1(in_1), .out_4(register_1_out_4), .in_2(in_2[3]), .in_3(in_3[3]));
  REGISTER register_4 (.in_1(in_1), .out_4(register_1_out_4), .in_2(in_2[2]), .in_3(in_3[2]));
  REGISTER register_5 (.in_1(in_1), .out_4(register_1_out_4), .in_2(in_2[5]), .in_3(in_3[5]));
  REGISTER register_6 (.in_1(in_1), .out_4(register_1_out_4), .in_2(in_2[4]), .in_3(in_3[4]));
  REGISTER register_7 (.in_1(in_1), .out_4(register_1_out_4), .in_2(in_2[6]), .in_3(in_3[6]));
  REGISTER register_8 (.in_1(in_1), .out_4(register_1_out_4), .in_2(in_2[7]), .in_3(in_3[7]));
  REGISTER register_9 (.in_1(in_1), .out_4(register_1_out_4), .in_2(in_2[9]), .in_3(in_3[9]));
  REGISTER register_10 (.in_1(in_1), .out_4(register_1_out_4), .in_2(in_2[8]), .in_3(in_3[8]));
  REGISTER register_11 (.in_1(in_1), .out_4(register_1_out_4), .in_2(in_2[11]), .in_3(in_3[11]));
  REGISTER register_12 (.in_1(in_1), .out_4(register_1_out_4), .in_2(in_2[10]), .in_3(in_3[10]));
  REGISTER register_13 (.in_1(in_1), .out_4(register_1_out_4), .in_2(in_2[12]), .in_3(in_3[12]));
  REGISTER register_14 (.in_1(in_1), .out_4(register_1_out_4), .in_2(in_2[13]), .in_3(in_3[13]));
  REGISTER register_15 (.in_1(in_1), .out_4(register_1_out_4), .in_2(in_2[15]), .in_3(in_3[15]));
  REGISTER register_16 (.in_1(in_1), .out_4(register_1_out_4), .in_2(in_2[14]), .in_3(in_3[14]));
  assign out_4 = or_1_out ? register_1_out_4 : 32'bz;  // Controlled_Buffer controlled_buffer_1
  or or_1 (or_1_out, in_3[0], in_3[1], in_3[2], in_3[3], in_3[4], in_3[5], in_3[6], in_3[7], in_3[8], in_3[9], in_3[10], in_3[11], in_3[12], in_3[13], in_3[14], in_3[15], 1'b0);
endmodule

module stepper (
  input  in_1,
  input  in_2,
  output out_3,
  output [3:0] out_4
);

  wire and_1_out, and_2_out, and_3_out, d_ff_2_q, d_ff_3_q, d_ff_4_q, d_ff_5_q, d_ff_6_q, d_ff_7_q,
       d_ff_7_qn, d_ff_8_q, not_1_out, not_2_out, xor_1_out, xor_2_out, xor_3_out, xor_4_out, xor_5_out;

  and and_1 (and_1_out, d_ff_3_q, in_1);
  not not_1 (not_1_out, 1'b0);
  and and_2 (and_2_out, not_1_out, 1'b0);
  D_Flip_Flop d_ff_1 (.clk(in_1), .D(1'b1), .Q(out_3), .reset(and_3_out));  // open: Qn, preset, en
  not not_2 (not_2_out, and_1_out);
  and and_3 (and_3_out, not_2_out, in_2);
  D_Flip_Flop d_ff_2 (.clk(1'b0), .D(d_ff_7_qn), .Q(d_ff_2_q), .reset(and_2_out));  // open: Qn, preset, en
  D_Flip_Flop d_ff_3 (.clk(in_1), .D(out_3), .Q(d_ff_3_q), .reset(and_3_out));  // open: Qn, preset, en
  Counter #(.width(4), .max('hf)) counter_1 (
    .count(1'b1), .Q(out_4), .clk(and_1_out), .clr(and_3_out));  // open: load, D, carry
  D_Flip_Flop d_ff_4 (.clk(1'b0), .D(d_ff_2_q), .Q(d_ff_4_q), .reset(and_2_out));  // open: Qn, preset, en
  xor xor_1 (xor_1_out, d_ff_2_q, d_ff_4_q);
  D_Flip_Flop d_ff_5 (.clk(1'b0), .D(d_ff_4_q), .Q(d_ff_5_q), .reset(and_2_out));  // open: Qn, preset, en
  xor xor_2 (xor_2_out, d_ff_4_q, d_ff_5_q);
  xor xor_3 (xor_3_out, d_ff_5_q, d_ff_6_q);
  D_Flip_Flop d_ff_6 (.clk(1'b0), .D(d_ff_5_q), .Q(d_ff_6_q), .reset(and_2_out));  // open: Qn, preset, en
  xor xor_4 (xor_4_out, d_ff_6_q, d_ff_7_q);
  D_Flip_Flop d_ff_7 (.clk(1'b0), .D(d_ff_6_q), .Q(d_ff_7_q), .Qn(d_ff_7_qn), .reset(and_2_out));  // open: preset, en
  xor xor_5 (xor_5_out, d_ff_7_q, d_ff_8_q);
  D_Flip_Flop d_ff_8 (.clk(1'b0), .D(d_ff_7_q), .Q(d_ff_8_q), .reset(and_2_out));  // open: Qn, preset, en
endmodule

module ALU (
  input  [31:0] A,
  input  [31:0] B,
  input  in_3,
  input  [5:0] in_4,
  output out_5,
  output out_6,
  output out_7,
  output out_8,
  output [31:0] A_2
);

  wire adder_1_cout, and_2_out, and_3_out, and_4_out, and_5_out, bitfinder_1_found, comparator_1_gt,
       decoder_1_out0, decoder_1_out1, decoder_1_out2, decoder_1_out3, decoder_1_out4, decoder_1_out5,
       decoder_1_out6, decoder_1_out7, decoder_1_out8, decoder_1_out9, decoder_1_out10, decoder_1_out11,
       decoder_1_out12, decoder_1_out13, fpu_1_out_5, not_1_out, not_2_out, not_4_out, or_1_out, or_4_out,
       or_5_out, or_6_out, sign_controller_1_out_3, subtractor_1_bout;
  wire [0:0] or_2_out;
  wire [31:0] adder_1_out, and_1_out, controlled_buffer_1_out, controlled_buffer_2_out,
       controlled_buffer_4_out, demultiplexer_1_out0, demultiplexer_1_out1, demultiplexer_2_out0,
       demultiplexer_2_out1, divider_1_out, divider_1_rem, multiplier_1_out, negator_1_out, negator_2_out,
       not_3_out, or_3_out, pull_resistor_2_node, sign_controller_1_out_4, sign_controller_1_out_5,
       subtractor_1_out, xor_1_out;

  Demultiplexer #(.width(32), .enable("false")) demultiplexer_1 (
    .out0(demultiplexer_1_out0), .out1(demultiplexer_1_out1), .in(controlled_buffer_1_out), .sel(not_2_out));
  assign controlled_buffer_1_out = in_4[5] ? A : 32'bz;  // Controlled_Buffer controlled_buffer_1
  assign controlled_buffer_2_out = in_4[5] ? B : 32'bz;  // Controlled_Buffer controlled_buffer_2
  Demultiplexer #(.width(32), .enable("false")) demultiplexer_2 (
    .out0(demultiplexer_2_out0), .out1(demultiplexer_2_out1), .in(controlled_buffer_2_out), .sel(not_2_out));
  Pull_Resistor pull_resistor_1 (.node(demultiplexer_1_out1));
  Pull_Resistor pull_resistor_2 (.node(pull_resistor_2_node));
  assign pull_resistor_2_node = not_1_out ? demultiplexer_2_out1 : 32'bz;  // Controlled_Buffer controlled_buffer_3
  not not_1 (not_1_out, or_1_out);
  or or_1 (or_1_out, decoder_1_out12, decoder_1_out11);
  not not_2 (not_2_out, in_4[4]);
  or or_2 (or_2_out[0], in_3, decoder_1_out11, decoder_1_out12);
  sign_controller sign_controller_1 (
    .in_1(demultiplexer_1_out1), .in_2(pull_resistor_2_node), .out_4(sign_controller_1_out_4),
    .out_5(sign_controller_1_out_5), .out_3(sign_controller_1_out_3));
  Adder #(.width(32)) adder_1 (
    .a(demultiplexer_1_out1), .b(pull_resistor_2_node), .out(adder_1_out), .cin(or_2_out[0]),
    .cout(adder_1_cout));
  Subtractor #(.width(32)) subtractor_1 (
    .a(demultiplexer_1_out1), .b(pull_resistor_2_node), .out(subtractor_1_out), .bin(or_2_out[0]),
    .bout(subtractor_1_bout));
  Multiplier #(.width(32)) multiplier_1 (
    .a(sign_controller_1_out_4), .b(sign_controller_1_out_5), .out(multiplier_1_out));  // open: cin, cout
  Divider #(.width(32)) divider_1 (
    .a(sign_controller_1_out_4), .b(sign_controller_1_out_5), .out(divider_1_out), .rem(divider_1_rem));  // open: upper
  assign controlled_buffer_4_out = decoder_1_out10 ? divider_1_rem : 32'bz;  // Controlled_Buffer controlled_buffer_4
  Comparator #(.width(32)) comparator_1 (
    .a(demultiplexer_1_out1), .b(pull_resistor_2_node), .gt(comparator_1_gt));  // open: eq, lt
  Negator #(.width(32)) negator_1 (.in(demultiplexer_1_out1), .out(negator_1_out));
  assign xor_1_out = demultiplexer_1_out1 ^ pull_resistor_2_node;  // XOR_Gate xor_1, 32 bits wide
  assign or_3_out = demultiplexer_1_out1 | pull_resistor_2_node;  // OR_Gate or_3, 32 bits wide
  assign and_1_out = demultiplexer_1_out1 & pull_resistor_2_node;  // AND_Gate and_1, 32 bits wide
  assign not_3_out = ~demultiplexer_1_out1;  // NOT_Gate not_3, 32 bits wide
  and and_2 (and_2_out, decoder_1_out4, demultiplexer_1_out1[31]);
  and and_3 (and_3_out, demultiplexer_1_out1[0], decoder_1_out5);
  or or_4 (or_4_out, decoder_1_out0, decoder_1_out11);
  or or_5 (or_5_out, decoder_1_out12, decoder_1_out1);
  FPU fpu_1 (
    .in_1(demultiplexer_1_out0), .in_2(demultiplexer_2_out0), .in_3(in_4), .out_4(A_2), .out_5(fpu_1_out_5));  // open: out_6
  assign A_2 = decoder_1_out13 ? negator_1_out : 32'bz;  // Controlled_Buffer controlled_buffer_5
  assign A_2 = decoder_1_out9 ? xor_1_out : 32'bz;  // Controlled_Buffer controlled_buffer_6
  assign A_2 = decoder_1_out8 ? or_3_out : 32'bz;  // Controlled_Buffer controlled_buffer_7
  assign A_2 = decoder_1_out7 ? and_1_out : 32'bz;  // Controlled_Buffer controlled_buffer_8
  assign A_2 = decoder_1_out6 ? not_3_out : 32'bz;  // Controlled_Buffer controlled_buffer_9
  assign A_2 = decoder_1_out4 ? {demultiplexer_1_out1[30:0], or_2_out[0]} : 32'bz;  // Controlled_Buffer controlled_buffer_10
  or or_6 (or_6_out, and_2_out, and_3_out);
  assign A_2 = decoder_1_out5 ? {or_2_out[0], demultiplexer_1_out1[31:1]} : 32'bz;  // Controlled_Buffer controlled_buffer_11
  assign A_2 = or_4_out ? adder_1_out : 32'bz;  // Controlled_Buffer controlled_buffer_12
  and and_4 (and_4_out, adder_1_cout, or_4_out);
  assign A_2 = or_5_out ? subtractor_1_out : 32'bz;  // Controlled_Buffer controlled_buffer_13
  and and_5 (and_5_out, subtractor_1_bout, or_5_out);
  assign controlled_buffer_4_out = decoder_1_out2 ? multiplier_1_out : 32'bz;  // Controlled_Buffer controlled_buffer_14
  assign controlled_buffer_4_out = decoder_1_out3 ? divider_1_out : 32'bz;  // Controlled_Buffer controlled_buffer_15
  Decoder #(.select(4), .disabled(0)) decoder_1 (
    .out0(decoder_1_out0), .out1(decoder_1_out1), .out2(decoder_1_out2), .out3(decoder_1_out3),
    .out4(decoder_1_out4), .out5(decoder_1_out5), .out6(decoder_1_out6), .out7(decoder_1_out7),
    .out8(decoder_1_out8), .out9(decoder_1_out9), .out10(decoder_1_out10), .out11(decoder_1_out11),
    .out12(decoder_1_out12), .out13(decoder_1_out13), .sel(in_4[3:0]), .en(not_4_out));  // open: out14, out15
  not not_4 (not_4_out, in_4[4]);
  or or_7 (out_8, or_6_out, and_4_out, and_5_out);
  Multiplexer #(.enable("false")) multiplexer_1 (
    .in0(fpu_1_out_5), .in1(comparator_1_gt), .out(out_5), .sel(not_2_out));
  Pull_Resistor pull_resistor_3 (.node(A_2));
  Negator #(.width(32)) negator_2 (.in(controlled_buffer_4_out), .out(negator_2_out));
  Multiplexer #(.width(32), .enable("false")) multiplexer_2 (
    .in0(negator_2_out), .in1(controlled_buffer_4_out), .out(A_2), .sel(sign_controller_1_out_3));
  BitFinder #(.width(32)) bitfinder_1 (.in(A_2), .found(bitfinder_1_found));  // open: index
  not not_5 (out_7, bitfinder_1_found);
  Pull_Resistor pull_resistor_4 (.node(out_8));

  assign out_6 = A_2[31];
endmodule

module INTRUCTION_REGISTER_IR (
  input  [31:0] in_1,
  input  in_2,
  output [15:0] out_3
);

  Register #(.width(16)) register_1 (.D(in_1[15:0]), .Q(out_3), .clk(in_2));  // open: en, clr
endmodule

module REGISTER (
  input  [31:0] in_1,
  input  in_2,
  input  in_3,
  output [31:0] out_4
);

  wire [31:0] register_1_q;

  assign out_4 = in_3 ? register_1_q : 32'bz;  // Controlled_Buffer controlled_buffer_1
  Register #(.width(32)) register_1 (.D(in_1), .Q(register_1_q), .clk(in_2));  // open: en, clr
endmodule

module CLOCK (
  input  in_1,
  output out_2,
  output out_3,
  output out_4
);

  wire buffer_1_out_2, buffer_2_out_2;

  buffer buffer_1 (.in_1(in_1), .out_2(buffer_1_out_2));
  buffer buffer_2 (.in_1(buffer_1_out_2), .out_2(buffer_2_out_2));
  and and_1 (out_2, buffer_2_out_2, in_1);
  or or_1 (out_4, buffer_2_out_2, in_1);

  assign out_3 = in_1;
endmodule

module FLAG_REG (
  input  in_1,
  input  in_2,
  input  in_3,
  input  in_4,
  input  in_5,
  output out_6,
  output out_7,
  output out_8,
  output out_9
);

  Register #(.width(1)) register_1 (.D(in_1), .Q(out_6), .clk(in_5));  // open: en, clr
  Register #(.width(1)) register_2 (.D(in_2), .Q(out_7), .clk(in_5));  // open: en, clr
  Register #(.width(1)) register_3 (.D(in_3), .Q(out_8), .clk(in_5));  // open: en, clr
  Register #(.width(1)) register_4 (.D(in_4), .Q(out_9), .clk(in_5));  // open: en, clr
endmodule

module TMP (
  input  [31:0] in_1,
  input  in_2,
  input  in_3,
  output [31:0] out_4
);

  wire not_1_out;
  wire [0:0] controlled_buffer_1_out;
  wire [31:0] register_1_q;

  Register #(.width(32)) register_1 (.D(in_1), .Q(register_1_q), .clk(in_2));  // open: en, clr
  assign {out_4[31:1], controlled_buffer_1_out[0]} = not_1_out ? register_1_q : 32'bz;  // Controlled_Buffer controlled_buffer_1
  Pull_Resistor pull_resistor_1 (.node({out_4[31:1], controlled_buffer_1_out[0]}));
  not not_1 (not_1_out, in_3);
  or or_1 (out_4[0], controlled_buffer_1_out[0], in_3);
endmodule

module ACC (
  input  [31:0] in_1,
  input  in_2,
  input  in_3,
  output [31:0] out_4
);

  wire [31:0] register_1_q;

  Register #(.width(32)) register_1 (.D(in_1), .Q(register_1_q), .clk(in_2));  // open: en, clr
  assign out_4 = in_3 ? register_1_q : 32'bz;  // Controlled_Buffer controlled_buffer_1
endmodule

module keyboard (
  input  [6:0] in_1,
  input  [31:0] in_2,
  input  [3:0] in_3,
  output [15:0] out_4,
  output out_5
);

  wire and_1_out, and_2_out, and_3_out, and_4_out, and_5_out, d_ff_1_q, not_1_out, not_2_out, not_3_out,
       or_1_out, or_2_out;
  wire [6:0] register_1_q;

  Register #(.width(7)) register_1 (.D(in_1), .Q(register_1_q), .clk(out_5));  // open: en, clr
  or or_1 (or_1_out, in_2[0], in_2[1], in_2[2]);
  and and_1 (and_1_out, in_2[4], in_2[5], in_2[6]);
  assign out_4[6:0] = out_5 ? register_1_q : 7'bz;  // Controlled_Buffer controlled_buffer_1
  or or_2 (or_2_out, or_1_out, in_2[3]);
  not not_1 (not_1_out, or_2_out);
  and and_2 (and_2_out, not_1_out, and_3_out);
  and and_3 (and_3_out, and_1_out, in_2[7]);
  not not_2 (not_2_out, in_3[3]);
  not not_3 (not_3_out, in_3[2]);
  D_Flip_Flop d_ff_1 (.clk(and_4_out), .D(and_2_out), .Q(d_ff_1_q));  // open: Qn, preset, en, reset
  and and_4 (and_4_out, in_3[0], in_3[2], in_3[3]);
  and and_5 (and_5_out, in_3[1], not_2_out, not_3_out);
  Register #(.width(7)) register_2 ();  // open: D, en, Q, clk, clr
  and and_6 (out_5, d_ff_1_q, and_5_out);

  // Notes on the sheet:
  //   CLOCK S
  //   CLK E
  //   D/A
  //   I/O
endmodule

module IAR (
  input  enable,
  input  clock,
  input  reset,
  input  set,
  input  [31:0] in_5,
  output [31:0] out_6
);

  wire and_1_out, and_2_out, and_3_out, and_4_out, and_5_out, and_6_out, and_7_out, and_8_out, and_9_out,
       and_10_out, and_11_out, and_12_out, and_13_out, and_14_out, and_15_out, and_16_out, and_17_out,
       and_18_out, and_19_out, and_20_out, and_21_out, and_22_out, and_23_out, and_24_out, and_25_out,
       and_26_out, and_27_out, and_28_out, and_29_out, and_30_out, and_31_out, and_32_out, and_33_out,
       and_34_out, or_1_out, or_2_out, or_3_out, or_4_out, or_5_out, or_6_out, or_7_out, or_8_out, or_9_out,
       or_10_out, or_11_out, or_12_out, or_13_out, or_14_out, or_15_out, or_16_out, or_17_out, t_ff_1_qn,
       t_ff_2_qn, t_ff_3_qn, t_ff_4_qn, t_ff_5_qn, t_ff_6_qn, t_ff_7_qn, t_ff_8_qn, t_ff_9_qn, t_ff_10_qn,
       t_ff_11_qn, t_ff_12_qn, t_ff_13_qn, t_ff_14_qn, t_ff_15_qn, t_ff_16_qn;
  wire [16:0] t_ff_1_q;

  and and_1 (and_1_out, in_5[0], set);
  T_Flip_Flop t_ff_1 (
    .clk(clock), .T(1'b1), .Q(t_ff_1_q[0]), .Qn(t_ff_1_qn), .preset(and_1_out), .reset(or_1_out));  // open: en
  or or_1 (or_1_out, reset, and_2_out);
  and and_2 (and_2_out, ~in_5[0], set);  // AND_Gate
  and and_3 (and_3_out, in_5[1], set);
  T_Flip_Flop t_ff_2 (
    .clk(t_ff_1_qn), .T(1'b1), .Q(t_ff_1_q[1]), .Qn(t_ff_2_qn), .preset(and_3_out), .reset(or_2_out));  // open: en
  or or_2 (or_2_out, reset, and_5_out);
  and and_4 (and_4_out, in_5[2], set);
  and and_5 (and_5_out, ~in_5[1], set);  // AND_Gate
  T_Flip_Flop t_ff_3 (
    .clk(t_ff_2_qn), .T(1'b1), .Q(t_ff_1_q[2]), .Qn(t_ff_3_qn), .preset(and_4_out), .reset(or_3_out));  // open: en
  or or_3 (or_3_out, reset, and_7_out);
  and and_6 (and_6_out, in_5[3], set);
  and and_7 (and_7_out, ~in_5[2], set);  // AND_Gate
  T_Flip_Flop t_ff_4 (
    .clk(t_ff_3_qn), .T(1'b1), .Q(t_ff_1_q[3]), .Qn(t_ff_4_qn), .preset(and_6_out), .reset(or_4_out));  // open: en
  or or_4 (or_4_out, reset, and_8_out);
  and and_8 (and_8_out, ~in_5[3], set);  // AND_Gate
  and and_9 (and_9_out, in_5[4], set);
  T_Flip_Flop t_ff_5 (
    .clk(t_ff_4_qn), .T(1'b1), .Q(t_ff_1_q[4]), .Qn(t_ff_5_qn), .preset(and_9_out), .reset(or_5_out));  // open: en
  or or_5 (or_5_out, reset, and_10_out);
  and and_10 (and_10_out, ~in_5[4], set);  // AND_Gate
  and and_11 (and_11_out, in_5[5], set);
  T_Flip_Flop t_ff_6 (
    .clk(t_ff_5_qn), .T(1'b1), .Q(t_ff_1_q[5]), .Qn(t_ff_6_qn), .preset(and_11_out), .reset(or_6_out));  // open: en
  or or_6 (or_6_out, reset, and_13_out);
  and and_12 (and_12_out, in_5[6], set);
  and and_13 (and_13_out, ~in_5[5], set);  // AND_Gate
  T_Flip_Flop t_ff_7 (
    .clk(t_ff_6_qn), .T(1'b1), .Q(t_ff_1_q[6]), .Qn(t_ff_7_qn), .preset(and_12_out), .reset(or_7_out));  // open: en
  or or_7 (or_7_out, reset, and_14_out);
  and and_14 (and_14_out, ~in_5[6], set);  // AND_Gate
  and and_15 (and_15_out, in_5[7], set);
  T_Flip_Flop t_ff_8 (
    .clk(t_ff_7_qn), .T(1'b1), .Q(t_ff_1_q[7]), .Qn(t_ff_8_qn), .preset(and_15_out), .reset(or_8_out));  // open: en
  or or_8 (or_8_out, reset, and_16_out);
  and and_16 (and_16_out, ~in_5[7], set);  // AND_Gate
  and and_17 (and_17_out, in_5[8], set);
  T_Flip_Flop t_ff_9 (
    .clk(t_ff_8_qn), .T(1'b1), .Q(t_ff_1_q[8]), .Qn(t_ff_9_qn), .preset(and_17_out), .reset(or_9_out));  // open: en
  or or_9 (or_9_out, reset, and_19_out);
  and and_18 (and_18_out, in_5[9], set);
  and and_19 (and_19_out, ~in_5[8], set);  // AND_Gate
  T_Flip_Flop t_ff_10 (
    .clk(t_ff_9_qn), .T(1'b1), .Q(t_ff_1_q[9]), .Qn(t_ff_10_qn), .preset(and_18_out), .reset(or_10_out));  // open: en
  or or_10 (or_10_out, reset, and_20_out);
  and and_20 (and_20_out, ~in_5[9], set);  // AND_Gate
  and and_21 (and_21_out, in_5[10], set);
  assign out_6 = enable ? {{15{1'b0}}, t_ff_1_q} : 32'bz;  // Controlled_Buffer controlled_buffer_1
  T_Flip_Flop t_ff_11 (
    .clk(t_ff_10_qn), .T(1'b1), .Q(t_ff_1_q[10]), .Qn(t_ff_11_qn), .preset(and_21_out), .reset(or_11_out));  // open: en
  or or_11 (or_11_out, reset, and_23_out);
  and and_22 (and_22_out, in_5[11], set);
  and and_23 (and_23_out, ~in_5[10], set);  // AND_Gate
  T_Flip_Flop t_ff_12 (
    .clk(t_ff_11_qn), .T(1'b1), .Q(t_ff_1_q[11]), .Qn(t_ff_12_qn), .preset(and_22_out), .reset(or_12_out));  // open: en
  or or_12 (or_12_out, reset, and_24_out);
  and and_24 (and_24_out, ~in_5[11], set);  // AND_Gate
  and and_25 (and_25_out, in_5[12], set);
  T_Flip_Flop t_ff_13 (
    .clk(t_ff_12_qn), .T(1'b1), .Q(t_ff_1_q[12]), .Qn(t_ff_13_qn), .preset(and_25_out), .reset(or_13_out));  // open: en
  or or_13 (or_13_out, reset, and_27_out);
  and and_26 (and_26_out, in_5[13], set);
  and and_27 (and_27_out, ~in_5[12], set);  // AND_Gate
  T_Flip_Flop t_ff_14 (
    .clk(t_ff_13_qn), .T(1'b1), .Q(t_ff_1_q[13]), .Qn(t_ff_14_qn), .preset(and_26_out), .reset(or_14_out));  // open: en
  or or_14 (or_14_out, reset, and_28_out);
  and and_28 (and_28_out, ~in_5[13], set);  // AND_Gate
  and and_29 (and_29_out, in_5[14], set);
  T_Flip_Flop t_ff_15 (
    .clk(t_ff_14_qn), .T(1'b1), .Q(t_ff_1_q[14]), .Qn(t_ff_15_qn), .preset(and_29_out), .reset(or_15_out));  // open: en
  or or_15 (or_15_out, reset, and_31_out);
  and and_30 (and_30_out, in_5[15], set);
  and and_31 (and_31_out, ~in_5[14], set);  // AND_Gate
  T_Flip_Flop t_ff_16 (
    .clk(t_ff_15_qn), .T(1'b1), .Q(t_ff_1_q[15]), .Qn(t_ff_16_qn), .preset(and_30_out), .reset(or_16_out));  // open: en
  or or_16 (or_16_out, reset, and_32_out);
  and and_32 (and_32_out, ~in_5[15], set);  // AND_Gate
  and and_33 (and_33_out, in_5[16], set);
  T_Flip_Flop t_ff_17 (
    .clk(t_ff_16_qn), .T(1'b1), .Q(t_ff_1_q[16]), .preset(and_33_out), .reset(or_17_out));  // open: Qn, en
  or or_17 (or_17_out, reset, and_34_out);
  and and_34 (and_34_out, ~in_5[16], set);  // AND_Gate
endmodule

module number_display (
  input  [31:0] in_1,
  input  [3:0] in_2,
  output [3:0] out_3,
  output [3:0] out_4,
  output [3:0] out_5,
  output [3:0] out_6,
  output [3:0] out_7,
  output [3:0] out_8,
  output [3:0] out_9,
  output [3:0] out_10
);

  wire and_1_out, and_2_out, and_3_out, and_4_out, d_ff_1_q, not_1_out, not_2_out, not_3_out, not_4_out,
       not_5_out, not_6_out;

  not not_1 (not_1_out, in_1[0]);
  not not_2 (not_2_out, in_1[1]);
  not not_3 (not_3_out, in_1[6]);
  not not_4 (not_4_out, in_1[7]);
  Register #(.width(32)) register_1 (
    .D(in_1), .Q({out_10, out_9, out_8, out_7, out_6, out_5, out_4, out_3}), .clk(and_4_out));  // open: en, clr
  and and_1 (and_1_out, 1'b1, not_1_out, not_2_out, in_1[2], in_1[3], in_1[4], in_1[5], not_3_out, not_4_out);
  not not_5 (not_5_out, in_2[3]);
  not not_6 (not_6_out, in_2[2]);
  D_Flip_Flop d_ff_1 (.clk(and_2_out), .D(and_1_out), .Q(d_ff_1_q));  // open: Qn, preset, en, reset
  and and_2 (and_2_out, in_2[0], in_2[2], in_2[3]);
  and and_3 (and_3_out, in_2[1], not_5_out, not_6_out);
  and and_4 (and_4_out, d_ff_1_q, and_3_out);

  // Notes on the sheet:
  //   CLOCK S
  //   CLK E
  //   D/A
  //   I/O
endmodule

module KEYBOARD (
  input  [6:0] in_1,
  input  [31:0] in_2,
  input  [3:0] in_3,
  output [31:0] out_4,
  output out_5
);

  wire and_1_out, and_2_out, and_3_out, and_4_out, and_5_out, d_ff_1_q, not_1_out, not_2_out, or_1_out,
       or_2_out;
  wire [6:0] register_1_q;

  Register #(.width(7)) register_1 (.D(in_1), .Q(register_1_q), .clk(out_5));  // open: en, clr
  or or_1 (or_1_out, in_2[0], in_2[1], in_2[2]);
  and and_1 (and_1_out, in_2[4], in_2[5], in_2[6]);
  assign out_4[6:0] = out_5 ? register_1_q : 7'bz;  // Controlled_Buffer controlled_buffer_1
  or or_2 (or_2_out, or_1_out, in_2[3]);
  not not_1 (not_1_out, or_2_out);
  and and_2 (and_2_out, not_1_out, and_3_out);
  and and_3 (and_3_out, and_1_out, in_2[7]);
  not not_2 (not_2_out, in_3[2]);
  D_Flip_Flop d_ff_1 (.clk(and_4_out), .D(and_2_out), .Q(d_ff_1_q));  // open: Qn, preset, en, reset
  and and_4 (and_4_out, in_3[0], in_3[2], in_3[3]);
  and and_5 (and_5_out, in_3[1], in_3[3], not_2_out);
  and and_6 (out_5, d_ff_1_q, and_5_out);

  // Notes on the sheet:
  //   CLOCK S
  //   CLK E
  //   D/A
  //   I/O
endmodule

module NUMBER_DISPLAY (
  input  [31:0] in_1,
  input  [3:0] in_2,
  output [3:0] out_3,
  output [3:0] out_4,
  output [3:0] out_5,
  output [3:0] out_6,
  output [3:0] out_7,
  output [3:0] out_8,
  output [3:0] out_9,
  output [3:0] out_10
);

  wire and_1_out, and_2_out, and_3_out, and_4_out, d_ff_1_q, not_1_out, not_2_out, not_3_out, not_4_out,
       not_5_out;

  not not_1 (not_1_out, in_1[0]);
  not not_2 (not_2_out, in_1[1]);
  not not_3 (not_3_out, in_1[6]);
  not not_4 (not_4_out, in_1[7]);
  Register #(.width(32)) register_1 (
    .D(in_1), .Q({out_10, out_9, out_8, out_7, out_6, out_5, out_4, out_3}), .clk(and_4_out));  // open: en, clr
  and and_1 (and_1_out, 1'b1, not_1_out, not_2_out, in_1[2], in_1[3], in_1[4], in_1[5], not_3_out, not_4_out);
  not not_5 (not_5_out, in_2[2]);
  D_Flip_Flop d_ff_1 (.clk(and_2_out), .D(and_1_out), .Q(d_ff_1_q));  // open: Qn, preset, en, reset
  and and_2 (and_2_out, in_2[0], in_2[2], in_2[3]);
  and and_3 (and_3_out, in_2[1], in_2[3], not_5_out);
  and and_4 (and_4_out, d_ff_1_q, and_3_out);

  // Notes on the sheet:
  //   CLOCK S
  //   CLK E
  //   D/A
  //   I/O
endmodule

module program_loader (
  input  in_1
);

  ROM_part rom_1 ();  // open: addr, data, sel
endmodule

module teste (
  input  [1:0] in_1,
  input  [31:0] in_2,
  input  [31:0] in_3
);

  wire bitfinder_1_found, not_2_out, pull_resistor_2_node, pull_resistor_3_node, subtractor_1_bout,
       subtractor_3_bout;
  wire [4:0] bit_extender_3_out, bitfinder_1_index, multiplexer_1_out, multiplexer_3_out, not_1_out,
       not_3_out, subtractor_1_out, subtractor_3_out;
  wire [7:0] adder_1_out, bit_extender_2_out, subtractor_2_out;
  wire [22:0] bit_extender_4_out;
  wire [23:23] bitfinder_2_found;
  wire [30:0] bit_extender_5_out, multiplexer_4_out, shifter_3_out, shifter_4_out;
  wire [31:0] bit_extender_1_out, multiplexer_2_out, pull_resistor_1_node, ram_1_data, shifter_1_out,
       shifter_2_out;

  BitFinder #(.width(32), .\type ("high1")) bitfinder_1 (
    .in(bit_extender_1_out), .index(bitfinder_1_index), .found(bitfinder_1_found));
  assign bit_extender_1_out = {{1{1'b0}}, in_3[30:0]};  // Bit_Extender bit_extender_1
  Pull_Resistor pull_resistor_1 (.node(pull_resistor_1_node));
  RAM_part #(.addrWidth(2), .dataWidth(32)) ram_1 (.addr(in_1), .data(ram_1_data));  // open: sel, clk, ld, clr
  Pull_Resistor pull_resistor_2 (.node(pull_resistor_2_node));
  Subtractor #(.width(5)) subtractor_1 (
    .a(5'b10111), .b(bitfinder_1_index), .out(subtractor_1_out), .bin(pull_resistor_2_node),
    .bout(subtractor_1_bout));
  assign pull_resistor_2_node = bitfinder_1_found ? subtractor_1_bout : 1'bz;  // Controlled_Buffer controlled_buffer_1
  assign bit_extender_2_out = {{3{1'b0}}, bitfinder_1_index};  // Bit_Extender bit_extender_2
  Subtractor subtractor_2 (.a(pull_resistor_1_node[30:23]), .b(8'h7f), .out(subtractor_2_out));  // open: bin, bout
  Multiplexer #(.width(5), .disabled(0), .enable("false")) multiplexer_1 (
    .in0(subtractor_1_out), .in1(not_1_out), .out(multiplexer_1_out), .sel(pull_resistor_2_node));
  assign not_1_out = ~subtractor_1_out;  // NOT_Gate not_1, 5 bits wide
  Adder adder_1 (.a(8'h7f), .b(bit_extender_2_out), .out(adder_1_out));  // open: cin, cout
  Pull_Resistor pull_resistor_3 (.node(pull_resistor_3_node));
  Bit_Extender #(.out_width(5)) bit_extender_3 (.in(subtractor_2_out), .out(bit_extender_3_out));
  Shifter #(.width(32), .shift("lr")) shifter_1 (
    .in(bit_extender_1_out), .\dist (multiplexer_1_out), .out(shifter_1_out));
  Shifter #(.width(32)) shifter_2 (.in(bit_extender_1_out), .\dist (multiplexer_1_out), .out(shifter_2_out));
  not not_2 (not_2_out, pull_resistor_2_node);
  Subtractor #(.width(5)) subtractor_3 (
    .a(5'b10111), .b(bit_extender_3_out), .out(subtractor_3_out), .bin(pull_resistor_3_node),
    .bout(subtractor_3_bout));
  assign not_3_out = ~subtractor_3_out;  // NOT_Gate not_3, 5 bits wide
  assign pull_resistor_3_node = bitfinder_2_found[23] ? subtractor_3_bout : 1'bz;  // Controlled_Buffer controlled_buffer_2
  BitFinder #(.width(32), .\type ("high1")) bitfinder_2 (
    .in(pull_resistor_1_node), .found(bitfinder_2_found[23]));  // open: index
  // Probe on ram_1_data
  Multiplexer #(.width(32), .disabled(0), .enable("false")) multiplexer_2 (
    .in0(shifter_1_out), .in1(shifter_2_out), .out(multiplexer_2_out), .sel(not_2_out));
  Bit_Extender #(.in_width(32), .out_width(23)) bit_extender_4 (.in(multiplexer_2_out), .out(bit_extender_4_out));
  Multiplexer #(.width(5), .disabled(0), .enable("false")) multiplexer_3 (
    .in0(subtractor_3_out), .in1(not_3_out), .out(multiplexer_3_out), .sel(pull_resistor_3_node));
  assign pull_resistor_1_node = bitfinder_1_found ? {in_3[31], adder_1_out, bit_extender_4_out} : 32'bz;  // Controlled_Buffer controlled_buffer_3
  assign bit_extender_5_out = {{7{1'b0}}, {bitfinder_2_found[23], pull_resistor_1_node[22:0]}};  // Bit_Extender bit_extender_5
  // Probe on pull_resistor_1_node
  Shifter #(.width(31), .shift("lr")) shifter_3 (
    .in(bit_extender_5_out), .\dist (multiplexer_3_out), .out(shifter_3_out));
  Multiplexer #(.width(31), .disabled(0), .enable("false")) multiplexer_4 (
    .in0(shifter_3_out), .in1(shifter_4_out), .out(multiplexer_4_out), .sel(pull_resistor_3_node));
  Shifter #(.width(31)) shifter_4 (.in(bit_extender_5_out), .\dist (multiplexer_3_out), .out(shifter_4_out));
  // Probe on {pull_resistor_1_node[31], multiplexer_4_out}
endmodule

module buffer (
  input  in_1,
  output out_2
);

  wire buffer_1_out, buffer_2_out, buffer_3_out, buffer_4_out, buffer_5_out, buffer_7_out, buffer_8_out,
       buffer_9_out, buffer_10_out, buffer_11_out, buffer_12_out, buffer_13_out, buffer_14_out,
       buffer_15_out, buffer_16_out, buffer_17_out, buffer_18_out, buffer_19_out, buffer_20_out,
       buffer_21_out, buffer_22_out, buffer_23_out, buffer_24_out, buffer_25_out, buffer_26_out,
       buffer_27_out, buffer_28_out, buffer_29_out, buffer_30_out, buffer_31_out, buffer_32_out,
       buffer_33_out, buffer_34_out, buffer_35_out, buffer_36_out, buffer_37_out, buffer_38_out,
       buffer_39_out, buffer_40_out, buffer_41_out, buffer_42_out, buffer_43_out, buffer_44_out,
       buffer_45_out, buffer_46_out, buffer_47_out, buffer_48_out, buffer_49_out, buffer_50_out,
       buffer_51_out, buffer_52_out, buffer_53_out, buffer_54_out, buffer_55_out, buffer_56_out,
       buffer_57_out, buffer_58_out, buffer_59_out, buffer_60_out, buffer_61_out, buffer_62_out,
       buffer_63_out, buffer_64_out, buffer_65_out, buffer_66_out, buffer_67_out, buffer_68_out,
       buffer_69_out, buffer_70_out, buffer_71_out, buffer_72_out, buffer_73_out, buffer_74_out,
       buffer_75_out, buffer_76_out, buffer_77_out, buffer_78_out, buffer_79_out, buffer_80_out,
       buffer_81_out, buffer_82_out, buffer_83_out, buffer_84_out, buffer_85_out, buffer_86_out,
       buffer_87_out, buffer_88_out, buffer_89_out, buffer_90_out, buffer_91_out, buffer_92_out,
       buffer_93_out, buffer_94_out, buffer_95_out, buffer_96_out, buffer_97_out, buffer_98_out,
       buffer_99_out, buffer_100_out, buffer_101_out, buffer_102_out, buffer_103_out, buffer_104_out,
       buffer_105_out, buffer_106_out, buffer_107_out, buffer_108_out, buffer_109_out, buffer_110_out,
       buffer_111_out, buffer_112_out, buffer_113_out, buffer_114_out, buffer_115_out, buffer_116_out,
       buffer_117_out, buffer_118_out, buffer_119_out, buffer_120_out, buffer_121_out, buffer_122_out,
       buffer_123_out, buffer_124_out, buffer_125_out, buffer_126_out, buffer_127_out, buffer_128_out;

  buf buffer_1 (buffer_1_out, in_1);
  buf buffer_2 (buffer_2_out, buffer_14_out);
  buf buffer_3 (buffer_3_out, buffer_2_out);
  buf buffer_4 (buffer_4_out, buffer_3_out);
  buf buffer_5 (buffer_5_out, buffer_19_out);
  buf buffer_6 (out_2, buffer_5_out);
  buf buffer_7 (buffer_7_out, buffer_8_out);
  buf buffer_8 (buffer_8_out, buffer_1_out);
  buf buffer_9 (buffer_9_out, buffer_10_out);
  buf buffer_10 (buffer_10_out, buffer_7_out);
  buf buffer_11 (buffer_11_out, buffer_30_out);
  buf buffer_12 (buffer_12_out, buffer_11_out);
  buf buffer_13 (buffer_13_out, buffer_12_out);
  buf buffer_14 (buffer_14_out, buffer_13_out);
  buf buffer_15 (buffer_15_out, buffer_4_out);
  buf buffer_16 (buffer_16_out, buffer_17_out);
  buf buffer_17 (buffer_17_out, buffer_18_out);
  buf buffer_18 (buffer_18_out, buffer_15_out);
  buf buffer_19 (buffer_19_out, buffer_22_out);
  buf buffer_20 (buffer_20_out, buffer_37_out);
  buf buffer_21 (buffer_21_out, buffer_20_out);
  buf buffer_22 (buffer_22_out, buffer_21_out);
  buf buffer_23 (buffer_23_out, buffer_25_out);
  buf buffer_24 (buffer_24_out, buffer_26_out);
  buf buffer_25 (buffer_25_out, buffer_9_out);
  buf buffer_26 (buffer_26_out, buffer_23_out);
  buf buffer_27 (buffer_27_out, buffer_45_out);
  buf buffer_28 (buffer_28_out, buffer_27_out);
  buf buffer_29 (buffer_29_out, buffer_28_out);
  buf buffer_30 (buffer_30_out, buffer_29_out);
  buf buffer_31 (buffer_31_out, buffer_34_out);
  buf buffer_32 (buffer_32_out, buffer_33_out);
  buf buffer_33 (buffer_33_out, buffer_31_out);
  buf buffer_34 (buffer_34_out, buffer_16_out);
  buf buffer_35 (buffer_35_out, buffer_36_out);
  buf buffer_36 (buffer_36_out, buffer_54_out);
  buf buffer_37 (buffer_37_out, buffer_38_out);
  buf buffer_38 (buffer_38_out, buffer_35_out);
  buf buffer_39 (buffer_39_out, buffer_41_out);
  buf buffer_40 (buffer_40_out, buffer_42_out);
  buf buffer_41 (buffer_41_out, buffer_24_out);
  buf buffer_42 (buffer_42_out, buffer_39_out);
  buf buffer_43 (buffer_43_out, buffer_44_out);
  buf buffer_44 (buffer_44_out, buffer_62_out);
  buf buffer_45 (buffer_45_out, buffer_46_out);
  buf buffer_46 (buffer_46_out, buffer_43_out);
  buf buffer_47 (buffer_47_out, buffer_49_out);
  buf buffer_48 (buffer_48_out, buffer_47_out);
  buf buffer_49 (buffer_49_out, buffer_32_out);
  buf buffer_50 (buffer_50_out, buffer_48_out);
  buf buffer_51 (buffer_51_out, buffer_69_out);
  buf buffer_52 (buffer_52_out, buffer_51_out);
  buf buffer_53 (buffer_53_out, buffer_52_out);
  buf buffer_54 (buffer_54_out, buffer_53_out);
  buf buffer_55 (buffer_55_out, buffer_57_out);
  buf buffer_56 (buffer_56_out, buffer_40_out);
  buf buffer_57 (buffer_57_out, buffer_56_out);
  buf buffer_58 (buffer_58_out, buffer_55_out);
  buf buffer_59 (buffer_59_out, buffer_61_out);
  buf buffer_60 (buffer_60_out, buffer_77_out);
  buf buffer_61 (buffer_61_out, buffer_60_out);
  buf buffer_62 (buffer_62_out, buffer_59_out);
  buf buffer_63 (buffer_63_out, buffer_64_out);
  buf buffer_64 (buffer_64_out, buffer_66_out);
  buf buffer_65 (buffer_65_out, buffer_63_out);
  buf buffer_66 (buffer_66_out, buffer_50_out);
  buf buffer_67 (buffer_67_out, buffer_84_out);
  buf buffer_68 (buffer_68_out, buffer_67_out);
  buf buffer_69 (buffer_69_out, buffer_70_out);
  buf buffer_70 (buffer_70_out, buffer_68_out);
  buf buffer_71 (buffer_71_out, buffer_73_out);
  buf buffer_72 (buffer_72_out, buffer_71_out);
  buf buffer_73 (buffer_73_out, buffer_74_out);
  buf buffer_74 (buffer_74_out, buffer_58_out);
  buf buffer_75 (buffer_75_out, buffer_76_out);
  buf buffer_76 (buffer_76_out, buffer_78_out);
  buf buffer_77 (buffer_77_out, buffer_75_out);
  buf buffer_78 (buffer_78_out, buffer_91_out);
  buf buffer_79 (buffer_79_out, buffer_65_out);
  buf buffer_80 (buffer_80_out, buffer_81_out);
  buf buffer_81 (buffer_81_out, buffer_79_out);
  buf buffer_82 (buffer_82_out, buffer_80_out);
  buf buffer_83 (buffer_83_out, buffer_99_out);
  buf buffer_84 (buffer_84_out, buffer_85_out);
  buf buffer_85 (buffer_85_out, buffer_86_out);
  buf buffer_86 (buffer_86_out, buffer_83_out);
  buf buffer_87 (buffer_87_out, buffer_89_out);
  buf buffer_88 (buffer_88_out, buffer_87_out);
  buf buffer_89 (buffer_89_out, buffer_72_out);
  buf buffer_90 (buffer_90_out, buffer_88_out);
  buf buffer_91 (buffer_91_out, buffer_94_out);
  buf buffer_92 (buffer_92_out, buffer_110_out);
  buf buffer_93 (buffer_93_out, buffer_92_out);
  buf buffer_94 (buffer_94_out, buffer_93_out);
  buf buffer_95 (buffer_95_out, buffer_98_out);
  buf buffer_96 (buffer_96_out, buffer_95_out);
  buf buffer_97 (buffer_97_out, buffer_96_out);
  buf buffer_98 (buffer_98_out, buffer_82_out);
  buf buffer_99 (buffer_99_out, buffer_102_out);
  buf buffer_100 (buffer_100_out, buffer_117_out);
  buf buffer_101 (buffer_101_out, buffer_100_out);
  buf buffer_102 (buffer_102_out, buffer_101_out);
  buf buffer_103 (buffer_103_out, buffer_90_out);
  buf buffer_104 (buffer_104_out, buffer_103_out);
  buf buffer_105 (buffer_105_out, buffer_104_out);
  buf buffer_106 (buffer_106_out, buffer_105_out);
  buf buffer_107 (buffer_107_out, buffer_123_out);
  buf buffer_108 (buffer_108_out, buffer_109_out);
  buf buffer_109 (buffer_109_out, buffer_107_out);
  buf buffer_110 (buffer_110_out, buffer_108_out);
  buf buffer_111 (buffer_111_out, buffer_114_out);
  buf buffer_112 (buffer_112_out, buffer_113_out);
  buf buffer_113 (buffer_113_out, buffer_111_out);
  buf buffer_114 (buffer_114_out, buffer_97_out);
  buf buffer_115 (buffer_115_out, buffer_118_out);
  buf buffer_116 (buffer_116_out, buffer_115_out);
  buf buffer_117 (buffer_117_out, buffer_116_out);
  buf buffer_118 (buffer_118_out, buffer_127_out);
  buf buffer_119 (buffer_119_out, buffer_106_out);
  buf buffer_120 (buffer_120_out, buffer_119_out);
  buf buffer_121 (buffer_121_out, buffer_120_out);
  buf buffer_122 (buffer_122_out, buffer_121_out);
  buf buffer_123 (buffer_123_out, buffer_122_out);
  buf buffer_124 (buffer_124_out, buffer_126_out);
  buf buffer_125 (buffer_125_out, buffer_124_out);
  buf buffer_126 (buffer_126_out, buffer_112_out);
  buf buffer_127 (buffer_127_out, buffer_128_out);
  buf buffer_128 (buffer_128_out, buffer_125_out);
endmodule

module sign_controller (
  input  [31:0] in_1,
  input  [31:0] in_2,
  output out_3,
  output [31:0] out_4,
  output [31:0] out_5
);

  wire not_1_out, not_2_out;
  wire [31:0] negator_1_out, negator_2_out;

  not not_1 (not_1_out, in_1[31]);
  Negator #(.width(32)) negator_1 (.in(in_1), .out(negator_1_out));
  not not_2 (not_2_out, in_2[31]);
  Negator #(.width(32)) negator_2 (.in(in_2), .out(negator_2_out));
  Multiplexer #(.width(32), .enable("false")) multiplexer_1 (
    .in0(negator_1_out), .in1(in_1), .out(out_4), .sel(not_1_out));
  Multiplexer #(.width(32), .enable("false")) multiplexer_2 (
    .in0(negator_2_out), .in1(in_2), .out(out_5), .sel(not_2_out));
  xnor xnor_1 (out_3, not_1_out, not_2_out);
endmodule
module _16bit_Lshifter (
  input  [15:0] in_1,
  input  [3:0] in_2,
  input  in_3,
  output [15:0] out_4,
  output [15:0] out_5
);

  wire decoder_1_out1, decoder_1_out2, decoder_1_out3, decoder_1_out4, decoder_1_out5, decoder_1_out6,
       decoder_1_out7, decoder_1_out8, decoder_1_out9, decoder_1_out10, decoder_1_out11, decoder_1_out12,
       decoder_1_out13, decoder_1_out14, decoder_1_out15, demultiplexer_1_out1, demultiplexer_2_out0,
       demultiplexer_2_out1, demultiplexer_3_out0, demultiplexer_3_out1, demultiplexer_4_out0,
       demultiplexer_4_out1, demultiplexer_5_out0, demultiplexer_5_out1, demultiplexer_6_out0,
       demultiplexer_6_out1, demultiplexer_7_out0, demultiplexer_7_out1, demultiplexer_8_out0,
       demultiplexer_8_out1, demultiplexer_9_out0, demultiplexer_9_out1, demultiplexer_10_out0,
       demultiplexer_10_out1, demultiplexer_11_out0, demultiplexer_11_out1, demultiplexer_12_out0,
       demultiplexer_12_out1, demultiplexer_13_out0, demultiplexer_13_out1, demultiplexer_14_out0,
       demultiplexer_14_out1, demultiplexer_15_out0, demultiplexer_15_out1, demultiplexer_16_out0,
       demultiplexer_16_out1, demultiplexer_17_out1, demultiplexer_18_out0, demultiplexer_18_out1,
       demultiplexer_19_out0, demultiplexer_19_out1, demultiplexer_20_out0, demultiplexer_20_out1,
       demultiplexer_21_out0, demultiplexer_21_out1, demultiplexer_22_out0, demultiplexer_22_out1,
       demultiplexer_23_out0, demultiplexer_23_out1, demultiplexer_24_out0, demultiplexer_24_out1,
       demultiplexer_25_out0, demultiplexer_25_out1, demultiplexer_26_out0, demultiplexer_26_out1,
       demultiplexer_27_out0, demultiplexer_27_out1, demultiplexer_28_out0, demultiplexer_28_out1,
       demultiplexer_29_out0, demultiplexer_29_out1, demultiplexer_30_out0, demultiplexer_30_out1,
       demultiplexer_31_out0, demultiplexer_31_out1, demultiplexer_32_out0, demultiplexer_32_out1,
       demultiplexer_33_out1, demultiplexer_34_out0, demultiplexer_34_out1, demultiplexer_35_out0,
       demultiplexer_35_out1, demultiplexer_36_out0, demultiplexer_36_out1, demultiplexer_37_out0,
       demultiplexer_37_out1, demultiplexer_38_out0, demultiplexer_38_out1, demultiplexer_39_out0,
       demultiplexer_39_out1, demultiplexer_40_out0, demultiplexer_40_out1, demultiplexer_41_out0,
       demultiplexer_41_out1, demultiplexer_42_out0, demultiplexer_42_out1, demultiplexer_43_out0,
       demultiplexer_43_out1, demultiplexer_44_out0, demultiplexer_44_out1, demultiplexer_45_out0,
       demultiplexer_45_out1, demultiplexer_46_out0, demultiplexer_46_out1, demultiplexer_47_out0,
       demultiplexer_47_out1, demultiplexer_48_out0, demultiplexer_48_out1, demultiplexer_49_out1,
       demultiplexer_50_out0, demultiplexer_50_out1, demultiplexer_51_out0, demultiplexer_51_out1,
       demultiplexer_52_out0, demultiplexer_52_out1, demultiplexer_53_out0, demultiplexer_53_out1,
       demultiplexer_54_out0, demultiplexer_54_out1, demultiplexer_55_out0, demultiplexer_55_out1,
       demultiplexer_56_out0, demultiplexer_56_out1, demultiplexer_57_out0, demultiplexer_57_out1,
       demultiplexer_58_out0, demultiplexer_58_out1, demultiplexer_59_out0, demultiplexer_59_out1,
       demultiplexer_60_out0, demultiplexer_60_out1, demultiplexer_61_out0, demultiplexer_61_out1,
       demultiplexer_62_out0, demultiplexer_62_out1, demultiplexer_63_out0, demultiplexer_63_out1,
       demultiplexer_64_out0, demultiplexer_64_out1, demultiplexer_65_out1, demultiplexer_66_out0,
       demultiplexer_66_out1, demultiplexer_67_out0, demultiplexer_67_out1, demultiplexer_68_out0,
       demultiplexer_68_out1, demultiplexer_69_out0, demultiplexer_69_out1, demultiplexer_70_out0,
       demultiplexer_70_out1, demultiplexer_71_out0, demultiplexer_71_out1, demultiplexer_72_out0,
       demultiplexer_72_out1, demultiplexer_73_out0, demultiplexer_73_out1, demultiplexer_74_out0,
       demultiplexer_74_out1, demultiplexer_75_out0, demultiplexer_75_out1, demultiplexer_76_out0,
       demultiplexer_76_out1, demultiplexer_77_out0, demultiplexer_77_out1, demultiplexer_78_out0,
       demultiplexer_78_out1, demultiplexer_79_out0, demultiplexer_79_out1, demultiplexer_80_out0,
       demultiplexer_80_out1, demultiplexer_81_out1, demultiplexer_82_out0, demultiplexer_82_out1,
       demultiplexer_83_out0, demultiplexer_83_out1, demultiplexer_84_out0, demultiplexer_84_out1,
       demultiplexer_85_out0, demultiplexer_85_out1, demultiplexer_86_out0, demultiplexer_86_out1,
       demultiplexer_87_out0, demultiplexer_87_out1, demultiplexer_88_out0, demultiplexer_88_out1,
       demultiplexer_89_out0, demultiplexer_89_out1, demultiplexer_90_out0, demultiplexer_90_out1,
       demultiplexer_91_out0, demultiplexer_91_out1, demultiplexer_92_out0, demultiplexer_92_out1,
       demultiplexer_93_out0, demultiplexer_93_out1, demultiplexer_94_out0, demultiplexer_94_out1,
       demultiplexer_95_out0, demultiplexer_95_out1, demultiplexer_96_out0, demultiplexer_96_out1,
       demultiplexer_97_out1, demultiplexer_98_out0, demultiplexer_98_out1, demultiplexer_99_out0,
       demultiplexer_99_out1, demultiplexer_100_out0, demultiplexer_100_out1, demultiplexer_101_out0,
       demultiplexer_101_out1, demultiplexer_102_out0, demultiplexer_102_out1, demultiplexer_103_out0,
       demultiplexer_103_out1, demultiplexer_104_out0, demultiplexer_104_out1, demultiplexer_105_out0,
       demultiplexer_105_out1, demultiplexer_106_out0, demultiplexer_106_out1, demultiplexer_107_out0,
       demultiplexer_107_out1, demultiplexer_108_out0, demultiplexer_108_out1, demultiplexer_109_out0,
       demultiplexer_109_out1, demultiplexer_110_out0, demultiplexer_110_out1, demultiplexer_111_out0,
       demultiplexer_111_out1, demultiplexer_112_out0, demultiplexer_112_out1, demultiplexer_113_out1,
       demultiplexer_114_out0, demultiplexer_114_out1, demultiplexer_115_out0, demultiplexer_115_out1,
       demultiplexer_116_out0, demultiplexer_116_out1, demultiplexer_117_out0, demultiplexer_117_out1,
       demultiplexer_118_out0, demultiplexer_118_out1, demultiplexer_119_out0, demultiplexer_119_out1,
       demultiplexer_120_out0, demultiplexer_120_out1, demultiplexer_121_out0, demultiplexer_121_out1,
       demultiplexer_122_out0, demultiplexer_122_out1, demultiplexer_123_out0, demultiplexer_123_out1,
       demultiplexer_124_out0, demultiplexer_124_out1, demultiplexer_125_out0, demultiplexer_125_out1,
       demultiplexer_126_out0, demultiplexer_126_out1, demultiplexer_127_out0, demultiplexer_127_out1,
       demultiplexer_128_out0, demultiplexer_128_out1, demultiplexer_129_out1, demultiplexer_130_out0,
       demultiplexer_130_out1, demultiplexer_131_out0, demultiplexer_131_out1, demultiplexer_132_out0,
       demultiplexer_132_out1, demultiplexer_133_out0, demultiplexer_133_out1, demultiplexer_134_out0,
       demultiplexer_134_out1, demultiplexer_135_out0, demultiplexer_135_out1, demultiplexer_136_out0,
       demultiplexer_136_out1, demultiplexer_137_out0, demultiplexer_137_out1, demultiplexer_138_out0,
       demultiplexer_138_out1, demultiplexer_139_out0, demultiplexer_139_out1, demultiplexer_140_out0,
       demultiplexer_140_out1, demultiplexer_141_out0, demultiplexer_141_out1, demultiplexer_142_out0,
       demultiplexer_142_out1, demultiplexer_143_out0, demultiplexer_143_out1, demultiplexer_144_out0,
       demultiplexer_144_out1, demultiplexer_145_out1, demultiplexer_146_out0, demultiplexer_146_out1,
       demultiplexer_147_out0, demultiplexer_147_out1, demultiplexer_148_out0, demultiplexer_148_out1,
       demultiplexer_149_out0, demultiplexer_149_out1, demultiplexer_150_out0, demultiplexer_150_out1,
       demultiplexer_151_out0, demultiplexer_151_out1, demultiplexer_152_out0, demultiplexer_152_out1,
       demultiplexer_153_out0, demultiplexer_153_out1, demultiplexer_154_out0, demultiplexer_154_out1,
       demultiplexer_155_out0, demultiplexer_155_out1, demultiplexer_156_out0, demultiplexer_156_out1,
       demultiplexer_157_out0, demultiplexer_157_out1, demultiplexer_158_out0, demultiplexer_158_out1,
       demultiplexer_159_out0, demultiplexer_159_out1, demultiplexer_160_out0, demultiplexer_160_out1,
       demultiplexer_161_out1, demultiplexer_162_out0, demultiplexer_162_out1, demultiplexer_163_out0,
       demultiplexer_163_out1, demultiplexer_164_out0, demultiplexer_164_out1, demultiplexer_165_out0,
       demultiplexer_165_out1, demultiplexer_166_out0, demultiplexer_166_out1, demultiplexer_167_out0,
       demultiplexer_167_out1, demultiplexer_168_out0, demultiplexer_168_out1, demultiplexer_169_out0,
       demultiplexer_169_out1, demultiplexer_170_out0, demultiplexer_170_out1, demultiplexer_171_out0,
       demultiplexer_171_out1, demultiplexer_172_out0, demultiplexer_172_out1, demultiplexer_173_out0,
       demultiplexer_173_out1, demultiplexer_174_out0, demultiplexer_174_out1, demultiplexer_175_out0,
       demultiplexer_175_out1, demultiplexer_176_out0, demultiplexer_176_out1, demultiplexer_177_out1,
       demultiplexer_178_out0, demultiplexer_178_out1, demultiplexer_179_out0, demultiplexer_179_out1,
       demultiplexer_180_out0, demultiplexer_180_out1, demultiplexer_181_out0, demultiplexer_181_out1,
       demultiplexer_182_out0, demultiplexer_182_out1, demultiplexer_183_out0, demultiplexer_183_out1,
       demultiplexer_184_out0, demultiplexer_184_out1, demultiplexer_185_out0, demultiplexer_185_out1,
       demultiplexer_186_out0, demultiplexer_186_out1, demultiplexer_187_out0, demultiplexer_187_out1,
       demultiplexer_188_out0, demultiplexer_188_out1, demultiplexer_189_out0, demultiplexer_189_out1,
       demultiplexer_190_out0, demultiplexer_190_out1, demultiplexer_191_out0, demultiplexer_191_out1,
       demultiplexer_192_out0, demultiplexer_192_out1, demultiplexer_193_out1, demultiplexer_194_out0,
       demultiplexer_194_out1, demultiplexer_195_out0, demultiplexer_195_out1, demultiplexer_196_out0,
       demultiplexer_196_out1, demultiplexer_197_out0, demultiplexer_197_out1, demultiplexer_198_out0,
       demultiplexer_198_out1, demultiplexer_199_out0, demultiplexer_199_out1, demultiplexer_200_out0,
       demultiplexer_200_out1, demultiplexer_201_out0, demultiplexer_201_out1, demultiplexer_202_out0,
       demultiplexer_202_out1, demultiplexer_203_out0, demultiplexer_203_out1, demultiplexer_204_out0,
       demultiplexer_204_out1, demultiplexer_205_out0, demultiplexer_205_out1, demultiplexer_206_out0,
       demultiplexer_206_out1, demultiplexer_207_out0, demultiplexer_207_out1, demultiplexer_208_out0,
       demultiplexer_208_out1, demultiplexer_209_out1, demultiplexer_210_out0, demultiplexer_210_out1,
       demultiplexer_211_out0, demultiplexer_211_out1, demultiplexer_212_out0, demultiplexer_212_out1,
       demultiplexer_213_out0, demultiplexer_213_out1, demultiplexer_214_out0, demultiplexer_214_out1,
       demultiplexer_215_out0, demultiplexer_215_out1, demultiplexer_216_out0, demultiplexer_216_out1,
       demultiplexer_217_out0, demultiplexer_217_out1, demultiplexer_218_out0, demultiplexer_218_out1,
       demultiplexer_219_out0, demultiplexer_219_out1, demultiplexer_220_out0, demultiplexer_220_out1,
       demultiplexer_221_out0, demultiplexer_221_out1, demultiplexer_222_out0, demultiplexer_222_out1,
       demultiplexer_223_out0, demultiplexer_223_out1, demultiplexer_224_out0, demultiplexer_224_out1,
       demultiplexer_225_out1, demultiplexer_226_out0, demultiplexer_226_out1, demultiplexer_227_out0,
       demultiplexer_227_out1, demultiplexer_228_out0, demultiplexer_228_out1, demultiplexer_229_out0,
       demultiplexer_229_out1, demultiplexer_230_out0, demultiplexer_230_out1, demultiplexer_231_out0,
       demultiplexer_231_out1, demultiplexer_232_out0, demultiplexer_232_out1, demultiplexer_233_out0,
       demultiplexer_233_out1, demultiplexer_234_out0, demultiplexer_234_out1, demultiplexer_235_out0,
       demultiplexer_235_out1, demultiplexer_236_out0, demultiplexer_236_out1, demultiplexer_237_out0,
       demultiplexer_237_out1, demultiplexer_238_out0, demultiplexer_238_out1, demultiplexer_239_out0,
       demultiplexer_239_out1, demultiplexer_240_out0, or_1_out, or_2_out, or_3_out, or_4_out, or_5_out,
       or_6_out, or_7_out, or_8_out, or_9_out, or_10_out, or_11_out, or_12_out, or_13_out, or_14_out,
       or_15_out, or_16_out, or_17_out, or_18_out, or_19_out, or_20_out, or_21_out, or_22_out, or_23_out,
       or_24_out, or_25_out, or_26_out, or_27_out, or_28_out, or_29_out, or_30_out, or_31_out, or_32_out,
       or_33_out, or_34_out, or_35_out, or_36_out, or_37_out, or_38_out, or_39_out, or_40_out, or_41_out,
       or_42_out, or_43_out, or_44_out, or_45_out, or_46_out, or_47_out, or_48_out, or_49_out, or_50_out,
       or_51_out, or_52_out, or_53_out, or_54_out, or_55_out, or_56_out, or_57_out, or_58_out, or_59_out,
       or_60_out, or_61_out, or_62_out, or_63_out, or_64_out, or_65_out, or_66_out, or_67_out, or_68_out,
       or_69_out, or_70_out, or_71_out, or_72_out, or_73_out, or_74_out, or_75_out, or_76_out, or_77_out,
       or_78_out, or_79_out, or_80_out, or_81_out, or_82_out, or_83_out, or_84_out, or_85_out, or_86_out,
       or_87_out, or_88_out, or_89_out, or_90_out, or_91_out, or_92_out, or_93_out, or_94_out, or_95_out,
       or_96_out, or_97_out, or_98_out, or_99_out, or_100_out, or_101_out, or_102_out, or_103_out,
       or_104_out, or_105_out, or_106_out, or_107_out, or_108_out, or_109_out, or_110_out, or_111_out,
       or_112_out, or_113_out, or_114_out, or_115_out, or_116_out, or_117_out, or_118_out, or_119_out,
       or_120_out, or_121_out, or_122_out, or_123_out, or_124_out, or_125_out, or_126_out, or_127_out,
       or_128_out, or_129_out, or_130_out, or_131_out, or_132_out, or_133_out, or_134_out, or_135_out,
       or_136_out, or_137_out, or_138_out, or_139_out, or_140_out, or_141_out, or_142_out, or_143_out,
       or_144_out, or_145_out, or_146_out, or_147_out, or_148_out, or_149_out, or_150_out, or_151_out,
       or_152_out, or_153_out, or_154_out, or_155_out, or_156_out, or_157_out, or_158_out, or_159_out,
       or_160_out, or_161_out, or_162_out, or_163_out, or_164_out, or_165_out, or_166_out, or_167_out,
       or_168_out, or_169_out, or_170_out, or_171_out, or_172_out, or_173_out, or_174_out, or_175_out,
       or_176_out, or_177_out, or_178_out, or_179_out, or_180_out, or_181_out, or_182_out, or_183_out,
       or_184_out, or_185_out, or_186_out, or_187_out, or_188_out, or_189_out, or_190_out, or_191_out,
       or_192_out, or_193_out, or_194_out, or_195_out, or_196_out, or_197_out, or_198_out, or_199_out,
       or_200_out, or_201_out, or_202_out, or_203_out, or_204_out, or_205_out, or_206_out, or_207_out,
       or_208_out, or_209_out, or_210_out, or_211_out, or_212_out, or_213_out, or_214_out, or_215_out,
       or_216_out, or_217_out, or_218_out, or_219_out, or_220_out, or_221_out, or_222_out, or_223_out,
       or_224_out;

  Decoder #(.select(4), .disabled(0)) decoder_1 (
    .out1(decoder_1_out1), .out2(decoder_1_out2), .out3(decoder_1_out3), .out4(decoder_1_out4),
    .out5(decoder_1_out5), .out6(decoder_1_out6), .out7(decoder_1_out7), .out8(decoder_1_out8),
    .out9(decoder_1_out9), .out10(decoder_1_out10), .out11(decoder_1_out11), .out12(decoder_1_out12),
    .out13(decoder_1_out13), .out14(decoder_1_out14), .out15(decoder_1_out15), .sel(in_2), .en(in_3));  // open: out0
  Demultiplexer #(.enable("false")) demultiplexer_1 (
    .out0(out_4[0]), .out1(demultiplexer_1_out1), .in(in_1[0]), .sel(or_1_out));
  Demultiplexer #(.enable("false")) demultiplexer_2 (
    .out0(demultiplexer_2_out0), .out1(demultiplexer_2_out1), .in(in_1[1]), .sel(or_1_out));
  Demultiplexer #(.enable("false")) demultiplexer_3 (
    .out0(demultiplexer_3_out0), .out1(demultiplexer_3_out1), .in(in_1[2]), .sel(or_1_out));
  Demultiplexer #(.enable("false")) demultiplexer_4 (
    .out0(demultiplexer_4_out0), .out1(demultiplexer_4_out1), .in(in_1[3]), .sel(or_1_out));
  Demultiplexer #(.enable("false")) demultiplexer_5 (
    .out0(demultiplexer_5_out0), .out1(demultiplexer_5_out1), .in(in_1[4]), .sel(or_1_out));
  Demultiplexer #(.enable("false")) demultiplexer_6 (
    .out0(demultiplexer_6_out0), .out1(demultiplexer_6_out1), .in(in_1[5]), .sel(or_1_out));
  Demultiplexer #(.enable("false")) demultiplexer_7 (
    .out0(demultiplexer_7_out0), .out1(demultiplexer_7_out1), .in(in_1[6]), .sel(or_1_out));
  Demultiplexer #(.enable("false")) demultiplexer_8 (
    .out0(demultiplexer_8_out0), .out1(demultiplexer_8_out1), .in(in_1[7]), .sel(or_1_out));
  Demultiplexer #(.enable("false")) demultiplexer_9 (
    .out0(demultiplexer_9_out0), .out1(demultiplexer_9_out1), .in(in_1[8]), .sel(or_1_out));
  Demultiplexer #(.enable("false")) demultiplexer_10 (
    .out0(demultiplexer_10_out0), .out1(demultiplexer_10_out1), .in(in_1[9]), .sel(or_1_out));
  Demultiplexer #(.enable("false")) demultiplexer_11 (
    .out0(demultiplexer_11_out0), .out1(demultiplexer_11_out1), .in(in_1[10]), .sel(or_1_out));
  Demultiplexer #(.enable("false")) demultiplexer_12 (
    .out0(demultiplexer_12_out0), .out1(demultiplexer_12_out1), .in(in_1[11]), .sel(or_1_out));
  Demultiplexer #(.enable("false")) demultiplexer_13 (
    .out0(demultiplexer_13_out0), .out1(demultiplexer_13_out1), .in(in_1[12]), .sel(or_1_out));
  Demultiplexer #(.enable("false")) demultiplexer_14 (
    .out0(demultiplexer_14_out0), .out1(demultiplexer_14_out1), .in(in_1[13]), .sel(or_1_out));
  Demultiplexer #(.enable("false")) demultiplexer_15 (
    .out0(demultiplexer_15_out0), .out1(demultiplexer_15_out1), .in(in_1[14]), .sel(or_1_out));
  Demultiplexer #(.enable("false")) demultiplexer_16 (
    .out0(demultiplexer_16_out0), .out1(demultiplexer_16_out1), .in(in_1[15]), .sel(or_1_out));
  or or_1 (or_1_out, decoder_1_out1, or_17_out);
  or or_2 (or_2_out, demultiplexer_1_out1, demultiplexer_2_out0);
  or or_3 (or_3_out, demultiplexer_2_out1, demultiplexer_3_out0);
  or or_4 (or_4_out, demultiplexer_3_out1, demultiplexer_4_out0);
  or or_5 (or_5_out, demultiplexer_4_out1, demultiplexer_5_out0);
  or or_6 (or_6_out, demultiplexer_5_out1, demultiplexer_6_out0);
  or or_7 (or_7_out, demultiplexer_6_out1, demultiplexer_7_out0);
  or or_8 (or_8_out, demultiplexer_7_out1, demultiplexer_8_out0);
  or or_9 (or_9_out, demultiplexer_8_out1, demultiplexer_9_out0);
  or or_10 (or_10_out, demultiplexer_9_out1, demultiplexer_10_out0);
  or or_11 (or_11_out, demultiplexer_10_out1, demultiplexer_11_out0);
  or or_12 (or_12_out, demultiplexer_11_out1, demultiplexer_12_out0);
  or or_13 (or_13_out, demultiplexer_12_out1, demultiplexer_13_out0);
  or or_14 (or_14_out, demultiplexer_13_out1, demultiplexer_14_out0);
  or or_15 (or_15_out, demultiplexer_14_out1, demultiplexer_15_out0);
  or or_16 (or_16_out, demultiplexer_15_out1, demultiplexer_16_out0);
  or or_17 (or_17_out, decoder_1_out2, or_33_out);
  Demultiplexer #(.enable("false")) demultiplexer_17 (
    .out0(out_4[1]), .out1(demultiplexer_17_out1), .in(or_2_out), .sel(or_17_out));
  Demultiplexer #(.enable("false")) demultiplexer_18 (
    .out0(demultiplexer_18_out0), .out1(demultiplexer_18_out1), .in(or_3_out), .sel(or_17_out));
  Demultiplexer #(.enable("false")) demultiplexer_19 (
    .out0(demultiplexer_19_out0), .out1(demultiplexer_19_out1), .in(or_4_out), .sel(or_17_out));
  Demultiplexer #(.enable("false")) demultiplexer_20 (
    .out0(demultiplexer_20_out0), .out1(demultiplexer_20_out1), .in(or_5_out), .sel(or_17_out));
  Demultiplexer #(.enable("false")) demultiplexer_21 (
    .out0(demultiplexer_21_out0), .out1(demultiplexer_21_out1), .in(or_6_out), .sel(or_17_out));
  Demultiplexer #(.enable("false")) demultiplexer_22 (
    .out0(demultiplexer_22_out0), .out1(demultiplexer_22_out1), .in(or_7_out), .sel(or_17_out));
  Demultiplexer #(.enable("false")) demultiplexer_23 (
    .out0(demultiplexer_23_out0), .out1(demultiplexer_23_out1), .in(or_8_out), .sel(or_17_out));
  Demultiplexer #(.enable("false")) demultiplexer_24 (
    .out0(demultiplexer_24_out0), .out1(demultiplexer_24_out1), .in(or_9_out), .sel(or_17_out));
  Demultiplexer #(.enable("false")) demultiplexer_25 (
    .out0(demultiplexer_25_out0), .out1(demultiplexer_25_out1), .in(or_10_out), .sel(or_17_out));
  Demultiplexer #(.enable("false")) demultiplexer_26 (
    .out0(demultiplexer_26_out0), .out1(demultiplexer_26_out1), .in(or_11_out), .sel(or_17_out));
  Demultiplexer #(.enable("false")) demultiplexer_27 (
    .out0(demultiplexer_27_out0), .out1(demultiplexer_27_out1), .in(or_12_out), .sel(or_17_out));
  Demultiplexer #(.enable("false")) demultiplexer_28 (
    .out0(demultiplexer_28_out0), .out1(demultiplexer_28_out1), .in(or_13_out), .sel(or_17_out));
  Demultiplexer #(.enable("false")) demultiplexer_29 (
    .out0(demultiplexer_29_out0), .out1(demultiplexer_29_out1), .in(or_14_out), .sel(or_17_out));
  Demultiplexer #(.enable("false")) demultiplexer_30 (
    .out0(demultiplexer_30_out0), .out1(demultiplexer_30_out1), .in(or_15_out), .sel(or_17_out));
  Demultiplexer #(.enable("false")) demultiplexer_31 (
    .out0(demultiplexer_31_out0), .out1(demultiplexer_31_out1), .in(or_16_out), .sel(or_17_out));
  Demultiplexer #(.enable("false")) demultiplexer_32 (
    .out0(demultiplexer_32_out0), .out1(demultiplexer_32_out1), .in(demultiplexer_16_out1), .sel(or_17_out));
  or or_18 (or_18_out, demultiplexer_17_out1, demultiplexer_18_out0);
  Demultiplexer #(.enable("false")) demultiplexer_33 (
    .out0(out_4[2]), .out1(demultiplexer_33_out1), .in(or_18_out), .sel(or_33_out));
  Demultiplexer #(.enable("false")) demultiplexer_34 (
    .out0(demultiplexer_34_out0), .out1(demultiplexer_34_out1), .in(or_19_out), .sel(or_33_out));
  or or_19 (or_19_out, demultiplexer_18_out1, demultiplexer_19_out0);
  Demultiplexer #(.enable("false")) demultiplexer_35 (
    .out0(demultiplexer_35_out0), .out1(demultiplexer_35_out1), .in(or_20_out), .sel(or_33_out));
  or or_20 (or_20_out, demultiplexer_19_out1, demultiplexer_20_out0);
  Demultiplexer #(.enable("false")) demultiplexer_36 (
    .out0(demultiplexer_36_out0), .out1(demultiplexer_36_out1), .in(or_21_out), .sel(or_33_out));
  or or_21 (or_21_out, demultiplexer_20_out1, demultiplexer_21_out0);
  or or_22 (or_22_out, demultiplexer_21_out1, demultiplexer_22_out0);
  Demultiplexer #(.enable("false")) demultiplexer_37 (
    .out0(demultiplexer_37_out0), .out1(demultiplexer_37_out1), .in(or_22_out), .sel(or_33_out));
  or or_23 (or_23_out, demultiplexer_22_out1, demultiplexer_23_out0);
  Demultiplexer #(.enable("false")) demultiplexer_38 (
    .out0(demultiplexer_38_out0), .out1(demultiplexer_38_out1), .in(or_23_out), .sel(or_33_out));
  Demultiplexer #(.enable("false")) demultiplexer_39 (
    .out0(demultiplexer_39_out0), .out1(demultiplexer_39_out1), .in(or_24_out), .sel(or_33_out));
  or or_24 (or_24_out, demultiplexer_23_out1, demultiplexer_24_out0);
  or or_25 (or_25_out, demultiplexer_24_out1, demultiplexer_25_out0);
  Demultiplexer #(.enable("false")) demultiplexer_40 (
    .out0(demultiplexer_40_out0), .out1(demultiplexer_40_out1), .in(or_25_out), .sel(or_33_out));
  or or_26 (or_26_out, demultiplexer_25_out1, demultiplexer_26_out0);
  Demultiplexer #(.enable("false")) demultiplexer_41 (
    .out0(demultiplexer_41_out0), .out1(demultiplexer_41_out1), .in(or_26_out), .sel(or_33_out));
  Demultiplexer #(.enable("false")) demultiplexer_42 (
    .out0(demultiplexer_42_out0), .out1(demultiplexer_42_out1), .in(or_27_out), .sel(or_33_out));
  or or_27 (or_27_out, demultiplexer_26_out1, demultiplexer_27_out0);
  Demultiplexer #(.enable("false")) demultiplexer_43 (
    .out0(demultiplexer_43_out0), .out1(demultiplexer_43_out1), .in(or_28_out), .sel(or_33_out));
  or or_28 (or_28_out, demultiplexer_27_out1, demultiplexer_28_out0);
  or or_29 (or_29_out, demultiplexer_28_out1, demultiplexer_29_out0);
  Demultiplexer #(.enable("false")) demultiplexer_44 (
    .out0(demultiplexer_44_out0), .out1(demultiplexer_44_out1), .in(or_29_out), .sel(or_33_out));
  or or_30 (or_30_out, demultiplexer_29_out1, demultiplexer_30_out0);
  Demultiplexer #(.enable("false")) demultiplexer_45 (
    .out0(demultiplexer_45_out0), .out1(demultiplexer_45_out1), .in(or_30_out), .sel(or_33_out));
  or or_31 (or_31_out, demultiplexer_30_out1, demultiplexer_31_out0);
  Demultiplexer #(.enable("false")) demultiplexer_46 (
    .out0(demultiplexer_46_out0), .out1(demultiplexer_46_out1), .in(or_31_out), .sel(or_33_out));
  or or_32 (or_32_out, demultiplexer_31_out1, demultiplexer_32_out0);
  Demultiplexer #(.enable("false")) demultiplexer_47 (
    .out0(demultiplexer_47_out0), .out1(demultiplexer_47_out1), .in(or_32_out), .sel(or_33_out));
  Demultiplexer #(.enable("false")) demultiplexer_48 (
    .out0(demultiplexer_48_out0), .out1(demultiplexer_48_out1), .in(demultiplexer_32_out1), .sel(or_33_out));
  or or_33 (or_33_out, decoder_1_out3, or_49_out);
  or or_34 (or_34_out, demultiplexer_33_out1, demultiplexer_34_out0);
  Demultiplexer #(.enable("false")) demultiplexer_49 (
    .out0(out_4[3]), .out1(demultiplexer_49_out1), .in(or_34_out), .sel(or_49_out));
  Demultiplexer #(.enable("false")) demultiplexer_50 (
    .out0(demultiplexer_50_out0), .out1(demultiplexer_50_out1), .in(or_35_out), .sel(or_49_out));
  or or_35 (or_35_out, demultiplexer_34_out1, demultiplexer_35_out0);
  Demultiplexer #(.enable("false")) demultiplexer_51 (
    .out0(demultiplexer_51_out0), .out1(demultiplexer_51_out1), .in(or_36_out), .sel(or_49_out));
  or or_36 (or_36_out, demultiplexer_35_out1, demultiplexer_36_out0);
  or or_37 (or_37_out, demultiplexer_36_out1, demultiplexer_37_out0);
  Demultiplexer #(.enable("false")) demultiplexer_52 (
    .out0(demultiplexer_52_out0), .out1(demultiplexer_52_out1), .in(or_37_out), .sel(or_49_out));
  or or_38 (or_38_out, demultiplexer_37_out1, demultiplexer_38_out0);
  Demultiplexer #(.enable("false")) demultiplexer_53 (
    .out0(demultiplexer_53_out0), .out1(demultiplexer_53_out1), .in(or_38_out), .sel(or_49_out));
  or or_39 (or_39_out, demultiplexer_38_out1, demultiplexer_39_out0);
  Demultiplexer #(.enable("false")) demultiplexer_54 (
    .out0(demultiplexer_54_out0), .out1(demultiplexer_54_out1), .in(or_39_out), .sel(or_49_out));
  Demultiplexer #(.enable("false")) demultiplexer_55 (
    .out0(demultiplexer_55_out0), .out1(demultiplexer_55_out1), .in(or_40_out), .sel(or_49_out));
  or or_40 (or_40_out, demultiplexer_39_out1, demultiplexer_40_out0);
  Demultiplexer #(.enable("false")) demultiplexer_56 (
    .out0(demultiplexer_56_out0), .out1(demultiplexer_56_out1), .in(or_41_out), .sel(or_49_out));
  or or_41 (or_41_out, demultiplexer_40_out1, demultiplexer_41_out0);
  Demultiplexer #(.enable("false")) demultiplexer_57 (
    .out0(demultiplexer_57_out0), .out1(demultiplexer_57_out1), .in(or_42_out), .sel(or_49_out));
  or or_42 (or_42_out, demultiplexer_41_out1, demultiplexer_42_out0);
  Demultiplexer #(.enable("false")) demultiplexer_58 (
    .out0(demultiplexer_58_out0), .out1(demultiplexer_58_out1), .in(or_43_out), .sel(or_49_out));
  or or_43 (or_43_out, demultiplexer_42_out1, demultiplexer_43_out0);
  Demultiplexer #(.enable("false")) demultiplexer_59 (
    .out0(demultiplexer_59_out0), .out1(demultiplexer_59_out1), .in(or_44_out), .sel(or_49_out));
  or or_44 (or_44_out, demultiplexer_43_out1, demultiplexer_44_out0);
  Demultiplexer #(.enable("false")) demultiplexer_60 (
    .out0(demultiplexer_60_out0), .out1(demultiplexer_60_out1), .in(or_45_out), .sel(or_49_out));
  or or_45 (or_45_out, demultiplexer_44_out1, demultiplexer_45_out0);
  Demultiplexer #(.enable("false")) demultiplexer_61 (
    .out0(demultiplexer_61_out0), .out1(demultiplexer_61_out1), .in(or_46_out), .sel(or_49_out));
  or or_46 (or_46_out, demultiplexer_45_out1, demultiplexer_46_out0);
  or or_47 (or_47_out, demultiplexer_46_out1, demultiplexer_47_out0);
  Demultiplexer #(.enable("false")) demultiplexer_62 (
    .out0(demultiplexer_62_out0), .out1(demultiplexer_62_out1), .in(or_47_out), .sel(or_49_out));
  or or_48 (or_48_out, demultiplexer_47_out1, demultiplexer_48_out0);
  Demultiplexer #(.enable("false")) demultiplexer_63 (
    .out0(demultiplexer_63_out0), .out1(demultiplexer_63_out1), .in(or_48_out), .sel(or_49_out));
  Demultiplexer #(.enable("false")) demultiplexer_64 (
    .out0(demultiplexer_64_out0), .out1(demultiplexer_64_out1), .in(demultiplexer_48_out1), .sel(or_49_out));
  or or_49 (or_49_out, decoder_1_out4, or_65_out);
  or or_50 (or_50_out, demultiplexer_49_out1, demultiplexer_50_out0);
  Demultiplexer #(.enable("false")) demultiplexer_65 (
    .out0(out_4[4]), .out1(demultiplexer_65_out1), .in(or_50_out), .sel(or_65_out));
  or or_51 (or_51_out, demultiplexer_50_out1, demultiplexer_51_out0);
  Demultiplexer #(.enable("false")) demultiplexer_66 (
    .out0(demultiplexer_66_out0), .out1(demultiplexer_66_out1), .in(or_51_out), .sel(or_65_out));
  Demultiplexer #(.enable("false")) demultiplexer_67 (
    .out0(demultiplexer_67_out0), .out1(demultiplexer_67_out1), .in(or_52_out), .sel(or_65_out));
  or or_52 (or_52_out, demultiplexer_51_out1, demultiplexer_52_out0);
  or or_53 (or_53_out, demultiplexer_52_out1, demultiplexer_53_out0);
  Demultiplexer #(.enable("false")) demultiplexer_68 (
    .out0(demultiplexer_68_out0), .out1(demultiplexer_68_out1), .in(or_53_out), .sel(or_65_out));
  Demultiplexer #(.enable("false")) demultiplexer_69 (
    .out0(demultiplexer_69_out0), .out1(demultiplexer_69_out1), .in(or_54_out), .sel(or_65_out));
  or or_54 (or_54_out, demultiplexer_53_out1, demultiplexer_54_out0);
  Demultiplexer #(.enable("false")) demultiplexer_70 (
    .out0(demultiplexer_70_out0), .out1(demultiplexer_70_out1), .in(or_55_out), .sel(or_65_out));
  or or_55 (or_55_out, demultiplexer_54_out1, demultiplexer_55_out0);
  Demultiplexer #(.enable("false")) demultiplexer_71 (
    .out0(demultiplexer_71_out0), .out1(demultiplexer_71_out1), .in(or_56_out), .sel(or_65_out));
  or or_56 (or_56_out, demultiplexer_55_out1, demultiplexer_56_out0);
  Demultiplexer #(.enable("false")) demultiplexer_72 (
    .out0(demultiplexer_72_out0), .out1(demultiplexer_72_out1), .in(or_57_out), .sel(or_65_out));
  or or_57 (or_57_out, demultiplexer_56_out1, demultiplexer_57_out0);
  Demultiplexer #(.enable("false")) demultiplexer_73 (
    .out0(demultiplexer_73_out0), .out1(demultiplexer_73_out1), .in(or_58_out), .sel(or_65_out));
  or or_58 (or_58_out, demultiplexer_57_out1, demultiplexer_58_out0);
  or or_59 (or_59_out, demultiplexer_58_out1, demultiplexer_59_out0);
  Demultiplexer #(.enable("false")) demultiplexer_74 (
    .out0(demultiplexer_74_out0), .out1(demultiplexer_74_out1), .in(or_59_out), .sel(or_65_out));
  or or_60 (or_60_out, demultiplexer_59_out1, demultiplexer_60_out0);
  Demultiplexer #(.enable("false")) demultiplexer_75 (
    .out0(demultiplexer_75_out0), .out1(demultiplexer_75_out1), .in(or_60_out), .sel(or_65_out));
  or or_61 (or_61_out, demultiplexer_60_out1, demultiplexer_61_out0);
  Demultiplexer #(.enable("false")) demultiplexer_76 (
    .out0(demultiplexer_76_out0), .out1(demultiplexer_76_out1), .in(or_61_out), .sel(or_65_out));
  Demultiplexer #(.enable("false")) demultiplexer_77 (
    .out0(demultiplexer_77_out0), .out1(demultiplexer_77_out1), .in(or_62_out), .sel(or_65_out));
  or or_62 (or_62_out, demultiplexer_61_out1, demultiplexer_62_out0);
  or or_63 (or_63_out, demultiplexer_62_out1, demultiplexer_63_out0);
  Demultiplexer #(.enable("false")) demultiplexer_78 (
    .out0(demultiplexer_78_out0), .out1(demultiplexer_78_out1), .in(or_63_out), .sel(or_65_out));
  Demultiplexer #(.enable("false")) demultiplexer_79 (
    .out0(demultiplexer_79_out0), .out1(demultiplexer_79_out1), .in(or_64_out), .sel(or_65_out));
  or or_64 (or_64_out, demultiplexer_63_out1, demultiplexer_64_out0);
  Demultiplexer #(.enable("false")) demultiplexer_80 (
    .out0(demultiplexer_80_out0), .out1(demultiplexer_80_out1), .in(demultiplexer_64_out1), .sel(or_65_out));
  or or_65 (or_65_out, decoder_1_out5, or_81_out);
  or or_66 (or_66_out, demultiplexer_65_out1, demultiplexer_66_out0);
  or or_67 (or_67_out, demultiplexer_66_out1, demultiplexer_67_out0);
  or or_68 (or_68_out, demultiplexer_67_out1, demultiplexer_68_out0);
  or or_69 (or_69_out, demultiplexer_68_out1, demultiplexer_69_out0);
  or or_70 (or_70_out, demultiplexer_69_out1, demultiplexer_70_out0);
  or or_71 (or_71_out, demultiplexer_70_out1, demultiplexer_71_out0);
  or or_72 (or_72_out, demultiplexer_71_out1, demultiplexer_72_out0);
  or or_73 (or_73_out, demultiplexer_72_out1, demultiplexer_73_out0);
  or or_74 (or_74_out, demultiplexer_73_out1, demultiplexer_74_out0);
  or or_75 (or_75_out, demultiplexer_74_out1, demultiplexer_75_out0);
  or or_76 (or_76_out, demultiplexer_75_out1, demultiplexer_76_out0);
  or or_77 (or_77_out, demultiplexer_76_out1, demultiplexer_77_out0);
  or or_78 (or_78_out, demultiplexer_77_out1, demultiplexer_78_out0);
  or or_79 (or_79_out, demultiplexer_78_out1, demultiplexer_79_out0);
  or or_80 (or_80_out, demultiplexer_79_out1, demultiplexer_80_out0);
  or or_81 (or_81_out, decoder_1_out6, or_97_out);
  Demultiplexer #(.enable("false")) demultiplexer_81 (
    .out0(out_4[5]), .out1(demultiplexer_81_out1), .in(or_66_out), .sel(or_81_out));
  Demultiplexer #(.enable("false")) demultiplexer_82 (
    .out0(demultiplexer_82_out0), .out1(demultiplexer_82_out1), .in(or_67_out), .sel(or_81_out));
  Demultiplexer #(.enable("false")) demultiplexer_83 (
    .out0(demultiplexer_83_out0), .out1(demultiplexer_83_out1), .in(or_68_out), .sel(or_81_out));
  Demultiplexer #(.enable("false")) demultiplexer_84 (
    .out0(demultiplexer_84_out0), .out1(demultiplexer_84_out1), .in(or_69_out), .sel(or_81_out));
  Demultiplexer #(.enable("false")) demultiplexer_85 (
    .out0(demultiplexer_85_out0), .out1(demultiplexer_85_out1), .in(or_70_out), .sel(or_81_out));
  Demultiplexer #(.enable("false")) demultiplexer_86 (
    .out0(demultiplexer_86_out0), .out1(demultiplexer_86_out1), .in(or_71_out), .sel(or_81_out));
  Demultiplexer #(.enable("false")) demultiplexer_87 (
    .out0(demultiplexer_87_out0), .out1(demultiplexer_87_out1), .in(or_72_out), .sel(or_81_out));
  Demultiplexer #(.enable("false")) demultiplexer_88 (
    .out0(demultiplexer_88_out0), .out1(demultiplexer_88_out1), .in(or_73_out), .sel(or_81_out));
  Demultiplexer #(.enable("false")) demultiplexer_89 (
    .out0(demultiplexer_89_out0), .out1(demultiplexer_89_out1), .in(or_74_out), .sel(or_81_out));
  Demultiplexer #(.enable("false")) demultiplexer_90 (
    .out0(demultiplexer_90_out0), .out1(demultiplexer_90_out1), .in(or_75_out), .sel(or_81_out));
  Demultiplexer #(.enable("false")) demultiplexer_91 (
    .out0(demultiplexer_91_out0), .out1(demultiplexer_91_out1), .in(or_76_out), .sel(or_81_out));
  Demultiplexer #(.enable("false")) demultiplexer_92 (
    .out0(demultiplexer_92_out0), .out1(demultiplexer_92_out1), .in(or_77_out), .sel(or_81_out));
  Demultiplexer #(.enable("false")) demultiplexer_93 (
    .out0(demultiplexer_93_out0), .out1(demultiplexer_93_out1), .in(or_78_out), .sel(or_81_out));
  Demultiplexer #(.enable("false")) demultiplexer_94 (
    .out0(demultiplexer_94_out0), .out1(demultiplexer_94_out1), .in(or_79_out), .sel(or_81_out));
  Demultiplexer #(.enable("false")) demultiplexer_95 (
    .out0(demultiplexer_95_out0), .out1(demultiplexer_95_out1), .in(or_80_out), .sel(or_81_out));
  Demultiplexer #(.enable("false")) demultiplexer_96 (
    .out0(demultiplexer_96_out0), .out1(demultiplexer_96_out1), .in(demultiplexer_80_out1), .sel(or_81_out));
  Demultiplexer #(.enable("false")) demultiplexer_97 (
    .out0(out_4[6]), .out1(demultiplexer_97_out1), .in(or_82_out), .sel(or_97_out));
  or or_82 (or_82_out, demultiplexer_81_out1, demultiplexer_82_out0);
  Demultiplexer #(.enable("false")) demultiplexer_98 (
    .out0(demultiplexer_98_out0), .out1(demultiplexer_98_out1), .in(or_83_out), .sel(or_97_out));
  or or_83 (or_83_out, demultiplexer_82_out1, demultiplexer_83_out0);
  or or_84 (or_84_out, demultiplexer_83_out1, demultiplexer_84_out0);
  Demultiplexer #(.enable("false")) demultiplexer_99 (
    .out0(demultiplexer_99_out0), .out1(demultiplexer_99_out1), .in(or_84_out), .sel(or_97_out));
  or or_85 (or_85_out, demultiplexer_84_out1, demultiplexer_85_out0);
  Demultiplexer #(.enable("false")) demultiplexer_100 (
    .out0(demultiplexer_100_out0), .out1(demultiplexer_100_out1), .in(or_85_out), .sel(or_97_out));
  or or_86 (or_86_out, demultiplexer_85_out1, demultiplexer_86_out0);
  Demultiplexer #(.enable("false")) demultiplexer_101 (
    .out0(demultiplexer_101_out0), .out1(demultiplexer_101_out1), .in(or_86_out), .sel(or_97_out));
  or or_87 (or_87_out, demultiplexer_86_out1, demultiplexer_87_out0);
  Demultiplexer #(.enable("false")) demultiplexer_102 (
    .out0(demultiplexer_102_out0), .out1(demultiplexer_102_out1), .in(or_87_out), .sel(or_97_out));
  or or_88 (or_88_out, demultiplexer_87_out1, demultiplexer_88_out0);
  Demultiplexer #(.enable("false")) demultiplexer_103 (
    .out0(demultiplexer_103_out0), .out1(demultiplexer_103_out1), .in(or_88_out), .sel(or_97_out));
  or or_89 (or_89_out, demultiplexer_88_out1, demultiplexer_89_out0);
  Demultiplexer #(.enable("false")) demultiplexer_104 (
    .out0(demultiplexer_104_out0), .out1(demultiplexer_104_out1), .in(or_89_out), .sel(or_97_out));
  or or_90 (or_90_out, demultiplexer_89_out1, demultiplexer_90_out0);
  Demultiplexer #(.enable("false")) demultiplexer_105 (
    .out0(demultiplexer_105_out0), .out1(demultiplexer_105_out1), .in(or_90_out), .sel(or_97_out));
  Demultiplexer #(.enable("false")) demultiplexer_106 (
    .out0(demultiplexer_106_out0), .out1(demultiplexer_106_out1), .in(or_91_out), .sel(or_97_out));
  or or_91 (or_91_out, demultiplexer_90_out1, demultiplexer_91_out0);
  or or_92 (or_92_out, demultiplexer_91_out1, demultiplexer_92_out0);
  Demultiplexer #(.enable("false")) demultiplexer_107 (
    .out0(demultiplexer_107_out0), .out1(demultiplexer_107_out1), .in(or_92_out), .sel(or_97_out));
  Demultiplexer #(.enable("false")) demultiplexer_108 (
    .out0(demultiplexer_108_out0), .out1(demultiplexer_108_out1), .in(or_93_out), .sel(or_97_out));
  or or_93 (or_93_out, demultiplexer_92_out1, demultiplexer_93_out0);
  Demultiplexer #(.enable("false")) demultiplexer_109 (
    .out0(demultiplexer_109_out0), .out1(demultiplexer_109_out1), .in(or_94_out), .sel(or_97_out));
  or or_94 (or_94_out, demultiplexer_93_out1, demultiplexer_94_out0);
  or or_95 (or_95_out, demultiplexer_94_out1, demultiplexer_95_out0);
  Demultiplexer #(.enable("false")) demultiplexer_110 (
    .out0(demultiplexer_110_out0), .out1(demultiplexer_110_out1), .in(or_95_out), .sel(or_97_out));
  or or_96 (or_96_out, demultiplexer_95_out1, demultiplexer_96_out0);
  Demultiplexer #(.enable("false")) demultiplexer_111 (
    .out0(demultiplexer_111_out0), .out1(demultiplexer_111_out1), .in(or_96_out), .sel(or_97_out));
  Demultiplexer #(.enable("false")) demultiplexer_112 (
    .out0(demultiplexer_112_out0), .out1(demultiplexer_112_out1), .in(demultiplexer_96_out1), .sel(or_97_out));
  or or_97 (or_97_out, decoder_1_out7, or_113_out);
  Demultiplexer #(.enable("false")) demultiplexer_113 (
    .out0(out_4[7]), .out1(demultiplexer_113_out1), .in(or_98_out), .sel(or_113_out));
  or or_98 (or_98_out, demultiplexer_97_out1, demultiplexer_98_out0);
  or or_99 (or_99_out, demultiplexer_98_out1, demultiplexer_99_out0);
  Demultiplexer #(.enable("false")) demultiplexer_114 (
    .out0(demultiplexer_114_out0), .out1(demultiplexer_114_out1), .in(or_99_out), .sel(or_113_out));
  or or_100 (or_100_out, demultiplexer_99_out1, demultiplexer_100_out0);
  Demultiplexer #(.enable("false")) demultiplexer_115 (
    .out0(demultiplexer_115_out0), .out1(demultiplexer_115_out1), .in(or_100_out), .sel(or_113_out));
  or or_101 (or_101_out, demultiplexer_100_out1, demultiplexer_101_out0);
  Demultiplexer #(.enable("false")) demultiplexer_116 (
    .out0(demultiplexer_116_out0), .out1(demultiplexer_116_out1), .in(or_101_out), .sel(or_113_out));
  or or_102 (or_102_out, demultiplexer_101_out1, demultiplexer_102_out0);
  Demultiplexer #(.enable("false")) demultiplexer_117 (
    .out0(demultiplexer_117_out0), .out1(demultiplexer_117_out1), .in(or_102_out), .sel(or_113_out));
  or or_103 (or_103_out, demultiplexer_102_out1, demultiplexer_103_out0);
  Demultiplexer #(.enable("false")) demultiplexer_118 (
    .out0(demultiplexer_118_out0), .out1(demultiplexer_118_out1), .in(or_103_out), .sel(or_113_out));
  or or_104 (or_104_out, demultiplexer_103_out1, demultiplexer_104_out0);
  Demultiplexer #(.enable("false")) demultiplexer_119 (
    .out0(demultiplexer_119_out0), .out1(demultiplexer_119_out1), .in(or_104_out), .sel(or_113_out));
  or or_105 (or_105_out, demultiplexer_104_out1, demultiplexer_105_out0);
  Demultiplexer #(.enable("false")) demultiplexer_120 (
    .out0(demultiplexer_120_out0), .out1(demultiplexer_120_out1), .in(or_105_out), .sel(or_113_out));
  or or_106 (or_106_out, demultiplexer_105_out1, demultiplexer_106_out0);
  Demultiplexer #(.enable("false")) demultiplexer_121 (
    .out0(demultiplexer_121_out0), .out1(demultiplexer_121_out1), .in(or_106_out), .sel(or_113_out));
  or or_107 (or_107_out, demultiplexer_106_out1, demultiplexer_107_out0);
  Demultiplexer #(.enable("false")) demultiplexer_122 (
    .out0(demultiplexer_122_out0), .out1(demultiplexer_122_out1), .in(or_107_out), .sel(or_113_out));
  or or_108 (or_108_out, demultiplexer_107_out1, demultiplexer_108_out0);
  Demultiplexer #(.enable("false")) demultiplexer_123 (
    .out0(demultiplexer_123_out0), .out1(demultiplexer_123_out1), .in(or_108_out), .sel(or_113_out));
  or or_109 (or_109_out, demultiplexer_108_out1, demultiplexer_109_out0);
  Demultiplexer #(.enable("false")) demultiplexer_124 (
    .out0(demultiplexer_124_out0), .out1(demultiplexer_124_out1), .in(or_109_out), .sel(or_113_out));
  Demultiplexer #(.enable("false")) demultiplexer_125 (
    .out0(demultiplexer_125_out0), .out1(demultiplexer_125_out1), .in(or_110_out), .sel(or_113_out));
  or or_110 (or_110_out, demultiplexer_109_out1, demultiplexer_110_out0);
  Demultiplexer #(.enable("false")) demultiplexer_126 (
    .out0(demultiplexer_126_out0), .out1(demultiplexer_126_out1), .in(or_111_out), .sel(or_113_out));
  or or_111 (or_111_out, demultiplexer_110_out1, demultiplexer_111_out0);
  Demultiplexer #(.enable("false")) demultiplexer_127 (
    .out0(demultiplexer_127_out0), .out1(demultiplexer_127_out1), .in(or_112_out), .sel(or_113_out));
  or or_112 (or_112_out, demultiplexer_111_out1, demultiplexer_112_out0);
  Demultiplexer #(.enable("false")) demultiplexer_128 (
    .out0(demultiplexer_128_out0), .out1(demultiplexer_128_out1), .in(demultiplexer_112_out1),
    .sel(or_113_out));
  or or_113 (or_113_out, decoder_1_out8, or_129_out);
  Demultiplexer #(.enable("false")) demultiplexer_129 (
    .out0(out_4[8]), .out1(demultiplexer_129_out1), .in(or_114_out), .sel(or_129_out));
  or or_114 (or_114_out, demultiplexer_113_out1, demultiplexer_114_out0);
  or or_115 (or_115_out, demultiplexer_114_out1, demultiplexer_115_out0);
  Demultiplexer #(.enable("false")) demultiplexer_130 (
    .out0(demultiplexer_130_out0), .out1(demultiplexer_130_out1), .in(or_115_out), .sel(or_129_out));
  or or_116 (or_116_out, demultiplexer_115_out1, demultiplexer_116_out0);
  Demultiplexer #(.enable("false")) demultiplexer_131 (
    .out0(demultiplexer_131_out0), .out1(demultiplexer_131_out1), .in(or_116_out), .sel(or_129_out));
  Demultiplexer #(.enable("false")) demultiplexer_132 (
    .out0(demultiplexer_132_out0), .out1(demultiplexer_132_out1), .in(or_117_out), .sel(or_129_out));
  or or_117 (or_117_out, demultiplexer_116_out1, demultiplexer_117_out0);
  Demultiplexer #(.enable("false")) demultiplexer_133 (
    .out0(demultiplexer_133_out0), .out1(demultiplexer_133_out1), .in(or_118_out), .sel(or_129_out));
  or or_118 (or_118_out, demultiplexer_117_out1, demultiplexer_118_out0);
  or or_119 (or_119_out, demultiplexer_118_out1, demultiplexer_119_out0);
  Demultiplexer #(.enable("false")) demultiplexer_134 (
    .out0(demultiplexer_134_out0), .out1(demultiplexer_134_out1), .in(or_119_out), .sel(or_129_out));
  or or_120 (or_120_out, demultiplexer_119_out1, demultiplexer_120_out0);
  Demultiplexer #(.enable("false")) demultiplexer_135 (
    .out0(demultiplexer_135_out0), .out1(demultiplexer_135_out1), .in(or_120_out), .sel(or_129_out));
  or or_121 (or_121_out, demultiplexer_120_out1, demultiplexer_121_out0);
  Demultiplexer #(.enable("false")) demultiplexer_136 (
    .out0(demultiplexer_136_out0), .out1(demultiplexer_136_out1), .in(or_121_out), .sel(or_129_out));
  or or_122 (or_122_out, demultiplexer_121_out1, demultiplexer_122_out0);
  Demultiplexer #(.enable("false")) demultiplexer_137 (
    .out0(demultiplexer_137_out0), .out1(demultiplexer_137_out1), .in(or_122_out), .sel(or_129_out));
  or or_123 (or_123_out, demultiplexer_122_out1, demultiplexer_123_out0);
  Demultiplexer #(.enable("false")) demultiplexer_138 (
    .out0(demultiplexer_138_out0), .out1(demultiplexer_138_out1), .in(or_123_out), .sel(or_129_out));
  Demultiplexer #(.enable("false")) demultiplexer_139 (
    .out0(demultiplexer_139_out0), .out1(demultiplexer_139_out1), .in(or_124_out), .sel(or_129_out));
  or or_124 (or_124_out, demultiplexer_123_out1, demultiplexer_124_out0);
  or or_125 (or_125_out, demultiplexer_124_out1, demultiplexer_125_out0);
  Demultiplexer #(.enable("false")) demultiplexer_140 (
    .out0(demultiplexer_140_out0), .out1(demultiplexer_140_out1), .in(or_125_out), .sel(or_129_out));
  Demultiplexer #(.enable("false")) demultiplexer_141 (
    .out0(demultiplexer_141_out0), .out1(demultiplexer_141_out1), .in(or_126_out), .sel(or_129_out));
  or or_126 (or_126_out, demultiplexer_125_out1, demultiplexer_126_out0);
  or or_127 (or_127_out, demultiplexer_126_out1, demultiplexer_127_out0);
  Demultiplexer #(.enable("false")) demultiplexer_142 (
    .out0(demultiplexer_142_out0), .out1(demultiplexer_142_out1), .in(or_127_out), .sel(or_129_out));
  Demultiplexer #(.enable("false")) demultiplexer_143 (
    .out0(demultiplexer_143_out0), .out1(demultiplexer_143_out1), .in(or_128_out), .sel(or_129_out));
  or or_128 (or_128_out, demultiplexer_127_out1, demultiplexer_128_out0);
  Demultiplexer #(.enable("false")) demultiplexer_144 (
    .out0(demultiplexer_144_out0), .out1(demultiplexer_144_out1), .in(demultiplexer_128_out1),
    .sel(or_129_out));
  or or_129 (or_129_out, decoder_1_out9, or_145_out);
  or or_130 (or_130_out, demultiplexer_129_out1, demultiplexer_130_out0);
  or or_131 (or_131_out, demultiplexer_130_out1, demultiplexer_131_out0);
  or or_132 (or_132_out, demultiplexer_131_out1, demultiplexer_132_out0);
  or or_133 (or_133_out, demultiplexer_132_out1, demultiplexer_133_out0);
  or or_134 (or_134_out, demultiplexer_133_out1, demultiplexer_134_out0);
  or or_135 (or_135_out, demultiplexer_134_out1, demultiplexer_135_out0);
  or or_136 (or_136_out, demultiplexer_135_out1, demultiplexer_136_out0);
  or or_137 (or_137_out, demultiplexer_136_out1, demultiplexer_137_out0);
  or or_138 (or_138_out, demultiplexer_137_out1, demultiplexer_138_out0);
  or or_139 (or_139_out, demultiplexer_138_out1, demultiplexer_139_out0);
  or or_140 (or_140_out, demultiplexer_139_out1, demultiplexer_140_out0);
  or or_141 (or_141_out, demultiplexer_140_out1, demultiplexer_141_out0);
  or or_142 (or_142_out, demultiplexer_141_out1, demultiplexer_142_out0);
  or or_143 (or_143_out, demultiplexer_142_out1, demultiplexer_143_out0);
  or or_144 (or_144_out, demultiplexer_143_out1, demultiplexer_144_out0);
  or or_145 (or_145_out, decoder_1_out10, or_161_out);
  Demultiplexer #(.enable("false")) demultiplexer_145 (
    .out0(out_4[9]), .out1(demultiplexer_145_out1), .in(or_130_out), .sel(or_145_out));
  Demultiplexer #(.enable("false")) demultiplexer_146 (
    .out0(demultiplexer_146_out0), .out1(demultiplexer_146_out1), .in(or_131_out), .sel(or_145_out));
  Demultiplexer #(.enable("false")) demultiplexer_147 (
    .out0(demultiplexer_147_out0), .out1(demultiplexer_147_out1), .in(or_132_out), .sel(or_145_out));
  Demultiplexer #(.enable("false")) demultiplexer_148 (
    .out0(demultiplexer_148_out0), .out1(demultiplexer_148_out1), .in(or_133_out), .sel(or_145_out));
  Demultiplexer #(.enable("false")) demultiplexer_149 (
    .out0(demultiplexer_149_out0), .out1(demultiplexer_149_out1), .in(or_134_out), .sel(or_145_out));
  Demultiplexer #(.enable("false")) demultiplexer_150 (
    .out0(demultiplexer_150_out0), .out1(demultiplexer_150_out1), .in(or_135_out), .sel(or_145_out));
  Demultiplexer #(.enable("false")) demultiplexer_151 (
    .out0(demultiplexer_151_out0), .out1(demultiplexer_151_out1), .in(or_136_out), .sel(or_145_out));
  Demultiplexer #(.enable("false")) demultiplexer_152 (
    .out0(demultiplexer_152_out0), .out1(demultiplexer_152_out1), .in(or_137_out), .sel(or_145_out));
  Demultiplexer #(.enable("false")) demultiplexer_153 (
    .out0(demultiplexer_153_out0), .out1(demultiplexer_153_out1), .in(or_138_out), .sel(or_145_out));
  Demultiplexer #(.enable("false")) demultiplexer_154 (
    .out0(demultiplexer_154_out0), .out1(demultiplexer_154_out1), .in(or_139_out), .sel(or_145_out));
  Demultiplexer #(.enable("false")) demultiplexer_155 (
    .out0(demultiplexer_155_out0), .out1(demultiplexer_155_out1), .in(or_140_out), .sel(or_145_out));
  Demultiplexer #(.enable("false")) demultiplexer_156 (
    .out0(demultiplexer_156_out0), .out1(demultiplexer_156_out1), .in(or_141_out), .sel(or_145_out));
  Demultiplexer #(.enable("false")) demultiplexer_157 (
    .out0(demultiplexer_157_out0), .out1(demultiplexer_157_out1), .in(or_142_out), .sel(or_145_out));
  Demultiplexer #(.enable("false")) demultiplexer_158 (
    .out0(demultiplexer_158_out0), .out1(demultiplexer_158_out1), .in(or_143_out), .sel(or_145_out));
  Demultiplexer #(.enable("false")) demultiplexer_159 (
    .out0(demultiplexer_159_out0), .out1(demultiplexer_159_out1), .in(or_144_out), .sel(or_145_out));
  Demultiplexer #(.enable("false")) demultiplexer_160 (
    .out0(demultiplexer_160_out0), .out1(demultiplexer_160_out1), .in(demultiplexer_144_out1),
    .sel(or_145_out));
  or or_146 (or_146_out, demultiplexer_145_out1, demultiplexer_146_out0);
  Demultiplexer #(.enable("false")) demultiplexer_161 (
    .out0(out_4[10]), .out1(demultiplexer_161_out1), .in(or_146_out), .sel(or_161_out));
  or or_147 (or_147_out, demultiplexer_146_out1, demultiplexer_147_out0);
  Demultiplexer #(.enable("false")) demultiplexer_162 (
    .out0(demultiplexer_162_out0), .out1(demultiplexer_162_out1), .in(or_147_out), .sel(or_161_out));
  Demultiplexer #(.enable("false")) demultiplexer_163 (
    .out0(demultiplexer_163_out0), .out1(demultiplexer_163_out1), .in(or_148_out), .sel(or_161_out));
  or or_148 (or_148_out, demultiplexer_147_out1, demultiplexer_148_out0);
  Demultiplexer #(.enable("false")) demultiplexer_164 (
    .out0(demultiplexer_164_out0), .out1(demultiplexer_164_out1), .in(or_149_out), .sel(or_161_out));
  or or_149 (or_149_out, demultiplexer_148_out1, demultiplexer_149_out0);
  or or_150 (or_150_out, demultiplexer_149_out1, demultiplexer_150_out0);
  Demultiplexer #(.enable("false")) demultiplexer_165 (
    .out0(demultiplexer_165_out0), .out1(demultiplexer_165_out1), .in(or_150_out), .sel(or_161_out));
  Demultiplexer #(.enable("false")) demultiplexer_166 (
    .out0(demultiplexer_166_out0), .out1(demultiplexer_166_out1), .in(or_151_out), .sel(or_161_out));
  or or_151 (or_151_out, demultiplexer_150_out1, demultiplexer_151_out0);
  Demultiplexer #(.enable("false")) demultiplexer_167 (
    .out0(demultiplexer_167_out0), .out1(demultiplexer_167_out1), .in(or_152_out), .sel(or_161_out));
  or or_152 (or_152_out, demultiplexer_151_out1, demultiplexer_152_out0);
  Demultiplexer #(.enable("false")) demultiplexer_168 (
    .out0(demultiplexer_168_out0), .out1(demultiplexer_168_out1), .in(or_153_out), .sel(or_161_out));
  or or_153 (or_153_out, demultiplexer_152_out1, demultiplexer_153_out0);
  or or_154 (or_154_out, demultiplexer_153_out1, demultiplexer_154_out0);
  Demultiplexer #(.enable("false")) demultiplexer_169 (
    .out0(demultiplexer_169_out0), .out1(demultiplexer_169_out1), .in(or_154_out), .sel(or_161_out));
  Demultiplexer #(.enable("false")) demultiplexer_170 (
    .out0(demultiplexer_170_out0), .out1(demultiplexer_170_out1), .in(or_155_out), .sel(or_161_out));
  or or_155 (or_155_out, demultiplexer_154_out1, demultiplexer_155_out0);
  Demultiplexer #(.enable("false")) demultiplexer_171 (
    .out0(demultiplexer_171_out0), .out1(demultiplexer_171_out1), .in(or_156_out), .sel(or_161_out));
  or or_156 (or_156_out, demultiplexer_155_out1, demultiplexer_156_out0);
  Demultiplexer #(.enable("false")) demultiplexer_172 (
    .out0(demultiplexer_172_out0), .out1(demultiplexer_172_out1), .in(or_157_out), .sel(or_161_out));
  or or_157 (or_157_out, demultiplexer_156_out1, demultiplexer_157_out0);
  or or_158 (or_158_out, demultiplexer_157_out1, demultiplexer_158_out0);
  Demultiplexer #(.enable("false")) demultiplexer_173 (
    .out0(demultiplexer_173_out0), .out1(demultiplexer_173_out1), .in(or_158_out), .sel(or_161_out));
  or or_159 (or_159_out, demultiplexer_158_out1, demultiplexer_159_out0);
  Demultiplexer #(.enable("false")) demultiplexer_174 (
    .out0(demultiplexer_174_out0), .out1(demultiplexer_174_out1), .in(or_159_out), .sel(or_161_out));
  Demultiplexer #(.enable("false")) demultiplexer_175 (
    .out0(demultiplexer_175_out0), .out1(demultiplexer_175_out1), .in(or_160_out), .sel(or_161_out));
  or or_160 (or_160_out, demultiplexer_159_out1, demultiplexer_160_out0);
  Demultiplexer #(.enable("false")) demultiplexer_176 (
    .out0(demultiplexer_176_out0), .out1(demultiplexer_176_out1), .in(demultiplexer_160_out1),
    .sel(or_161_out));
  or or_161 (or_161_out, decoder_1_out11, or_177_out);
  or or_162 (or_162_out, demultiplexer_161_out1, demultiplexer_162_out0);
  Demultiplexer #(.enable("false")) demultiplexer_177 (
    .out0(out_4[11]), .out1(demultiplexer_177_out1), .in(or_162_out), .sel(or_177_out));
  Demultiplexer #(.enable("false")) demultiplexer_178 (
    .out0(demultiplexer_178_out0), .out1(demultiplexer_178_out1), .in(or_163_out), .sel(or_177_out));
  or or_163 (or_163_out, demultiplexer_162_out1, demultiplexer_163_out0);
  Demultiplexer #(.enable("false")) demultiplexer_179 (
    .out0(demultiplexer_179_out0), .out1(demultiplexer_179_out1), .in(or_164_out), .sel(or_177_out));
  or or_164 (or_164_out, demultiplexer_163_out1, demultiplexer_164_out0);
  or or_165 (or_165_out, demultiplexer_164_out1, demultiplexer_165_out0);
  Demultiplexer #(.enable("false")) demultiplexer_180 (
    .out0(demultiplexer_180_out0), .out1(demultiplexer_180_out1), .in(or_165_out), .sel(or_177_out));
  or or_166 (or_166_out, demultiplexer_165_out1, demultiplexer_166_out0);
  Demultiplexer #(.enable("false")) demultiplexer_181 (
    .out0(demultiplexer_181_out0), .out1(demultiplexer_181_out1), .in(or_166_out), .sel(or_177_out));
  Demultiplexer #(.enable("false")) demultiplexer_182 (
    .out0(demultiplexer_182_out0), .out1(demultiplexer_182_out1), .in(or_167_out), .sel(or_177_out));
  or or_167 (or_167_out, demultiplexer_166_out1, demultiplexer_167_out0);
  or or_168 (or_168_out, demultiplexer_167_out1, demultiplexer_168_out0);
  Demultiplexer #(.enable("false")) demultiplexer_183 (
    .out0(demultiplexer_183_out0), .out1(demultiplexer_183_out1), .in(or_168_out), .sel(or_177_out));
  Demultiplexer #(.enable("false")) demultiplexer_184 (
    .out0(demultiplexer_184_out0), .out1(demultiplexer_184_out1), .in(or_169_out), .sel(or_177_out));
  or or_169 (or_169_out, demultiplexer_168_out1, demultiplexer_169_out0);
  Demultiplexer #(.enable("false")) demultiplexer_185 (
    .out0(demultiplexer_185_out0), .out1(demultiplexer_185_out1), .in(or_170_out), .sel(or_177_out));
  or or_170 (or_170_out, demultiplexer_169_out1, demultiplexer_170_out0);
  or or_171 (or_171_out, demultiplexer_170_out1, demultiplexer_171_out0);
  Demultiplexer #(.enable("false")) demultiplexer_186 (
    .out0(demultiplexer_186_out0), .out1(demultiplexer_186_out1), .in(or_171_out), .sel(or_177_out));
  Demultiplexer #(.enable("false")) demultiplexer_187 (
    .out0(demultiplexer_187_out0), .out1(demultiplexer_187_out1), .in(or_172_out), .sel(or_177_out));
  or or_172 (or_172_out, demultiplexer_171_out1, demultiplexer_172_out0);
  or or_173 (or_173_out, demultiplexer_172_out1, demultiplexer_173_out0);
  Demultiplexer #(.enable("false")) demultiplexer_188 (
    .out0(demultiplexer_188_out0), .out1(demultiplexer_188_out1), .in(or_173_out), .sel(or_177_out));
  or or_174 (or_174_out, demultiplexer_173_out1, demultiplexer_174_out0);
  Demultiplexer #(.enable("false")) demultiplexer_189 (
    .out0(demultiplexer_189_out0), .out1(demultiplexer_189_out1), .in(or_174_out), .sel(or_177_out));
  or or_175 (or_175_out, demultiplexer_174_out1, demultiplexer_175_out0);
  Demultiplexer #(.enable("false")) demultiplexer_190 (
    .out0(demultiplexer_190_out0), .out1(demultiplexer_190_out1), .in(or_175_out), .sel(or_177_out));
  or or_176 (or_176_out, demultiplexer_175_out1, demultiplexer_176_out0);
  Demultiplexer #(.enable("false")) demultiplexer_191 (
    .out0(demultiplexer_191_out0), .out1(demultiplexer_191_out1), .in(or_176_out), .sel(or_177_out));
  Demultiplexer #(.enable("false")) demultiplexer_192 (
    .out0(demultiplexer_192_out0), .out1(demultiplexer_192_out1), .in(demultiplexer_176_out1),
    .sel(or_177_out));
  or or_177 (or_177_out, decoder_1_out12, or_193_out);
  Demultiplexer #(.enable("false")) demultiplexer_193 (
    .out0(out_4[12]), .out1(demultiplexer_193_out1), .in(or_178_out), .sel(or_193_out));
  or or_178 (or_178_out, demultiplexer_177_out1, demultiplexer_178_out0);
  Demultiplexer #(.enable("false")) demultiplexer_194 (
    .out0(demultiplexer_194_out0), .out1(demultiplexer_194_out1), .in(or_179_out), .sel(or_193_out));
  or or_179 (or_179_out, demultiplexer_178_out1, demultiplexer_179_out0);
  Demultiplexer #(.enable("false")) demultiplexer_195 (
    .out0(demultiplexer_195_out0), .out1(demultiplexer_195_out1), .in(or_180_out), .sel(or_193_out));
  or or_180 (or_180_out, demultiplexer_179_out1, demultiplexer_180_out0);
  or or_181 (or_181_out, demultiplexer_180_out1, demultiplexer_181_out0);
  Demultiplexer #(.enable("false")) demultiplexer_196 (
    .out0(demultiplexer_196_out0), .out1(demultiplexer_196_out1), .in(or_181_out), .sel(or_193_out));
  Demultiplexer #(.enable("false")) demultiplexer_197 (
    .out0(demultiplexer_197_out0), .out1(demultiplexer_197_out1), .in(or_182_out), .sel(or_193_out));
  or or_182 (or_182_out, demultiplexer_181_out1, demultiplexer_182_out0);
  or or_183 (or_183_out, demultiplexer_182_out1, demultiplexer_183_out0);
  Demultiplexer #(.enable("false")) demultiplexer_198 (
    .out0(demultiplexer_198_out0), .out1(demultiplexer_198_out1), .in(or_183_out), .sel(or_193_out));
  Demultiplexer #(.enable("false")) demultiplexer_199 (
    .out0(demultiplexer_199_out0), .out1(demultiplexer_199_out1), .in(or_184_out), .sel(or_193_out));
  or or_184 (or_184_out, demultiplexer_183_out1, demultiplexer_184_out0);
  Demultiplexer #(.enable("false")) demultiplexer_200 (
    .out0(demultiplexer_200_out0), .out1(demultiplexer_200_out1), .in(or_185_out), .sel(or_193_out));
  or or_185 (or_185_out, demultiplexer_184_out1, demultiplexer_185_out0);
  or or_186 (or_186_out, demultiplexer_185_out1, demultiplexer_186_out0);
  Demultiplexer #(.enable("false")) demultiplexer_201 (
    .out0(demultiplexer_201_out0), .out1(demultiplexer_201_out1), .in(or_186_out), .sel(or_193_out));
  or or_187 (or_187_out, demultiplexer_186_out1, demultiplexer_187_out0);
  Demultiplexer #(.enable("false")) demultiplexer_202 (
    .out0(demultiplexer_202_out0), .out1(demultiplexer_202_out1), .in(or_187_out), .sel(or_193_out));
  or or_188 (or_188_out, demultiplexer_187_out1, demultiplexer_188_out0);
  Demultiplexer #(.enable("false")) demultiplexer_203 (
    .out0(demultiplexer_203_out0), .out1(demultiplexer_203_out1), .in(or_188_out), .sel(or_193_out));
  Demultiplexer #(.enable("false")) demultiplexer_204 (
    .out0(demultiplexer_204_out0), .out1(demultiplexer_204_out1), .in(or_189_out), .sel(or_193_out));
  or or_189 (or_189_out, demultiplexer_188_out1, demultiplexer_189_out0);
  or or_190 (or_190_out, demultiplexer_189_out1, demultiplexer_190_out0);
  Demultiplexer #(.enable("false")) demultiplexer_205 (
    .out0(demultiplexer_205_out0), .out1(demultiplexer_205_out1), .in(or_190_out), .sel(or_193_out));
  or or_191 (or_191_out, demultiplexer_190_out1, demultiplexer_191_out0);
  Demultiplexer #(.enable("false")) demultiplexer_206 (
    .out0(demultiplexer_206_out0), .out1(demultiplexer_206_out1), .in(or_191_out), .sel(or_193_out));
  or or_192 (or_192_out, demultiplexer_191_out1, demultiplexer_192_out0);
  Demultiplexer #(.enable("false")) demultiplexer_207 (
    .out0(demultiplexer_207_out0), .out1(demultiplexer_207_out1), .in(or_192_out), .sel(or_193_out));
  Demultiplexer #(.enable("false")) demultiplexer_208 (
    .out0(demultiplexer_208_out0), .out1(demultiplexer_208_out1), .in(demultiplexer_192_out1),
    .sel(or_193_out));
  or or_193 (or_193_out, decoder_1_out13, or_209_out);
  or or_194 (or_194_out, demultiplexer_193_out1, demultiplexer_194_out0);
  or or_195 (or_195_out, demultiplexer_194_out1, demultiplexer_195_out0);
  or or_196 (or_196_out, demultiplexer_195_out1, demultiplexer_196_out0);
  or or_197 (or_197_out, demultiplexer_196_out1, demultiplexer_197_out0);
  or or_198 (or_198_out, demultiplexer_197_out1, demultiplexer_198_out0);
  or or_199 (or_199_out, demultiplexer_198_out1, demultiplexer_199_out0);
  or or_200 (or_200_out, demultiplexer_199_out1, demultiplexer_200_out0);
  or or_201 (or_201_out, demultiplexer_200_out1, demultiplexer_201_out0);
  or or_202 (or_202_out, demultiplexer_201_out1, demultiplexer_202_out0);
  or or_203 (or_203_out, demultiplexer_202_out1, demultiplexer_203_out0);
  or or_204 (or_204_out, demultiplexer_203_out1, demultiplexer_204_out0);
  or or_205 (or_205_out, demultiplexer_204_out1, demultiplexer_205_out0);
  or or_206 (or_206_out, demultiplexer_205_out1, demultiplexer_206_out0);
  or or_207 (or_207_out, demultiplexer_206_out1, demultiplexer_207_out0);
  or or_208 (or_208_out, demultiplexer_207_out1, demultiplexer_208_out0);
  or or_209 (or_209_out, decoder_1_out14, decoder_1_out15);
  Demultiplexer #(.enable("false")) demultiplexer_209 (
    .out0(out_4[13]), .out1(demultiplexer_209_out1), .in(or_194_out), .sel(or_209_out));
  Demultiplexer #(.enable("false")) demultiplexer_210 (
    .out0(demultiplexer_210_out0), .out1(demultiplexer_210_out1), .in(or_195_out), .sel(or_209_out));
  Demultiplexer #(.enable("false")) demultiplexer_211 (
    .out0(demultiplexer_211_out0), .out1(demultiplexer_211_out1), .in(or_196_out), .sel(or_209_out));
  Demultiplexer #(.enable("false")) demultiplexer_212 (
    .out0(demultiplexer_212_out0), .out1(demultiplexer_212_out1), .in(or_197_out), .sel(or_209_out));
  Demultiplexer #(.enable("false")) demultiplexer_213 (
    .out0(demultiplexer_213_out0), .out1(demultiplexer_213_out1), .in(or_198_out), .sel(or_209_out));
  Demultiplexer #(.enable("false")) demultiplexer_214 (
    .out0(demultiplexer_214_out0), .out1(demultiplexer_214_out1), .in(or_199_out), .sel(or_209_out));
  Demultiplexer #(.enable("false")) demultiplexer_215 (
    .out0(demultiplexer_215_out0), .out1(demultiplexer_215_out1), .in(or_200_out), .sel(or_209_out));
  Demultiplexer #(.enable("false")) demultiplexer_216 (
    .out0(demultiplexer_216_out0), .out1(demultiplexer_216_out1), .in(or_201_out), .sel(or_209_out));
  Demultiplexer #(.enable("false")) demultiplexer_217 (
    .out0(demultiplexer_217_out0), .out1(demultiplexer_217_out1), .in(or_202_out), .sel(or_209_out));
  Demultiplexer #(.enable("false")) demultiplexer_218 (
    .out0(demultiplexer_218_out0), .out1(demultiplexer_218_out1), .in(or_203_out), .sel(or_209_out));
  Demultiplexer #(.enable("false")) demultiplexer_219 (
    .out0(demultiplexer_219_out0), .out1(demultiplexer_219_out1), .in(or_204_out), .sel(or_209_out));
  Demultiplexer #(.enable("false")) demultiplexer_220 (
    .out0(demultiplexer_220_out0), .out1(demultiplexer_220_out1), .in(or_205_out), .sel(or_209_out));
  Demultiplexer #(.enable("false")) demultiplexer_221 (
    .out0(demultiplexer_221_out0), .out1(demultiplexer_221_out1), .in(or_206_out), .sel(or_209_out));
  Demultiplexer #(.enable("false")) demultiplexer_222 (
    .out0(demultiplexer_222_out0), .out1(demultiplexer_222_out1), .in(or_207_out), .sel(or_209_out));
  Demultiplexer #(.enable("false")) demultiplexer_223 (
    .out0(demultiplexer_223_out0), .out1(demultiplexer_223_out1), .in(or_208_out), .sel(or_209_out));
  Demultiplexer #(.enable("false")) demultiplexer_224 (
    .out0(demultiplexer_224_out0), .out1(demultiplexer_224_out1), .in(demultiplexer_208_out1),
    .sel(or_209_out));
  or or_210 (or_210_out, demultiplexer_209_out1, demultiplexer_210_out0);
  Demultiplexer #(.enable("false")) demultiplexer_225 (
    .out0(out_4[14]), .out1(demultiplexer_225_out1), .in(or_210_out), .sel(decoder_1_out15));
  Demultiplexer #(.enable("false")) demultiplexer_226 (
    .out0(demultiplexer_226_out0), .out1(demultiplexer_226_out1), .in(or_211_out), .sel(decoder_1_out15));
  or or_211 (or_211_out, demultiplexer_210_out1, demultiplexer_211_out0);
  or or_212 (or_212_out, demultiplexer_211_out1, demultiplexer_212_out0);
  Demultiplexer #(.enable("false")) demultiplexer_227 (
    .out0(demultiplexer_227_out0), .out1(demultiplexer_227_out1), .in(or_212_out), .sel(decoder_1_out15));
  or or_213 (or_213_out, demultiplexer_212_out1, demultiplexer_213_out0);
  Demultiplexer #(.enable("false")) demultiplexer_228 (
    .out0(demultiplexer_228_out0), .out1(demultiplexer_228_out1), .in(or_213_out), .sel(decoder_1_out15));
  Demultiplexer #(.enable("false")) demultiplexer_229 (
    .out0(demultiplexer_229_out0), .out1(demultiplexer_229_out1), .in(or_214_out), .sel(decoder_1_out15));
  or or_214 (or_214_out, demultiplexer_213_out1, demultiplexer_214_out0);
  or or_215 (or_215_out, demultiplexer_214_out1, demultiplexer_215_out0);
  Demultiplexer #(.enable("false")) demultiplexer_230 (
    .out0(demultiplexer_230_out0), .out1(demultiplexer_230_out1), .in(or_215_out), .sel(decoder_1_out15));
  or or_216 (or_216_out, demultiplexer_215_out1, demultiplexer_216_out0);
  Demultiplexer #(.enable("false")) demultiplexer_231 (
    .out0(demultiplexer_231_out0), .out1(demultiplexer_231_out1), .in(or_216_out), .sel(decoder_1_out15));
  or or_217 (or_217_out, demultiplexer_216_out1, demultiplexer_217_out0);
  Demultiplexer #(.enable("false")) demultiplexer_232 (
    .out0(demultiplexer_232_out0), .out1(demultiplexer_232_out1), .in(or_217_out), .sel(decoder_1_out15));
  or or_218 (or_218_out, demultiplexer_217_out1, demultiplexer_218_out0);
  Demultiplexer #(.enable("false")) demultiplexer_233 (
    .out0(demultiplexer_233_out0), .out1(demultiplexer_233_out1), .in(or_218_out), .sel(decoder_1_out15));
  Demultiplexer #(.enable("false")) demultiplexer_234 (
    .out0(demultiplexer_234_out0), .out1(demultiplexer_234_out1), .in(or_219_out), .sel(decoder_1_out15));
  or or_219 (or_219_out, demultiplexer_218_out1, demultiplexer_219_out0);
  Demultiplexer #(.enable("false")) demultiplexer_235 (
    .out0(demultiplexer_235_out0), .out1(demultiplexer_235_out1), .in(or_220_out), .sel(decoder_1_out15));
  or or_220 (or_220_out, demultiplexer_219_out1, demultiplexer_220_out0);
  or or_221 (or_221_out, demultiplexer_220_out1, demultiplexer_221_out0);
  Demultiplexer #(.enable("false")) demultiplexer_236 (
    .out0(demultiplexer_236_out0), .out1(demultiplexer_236_out1), .in(or_221_out), .sel(decoder_1_out15));
  Demultiplexer #(.enable("false")) demultiplexer_237 (
    .out0(demultiplexer_237_out0), .out1(demultiplexer_237_out1), .in(or_222_out), .sel(decoder_1_out15));
  or or_222 (or_222_out, demultiplexer_221_out1, demultiplexer_222_out0);
  or or_223 (or_223_out, demultiplexer_222_out1, demultiplexer_223_out0);
  Demultiplexer #(.enable("false")) demultiplexer_238 (
    .out0(demultiplexer_238_out0), .out1(demultiplexer_238_out1), .in(or_223_out), .sel(decoder_1_out15));
  or or_224 (or_224_out, demultiplexer_223_out1, demultiplexer_224_out0);
  Demultiplexer #(.enable("false")) demultiplexer_239 (
    .out0(demultiplexer_239_out0), .out1(demultiplexer_239_out1), .in(or_224_out), .sel(decoder_1_out15));
  Demultiplexer #(.enable("false")) demultiplexer_240 (
    .out0(demultiplexer_240_out0), .out1(out_5[14]), .in(demultiplexer_224_out1), .sel(decoder_1_out15));
  or or_225 (out_4[15], demultiplexer_225_out1, demultiplexer_226_out0);
  or or_226 (out_5[0], demultiplexer_226_out1, demultiplexer_227_out0);
  or or_227 (out_5[1], demultiplexer_227_out1, demultiplexer_228_out0);
  or or_228 (out_5[2], demultiplexer_228_out1, demultiplexer_229_out0);
  or or_229 (out_5[3], demultiplexer_229_out1, demultiplexer_230_out0);
  or or_230 (out_5[4], demultiplexer_230_out1, demultiplexer_231_out0);
  or or_231 (out_5[5], demultiplexer_231_out1, demultiplexer_232_out0);
  or or_232 (out_5[6], demultiplexer_232_out1, demultiplexer_233_out0);
  or or_233 (out_5[7], demultiplexer_233_out1, demultiplexer_234_out0);
  or or_234 (out_5[8], demultiplexer_234_out1, demultiplexer_235_out0);
  or or_235 (out_5[9], demultiplexer_235_out1, demultiplexer_236_out0);
  or or_236 (out_5[10], demultiplexer_236_out1, demultiplexer_237_out0);
  or or_237 (out_5[11], demultiplexer_237_out1, demultiplexer_238_out0);
  or or_238 (out_5[12], demultiplexer_238_out1, demultiplexer_239_out0);
  or or_239 (out_5[13], demultiplexer_239_out1, demultiplexer_240_out0);

  assign out_5[15] = 1'b0;
endmodule

module _32_bit_Lshifter (
  input  [31:0] in_1,
  input  in_2,
  input  [4:0] in_3,
  output [31:0] out_4,
  output [31:0] out_5
);

  wire [15:0] demultiplexer_1_out0, demultiplexer_1_out1, demultiplexer_2_out0, demultiplexer_2_out1,
       n16bit_lshifter_1_out_5, n16bit_lshifter_2_out_4, n16bit_lshifter_2_out_5, n16bit_lshifter_3_out_4,
       or_1_out;

  Demultiplexer #(.width(16)) demultiplexer_1 (
    .out0(demultiplexer_1_out0), .out1(demultiplexer_1_out1), .in(in_1[15:0]), .sel(in_3[4]), .en(in_2));
  Demultiplexer #(.width(16)) demultiplexer_2 (
    .out0(demultiplexer_2_out0), .out1(demultiplexer_2_out1), .in(in_1[31:16]), .sel(in_3[4]), .en(in_2));
  Pull_Resistor pull_resistor_1 (.node(demultiplexer_1_out0));
  Pull_Resistor pull_resistor_2 (.node(demultiplexer_1_out1));
  assign or_1_out = demultiplexer_1_out1 | demultiplexer_2_out0;  // OR_Gate or_1, 16 bits wide
  Pull_Resistor pull_resistor_3 (.node(demultiplexer_2_out0));
  Pull_Resistor pull_resistor_4 (.node(demultiplexer_2_out1));
  _16bit_Lshifter u_16bit_lshifter_1 (
    .out_4(out_4[15:0]), .out_5(n16bit_lshifter_1_out_5), .in_1(demultiplexer_1_out0), .in_2(in_3[3:0]),
    .in_3(in_2));
  _16bit_Lshifter u_16bit_lshifter_2 (
    .out_4(n16bit_lshifter_2_out_4), .out_5(n16bit_lshifter_2_out_5), .in_1(or_1_out), .in_2(in_3[3:0]),
    .in_3(in_2));
  _16bit_Lshifter u_16bit_lshifter_3 (
    .out_4(n16bit_lshifter_3_out_4), .out_5(out_5[31:16]), .in_1(demultiplexer_2_out1), .in_2(in_3[3:0]),
    .in_3(in_2));
  assign out_4[31:16] = n16bit_lshifter_1_out_5 | n16bit_lshifter_2_out_4;  // OR_Gate or_2, 16 bits wide
  assign out_5[15:0] = n16bit_lshifter_2_out_5 | n16bit_lshifter_3_out_4;  // OR_Gate or_3, 16 bits wide
endmodule

module Float_Arithmetic (
  input  [31:0] in_1,
  input  in_2,
  input  in_3,
  input  in_4,
  input  in_5,
  input  in_6,
  input  in_7,
  input  [31:0] in_8,
  input  [31:0] in_9,
  input  in_10
);

  wire and_1_out, and_2_out, and_3_out, and_4_out, and_5_out, and_6_out, and_7_out, and_8_out, and_9_out,
       and_10_out, and_11_out, bitfinder_1_found, bitfinder_2_found, bitfinder_3_found, bitfinder_5_found,
       comparator_1_eq, comparator_1_gt, comparator_1_lt, comparator_2_eq, comparator_2_gt, comparator_2_lt,
       comparator_3_eq, comparator_3_lt, comparator_4_lt, controlled_buffer_4_out, controlled_buffer_5_out,
       controlled_buffer_6_out, controlled_buffer_10_out, multiplexer_26_out, multiplexer_27_out,
       multiplexer_29_out, multiplexer_30_out, not_1_out, not_3_out, not_4_out, not_5_out, not_6_out,
       not_7_out, not_8_out, or_1_out, or_2_out, or_3_out, or_4_out, or_5_out, pull_resistor_4_node,
       subtractor_1_bout, subtractor_3_bout, subtractor_4_bout, subtractor_5_bout, subtractor_8_bout,
       subtractor_9_bout, xnor_1_out, xor_2_out, xor_3_out;
  wire [4:0] bit_extender_2_out, bit_extender_12_out, bit_extender_13_out, bitfinder_1_index,
       bitfinder_2_index, bitfinder_3_index, bitfinder_7_index, multiplexer_4_out, multiplexer_6_out,
       multiplexer_7_out, multiplexer_9_out, multiplexer_12_out, multiplexer_28_out, negator_4_out,
       negator_5_out, negator_6_out, negator_7_out, negator_10_out, subtractor_1_out, subtractor_3_out,
       subtractor_4_out, subtractor_5_out, subtractor_9_out, subtractor_11_out;
  wire [7:0] adder_1_out, adder_2_out, adder_3_out, adder_4_out, adder_5_out, adder_6_out,
       bit_extender_1_out, bit_extender_3_out, bit_extender_4_out, bit_extender_14_out,
       controlled_buffer_8_out, controlled_buffer_9_out, multiplexer_5_out, multiplexer_13_out,
       multiplexer_14_out, multiplexer_15_out, multiplexer_16_out, multiplexer_22_out, multiplexer_25_out,
       negator_9_out, pull_resistor_1_node_2, subtractor_2_out, subtractor_6_out, subtractor_7_out,
       subtractor_8_out;
  wire [22:0] bit_extender_5_out, bit_extender_7_out, bit_extender_8_out, bit_extender_15_out,
       controlled_buffer_8_out_3, controlled_buffer_9_out_3, pull_resistor_1_node;
  wire [23:0] divider_1_out, multiplexer_18_out, multiplier_1_cout, multiplier_1_out, shifter_9_out,
       shifter_10_out;
  wire [23:23] bitfinder_4_found, bitfinder_6_found;
  wire [30:0] adder_7_out, bit_extender_10_out, bit_extender_11_out, multiplexer_23_out, multiplexer_24_out,
       multiplexer_31_out, multiplexer_32_out, multiplexer_33_out, shifter_11_out, shifter_14_out,
       subtractor_10_out;
  wire [31:0] bit_extender_6_out, bit_extender_16_out, multiplexer_1_out, multiplexer_2_out,
       multiplexer_3_out, multiplexer_8_out, multiplexer_10_out, multiplexer_11_out, multiplexer_17_out,
       multiplexer_19_out, multiplexer_20_out, multiplexer_21_out, multiplexer_34_out, multiplexer_35_out,
       negator_1_out, negator_2_out, negator_3_out, negator_8_out, negator_11_out, pull_resistor_11_node,
       shifter_1_out, shifter_2_out, shifter_3_out, shifter_4_out, shifter_5_out, shifter_6_out,
       shifter_7_out, shifter_8_out, shifter_12_out, shifter_13_out;
  wire [31:31] controlled_buffer_1_out, controlled_buffer_2_out, controlled_buffer_8_out_2,
       controlled_buffer_9_out_2, not_2_out, or_6_out, pull_resistor_1_node_3, undriven;

  BitFinder #(.width(32), .\type ("high1")) bitfinder_1 (
    .in(multiplexer_1_out), .index(bitfinder_1_index), .found(bitfinder_1_found));
  Negator #(.width(32)) negator_1 (.in(in_1), .out(negator_1_out));
  Pull_Resistor pull_resistor_1 (.node({pull_resistor_1_node_3[31], pull_resistor_1_node_2, pull_resistor_1_node}));
  BitFinder #(.width(32), .\type ("high1")) bitfinder_2 (
    .in(multiplexer_2_out), .index(bitfinder_2_index), .found(bitfinder_2_found));
  Negator #(.width(32)) negator_2 (.in(in_8), .out(negator_2_out));
  BitFinder #(.width(32), .\type ("high1")) bitfinder_3 (
    .in(multiplexer_3_out), .index(bitfinder_3_index), .found(bitfinder_3_found));
  Negator #(.width(32)) negator_3 (.in(in_9), .out(negator_3_out));
  Subtractor #(.width(5)) subtractor_1 (
    .a(5'b10111), .b(bitfinder_1_index), .out(subtractor_1_out), .bout(subtractor_1_bout));  // open: bin
  Multiplexer #(.width(32), .disabled(0), .enable("false")) multiplexer_1 (
    .in0(in_1), .in1(negator_1_out), .out(multiplexer_1_out), .sel(in_1[31]));
  Subtractor subtractor_2 (.a(pull_resistor_1_node_2), .b(8'h7f), .out(subtractor_2_out));  // open: bin, bout
  Subtractor #(.width(5)) subtractor_3 (
    .a(5'b10111), .b(bitfinder_2_index), .out(subtractor_3_out), .bout(subtractor_3_bout));  // open: bin
  Multiplexer #(.width(32), .disabled(0), .enable("false")) multiplexer_2 (
    .in0(in_8), .in1(negator_2_out), .out(multiplexer_2_out), .sel(controlled_buffer_1_out[31]));
  assign controlled_buffer_1_out[31] = in_2 ? in_8[31] : 1'bz;  // Controlled_Buffer controlled_buffer_1
  Pull_Resistor pull_resistor_2 (.node(controlled_buffer_1_out[31]));
  Subtractor #(.width(5)) subtractor_4 (
    .a(5'b10111), .b(bitfinder_3_index), .out(subtractor_4_out), .bout(subtractor_4_bout));  // open: bin
  Multiplexer #(.width(32), .disabled(0), .enable("false")) multiplexer_3 (
    .in0(in_9), .in1(negator_3_out), .out(multiplexer_3_out), .sel(controlled_buffer_2_out[31]));
  assign controlled_buffer_2_out[31] = in_6 ? in_9[31] : 1'bz;  // Controlled_Buffer controlled_buffer_2
  Pull_Resistor pull_resistor_3 (.node(controlled_buffer_2_out[31]));
  Multiplexer #(.width(5), .disabled(0), .enable("false")) multiplexer_4 (
    .in0(subtractor_1_out), .in1(negator_4_out), .out(multiplexer_4_out), .sel(pull_resistor_4_node));
  Negator #(.width(5)) negator_4 (.in(subtractor_1_out), .out(negator_4_out));
  Pull_Resistor pull_resistor_4 (.node(pull_resistor_4_node));
  assign pull_resistor_4_node = bitfinder_1_found ? subtractor_1_bout : 1'bz;  // Controlled_Buffer controlled_buffer_3
  not not_1 (not_1_out, pull_resistor_4_node);
  assign bit_extender_1_out = {{3{1'b0}}, bitfinder_1_index};  // Bit_Extender bit_extender_1
  Bit_Extender #(.out_width(5)) bit_extender_2 (.in(subtractor_2_out), .out(bit_extender_2_out));
  Negator #(.width(5)) negator_5 (.in(subtractor_3_out), .out(negator_5_out));
  assign controlled_buffer_4_out = bitfinder_2_found ? subtractor_3_bout : 1'bz;  // Controlled_Buffer controlled_buffer_4
  Pull_Resistor pull_resistor_5 (.node(controlled_buffer_4_out));
  Negator #(.width(5)) negator_6 (.in(subtractor_4_out), .out(negator_6_out));
  assign controlled_buffer_5_out = bitfinder_3_found ? subtractor_4_bout : 1'bz;  // Controlled_Buffer controlled_buffer_5
  Pull_Resistor pull_resistor_6 (.node(controlled_buffer_5_out));
  not not_2 (not_2_out[31], undriven[31]);
  Multiplexer #(.width(8), .enable("false")) multiplexer_5 (
    .in0(8'h1), .in1({8{1'b1}}), .out(multiplexer_5_out), .sel(in_10));
  Shifter #(.width(32), .shift("lr")) shifter_1 (
    .in(multiplexer_1_out), .\dist (multiplexer_4_out), .out(shifter_1_out));
  Shifter #(.width(32)) shifter_2 (.in(multiplexer_1_out), .\dist (multiplexer_4_out), .out(shifter_2_out));
  Adder adder_1 (.a(8'h7f), .b(bit_extender_1_out), .out(adder_1_out));  // open: cin, cout
  Subtractor #(.width(5)) subtractor_5 (
    .a(5'b10111), .b(bit_extender_2_out), .out(subtractor_5_out), .bout(subtractor_5_bout));  // open: bin
  Negator #(.width(5)) negator_7 (.in(subtractor_5_out), .out(negator_7_out));
  assign controlled_buffer_6_out = bitfinder_4_found[23] ? subtractor_5_bout : 1'bz;  // Controlled_Buffer controlled_buffer_6
  BitFinder #(.width(32), .\type ("high1")) bitfinder_4 (
    .in({pull_resistor_1_node_3[31], pull_resistor_1_node_2, pull_resistor_1_node}),
    .found(bitfinder_4_found[23]));  // open: index
  Shifter #(.width(32), .shift("lr")) shifter_3 (
    .in(multiplexer_2_out), .\dist (multiplexer_6_out), .out(shifter_3_out));
  Multiplexer #(.width(5), .disabled(0), .enable("false")) multiplexer_6 (
    .in0(subtractor_3_out), .in1(negator_5_out), .out(multiplexer_6_out), .sel(controlled_buffer_4_out));
  Shifter #(.width(32)) shifter_4 (.in(multiplexer_2_out), .\dist (multiplexer_6_out), .out(shifter_4_out));
  not not_3 (not_3_out, controlled_buffer_4_out);
  Adder adder_2 (.a(8'h7f), .b(bit_extender_3_out), .out(adder_2_out));  // open: cin, cout
  assign bit_extender_3_out = {{3{1'b0}}, bitfinder_2_index};  // Bit_Extender bit_extender_3
  Shifter #(.width(32), .shift("lr")) shifter_5 (
    .in(multiplexer_3_out), .\dist (multiplexer_7_out), .out(shifter_5_out));
  Multiplexer #(.width(5), .disabled(0), .enable("false")) multiplexer_7 (
    .in0(subtractor_4_out), .in1(negator_6_out), .out(multiplexer_7_out), .sel(controlled_buffer_5_out));
  Shifter #(.width(32)) shifter_6 (.in(multiplexer_3_out), .\dist (multiplexer_7_out), .out(shifter_6_out));
  not not_4 (not_4_out, controlled_buffer_5_out);
  Adder adder_3 (.a(8'h7f), .b(bit_extender_4_out), .out(adder_3_out));  // open: cin, cout
  assign bit_extender_4_out = {{3{1'b0}}, bitfinder_3_index};  // Bit_Extender bit_extender_4
  Adder adder_4 (.a(controlled_buffer_8_out), .b(multiplexer_5_out), .out(adder_4_out));  // open: cin, cout
  Bit_Extender #(.in_width(32), .out_width(23)) bit_extender_5 (.in(multiplexer_8_out), .out(bit_extender_5_out));
  Multiplexer #(.width(32), .disabled(0), .enable("false")) multiplexer_8 (
    .in0(shifter_1_out), .in1(shifter_2_out), .out(multiplexer_8_out), .sel(not_1_out));
  Multiplexer #(.width(5), .disabled(0), .enable("false")) multiplexer_9 (
    .in0(subtractor_5_out), .in1(negator_7_out), .out(multiplexer_9_out), .sel(controlled_buffer_6_out));
  Multiplexer #(.width(32), .disabled(0), .enable("false")) multiplexer_10 (
    .in0(shifter_3_out), .in1(shifter_4_out), .out(multiplexer_10_out), .sel(not_3_out));
  Multiplexer #(.width(32), .disabled(0), .enable("false")) multiplexer_11 (
    .in0(shifter_5_out), .in1(shifter_6_out), .out(multiplexer_11_out), .sel(not_4_out));
  Multiplexer #(.width(5), .enable("false")) multiplexer_12 (
    .in0(5'b00001), .in1({5{1'b0}}), .out(multiplexer_12_out), .sel(multiplier_1_cout[23]));
  Multiplexer #(.width(8), .enable("false")) multiplexer_13 (
    .in0(controlled_buffer_8_out), .in1(subtractor_6_out), .out(multiplexer_13_out), .sel(in_7));
  Multiplexer #(.width(8), .enable("false")) multiplexer_14 (
    .in0(adder_5_out), .in1(controlled_buffer_8_out), .out(multiplexer_14_out), .sel(in_7));
  Pull_Resistor pull_resistor_7 (.node({pull_resistor_1_node_3[31], pull_resistor_1_node_2, pull_resistor_1_node}));
  assign {pull_resistor_1_node_3[31], pull_resistor_1_node_2, pull_resistor_1_node} = bitfinder_1_found ? {in_1[31], adder_1_out, bit_extender_5_out} : 32'bz;  // Controlled_Buffer controlled_buffer_7
  assign bit_extender_6_out = {{8{1'b0}}, {bitfinder_4_found[23], pull_resistor_1_node}};  // Bit_Extender bit_extender_6
  Pull_Resistor pull_resistor_8 (.node(controlled_buffer_6_out));
  Bit_Extender #(.in_width(32), .out_width(23)) bit_extender_7 (.in(multiplexer_10_out), .out(bit_extender_7_out));
  assign {controlled_buffer_8_out_2[31], controlled_buffer_8_out, controlled_buffer_8_out_3} = bitfinder_2_found ? {controlled_buffer_1_out[31], adder_2_out, bit_extender_7_out} : 32'bz;  // Controlled_Buffer controlled_buffer_8
  Bit_Extender #(.in_width(32), .out_width(23)) bit_extender_8 (.in(multiplexer_11_out), .out(bit_extender_8_out));
  assign {controlled_buffer_9_out_2[31], controlled_buffer_9_out, controlled_buffer_9_out_3} = bitfinder_3_found ? {controlled_buffer_2_out[31], adder_3_out, bit_extender_8_out} : 32'bz;  // Controlled_Buffer controlled_buffer_9
  xor xor_1 (multiplexer_19_out[31], controlled_buffer_8_out_2[31], controlled_buffer_9_out_2[31]);
  Divider #(.width(24)) divider_1 (
    .a({24{1'b0}}), .b({1'b1, controlled_buffer_9_out_3}), .out(divider_1_out),
    .upper({1'b1, controlled_buffer_8_out_3}));  // open: rem
  Multiplier #(.width(24)) multiplier_1 (
    .a({1'b1, controlled_buffer_8_out_3}), .b({1'b1, controlled_buffer_9_out_3}), .out(multiplier_1_out),
    .cout(multiplier_1_cout));  // open: cin
  not not_5 (not_5_out, in_7);
  Multiplexer #(.width(8), .enable("false")) multiplexer_15 (
    .in0(controlled_buffer_9_out), .in1(8'h7f), .out(multiplexer_15_out), .sel(in_7));
  Multiplexer #(.width(8), .enable("false")) multiplexer_16 (
    .in0(8'h7f), .in1(controlled_buffer_9_out), .out(multiplexer_16_out), .sel(in_7));
  // Probe on {pull_resistor_1_node_3[31], pull_resistor_1_node_2, pull_resistor_1_node}
  Shifter #(.width(32), .shift("lr")) shifter_7 (
    .in(bit_extender_6_out), .\dist (multiplexer_9_out), .out(shifter_7_out));
  Multiplexer #(.width(32), .disabled(0), .enable("false")) multiplexer_17 (
    .in0(shifter_7_out), .in1(shifter_8_out), .out(multiplexer_17_out), .sel(controlled_buffer_6_out));
  Shifter #(.width(32)) shifter_8 (.in(bit_extender_6_out), .\dist (multiplexer_9_out), .out(shifter_8_out));
  // Probe on {controlled_buffer_8_out_2[31], controlled_buffer_8_out, controlled_buffer_8_out_3}
  Pull_Resistor pull_resistor_9 (.node({controlled_buffer_8_out_2[31], controlled_buffer_8_out, controlled_buffer_8_out_3}));
  // Probe on {controlled_buffer_9_out_2[31], controlled_buffer_9_out, controlled_buffer_9_out_3}
  Pull_Resistor pull_resistor_10 (.node({controlled_buffer_9_out_2[31], controlled_buffer_9_out, controlled_buffer_9_out_3}));
  Shifter #(.width(24), .shift("lr")) shifter_9 (.in(divider_1_out), .\dist (5'b00001), .out(shifter_9_out));
  Shifter #(.width(24)) shifter_10 (.in(multiplier_1_cout), .\dist (multiplexer_12_out), .out(shifter_10_out));
  Multiplexer #(.width(24), .enable("false")) multiplexer_18 (
    .in0(shifter_9_out), .in1(shifter_10_out), .out(multiplexer_18_out), .sel(not_5_out));
  Adder adder_5 (
    .a(multiplexer_15_out), .b(multiplexer_13_out), .out(adder_5_out), .cin(multiplier_1_cout[23]));  // open: cout
  Multiplexer #(.width(8), .enable("false")) multiplexer_19 (
    .in0(adder_5_out), .in1(subtractor_6_out), .out(multiplexer_19_out[30:23]), .sel(not_5_out));
  Subtractor subtractor_6 (.a(multiplexer_14_out), .b(multiplexer_16_out), .out(subtractor_6_out));  // open: bin, bout
  Negator #(.width(32)) negator_8 (.in(multiplexer_17_out), .out(negator_8_out));
  Bit_Extender #(.in_width(24), .out_width(23)) bit_extender_9 (
    .in(multiplexer_18_out), .out(multiplexer_19_out[22:0]));
  Multiplexer #(.width(32), .disabled(0), .enable("false")) multiplexer_20 (
    .in0(multiplexer_17_out), .in1(negator_8_out), .out(multiplexer_20_out), .sel(pull_resistor_1_node_3[31]));
  // Probe on multiplexer_20_out
  Multiplexer #(.width(32), .enable("false")) multiplexer_21 (
    .in0({controlled_buffer_9_out_2[31], controlled_buffer_9_out, controlled_buffer_9_out_3}),
    .in1(32'h3f800000), .out(multiplexer_21_out), .sel(or_1_out));
  or or_1 (or_1_out, in_3, in_4);
  or or_2 (or_2_out, in_5, in_4);
  Pull_Resistor pull_resistor_11 (.node(pull_resistor_11_node));
  // Probe on multiplexer_35_out
  Comparator #(.width(23), .mode("unsigned")) comparator_1 (
    .a(controlled_buffer_8_out_3), .b(controlled_buffer_9_out_3), .gt(comparator_1_gt), .eq(comparator_1_eq),
    .lt(comparator_1_lt));
  Comparator comparator_2 (
    .a(controlled_buffer_8_out), .b(controlled_buffer_9_out), .gt(comparator_2_gt), .eq(comparator_2_eq),
    .lt(comparator_2_lt));
  and and_1 (and_1_out, xor_2_out, ~controlled_buffer_8_out_2[31], or_3_out);  // AND_Gate
  and and_2 (and_2_out, comparator_3_eq, not_6_out);
  xor xor_2 (xor_2_out, or_2_out, multiplexer_21_out[31]);
  Comparator #(.width(23)) comparator_3 (
    .a(controlled_buffer_8_out_3), .b(multiplexer_21_out[22:0]), .eq(comparator_3_eq), .lt(comparator_3_lt));  // open: gt
  BitFinder #(.\type ("high1")) bitfinder_5 (.in(subtractor_8_out), .found(bitfinder_5_found));  // open: index
  Multiplexer #(.width(8), .enable("false")) multiplexer_22 (
    .in0(controlled_buffer_8_out), .in1(multiplexer_21_out[30:23]), .out(multiplexer_22_out),
    .sel(subtractor_8_bout));
  Subtractor subtractor_7 (.a(multiplexer_19_out[30:23]), .b(8'h7f), .out(subtractor_7_out));  // open: bin, bout
  xnor xnor_1 (xnor_1_out, controlled_buffer_8_out_2[31], controlled_buffer_9_out_2[31]);
  and and_3 (and_3_out, comparator_1_gt, comparator_2_eq);
  and and_4 (and_4_out, comparator_1_lt, comparator_2_eq);
  and and_5 (and_5_out, controlled_buffer_9_out_2[31], ~controlled_buffer_8_out_2[31]);  // AND_Gate
  and and_6 (and_6_out, controlled_buffer_8_out_2[31], xor_2_out);
  and and_7 (and_7_out, controlled_buffer_8_out_2[31], ~xor_2_out, ~or_3_out);  // AND_Gate
  or or_3 (or_3_out, and_8_out, subtractor_8_bout);
  and and_8 (and_8_out, comparator_3_lt, not_6_out);
  assign bit_extender_10_out = {{7{1'b0}}, {1'b1, controlled_buffer_8_out_3}};  // Bit_Extender bit_extender_10
  not not_6 (not_6_out, bitfinder_5_found);
  assign bit_extender_11_out = {{7{1'b0}}, {1'b1, multiplexer_21_out[22:0]}};  // Bit_Extender bit_extender_11
  Subtractor subtractor_8 (
    .a(controlled_buffer_8_out), .b(multiplexer_21_out[30:23]), .out(subtractor_8_out),
    .bout(subtractor_8_bout));  // open: bin
  Negator negator_9 (.in(subtractor_8_out), .out(negator_9_out));
  Bit_Extender #(.out_width(5)) bit_extender_12 (.in(subtractor_7_out), .out(bit_extender_12_out));
  or or_4 (or_4_out, comparator_2_gt, and_3_out);
  not not_7 (not_7_out, xnor_1_out);
  and and_9 (and_9_out, comparator_1_eq, xnor_1_out, comparator_2_eq);
  or or_5 (or_5_out, and_4_out, comparator_2_lt);
  and and_10 (and_10_out, ~controlled_buffer_9_out_2[31], controlled_buffer_8_out_2[31]);  // AND_Gate
  or or_6 (or_6_out[31], and_1_out, and_7_out, and_6_out);
  xor xor_3 (xor_3_out, controlled_buffer_8_out_2[31], xor_2_out);
  Multiplexer #(.width(31), .enable("false")) multiplexer_23 (
    .in0(bit_extender_10_out), .in1(bit_extender_11_out), .out(multiplexer_23_out), .sel(subtractor_8_bout));
  Multiplexer #(.width(31), .enable("false")) multiplexer_24 (
    .in0(bit_extender_11_out), .in1(bit_extender_10_out), .out(multiplexer_24_out), .sel(subtractor_8_bout));
  Bit_Extender #(.out_width(5)) bit_extender_13 (.in(multiplexer_25_out), .out(bit_extender_13_out));
  Multiplexer #(.width(8), .enable("false")) multiplexer_25 (
    .in0(subtractor_8_out), .in1(negator_9_out), .out(multiplexer_25_out), .sel(subtractor_8_bout));
  Subtractor #(.width(5)) subtractor_9 (
    .a(5'b10111), .b(bit_extender_12_out), .out(subtractor_9_out), .bout(subtractor_9_bout));  // open: bin
  assign controlled_buffer_10_out = bitfinder_6_found[23] ? subtractor_9_bout : 1'bz;  // Controlled_Buffer controlled_buffer_10
  BitFinder #(.width(32), .\type ("high1")) bitfinder_6 (
    .in(multiplexer_19_out), .found(bitfinder_6_found[23]));  // open: index
  Multiplexer #(.enable("false")) multiplexer_26 (
    .in0(or_4_out), .in1(and_5_out), .out(multiplexer_26_out), .sel(not_7_out));
  Multiplexer #(.enable("false")) multiplexer_27 (
    .in0(or_5_out), .in1(and_10_out), .out(multiplexer_27_out), .sel(not_7_out));
  and and_11 (and_11_out, controlled_buffer_9_out_2[31], controlled_buffer_8_out_2[31]);
  not not_8 (not_8_out, xor_3_out);
  Comparator #(.width(31)) comparator_4 (
    .a(multiplexer_23_out), .b(shifter_11_out), .lt(comparator_4_lt));  // open: gt, eq
  Shifter #(.width(31), .shift("lr")) shifter_11 (
    .in(multiplexer_24_out), .\dist (bit_extender_13_out), .out(shifter_11_out));
  assign bit_extender_14_out = {{3{1'b0}}, subtractor_11_out};  // Bit_Extender bit_extender_14
  Multiplexer #(.width(5), .disabled(0), .enable("false")) multiplexer_28 (
    .in0(subtractor_9_out), .in1(negator_10_out), .out(multiplexer_28_out), .sel(controlled_buffer_10_out));
  Negator #(.width(5)) negator_10 (.in(subtractor_9_out), .out(negator_10_out));
  Multiplexer #(.enable("false")) multiplexer_29 (
    .in0(multiplexer_26_out), .in1(multiplexer_27_out), .out(multiplexer_29_out), .sel(and_11_out));
  Multiplexer #(.enable("false")) multiplexer_30 (
    .in0(multiplexer_27_out), .in1(multiplexer_26_out), .out(multiplexer_30_out), .sel(and_11_out));
  Multiplexer #(.width(31), .enable("false")) multiplexer_31 (
    .in0(multiplexer_23_out), .in1(shifter_11_out), .out(multiplexer_31_out), .sel(comparator_4_lt));
  Multiplexer #(.width(31), .enable("false")) multiplexer_32 (
    .in0(shifter_11_out), .in1(multiplexer_23_out), .out(multiplexer_32_out), .sel(comparator_4_lt));
  BitFinder #(.width(31), .\type ("high1")) bitfinder_7 (
    .in(multiplexer_33_out), .index(bitfinder_7_index));  // open: found
  Bit_Extender #(.in_width(31), .out_width(23)) bit_extender_15 (.in(shifter_14_out), .out(bit_extender_15_out));
  Adder adder_6 (.a(bit_extender_14_out), .b(multiplexer_22_out), .out(adder_6_out));  // open: cin, cout
  assign bit_extender_16_out = {{8{1'b0}}, {bitfinder_6_found[23], multiplexer_19_out[22:0]}};  // Bit_Extender bit_extender_16
  Subtractor #(.width(31)) subtractor_10 (
    .a(multiplexer_31_out), .b(multiplexer_32_out), .out(subtractor_10_out));  // open: bin, bout
  Adder #(.width(31)) adder_7 (.a(multiplexer_31_out), .b(multiplexer_32_out), .out(adder_7_out));  // open: cin, cout
  Subtractor #(.width(5)) subtractor_11 (
    .a(bitfinder_7_index), .b(5'b10111), .out(subtractor_11_out));  // open: bin, bout
  Shifter #(.width(32), .shift("lr")) shifter_12 (
    .in(bit_extender_16_out), .\dist (multiplexer_28_out), .out(shifter_12_out));
  Shifter #(.width(32)) shifter_13 (.in(bit_extender_16_out), .\dist (multiplexer_28_out), .out(shifter_13_out));
  Multiplexer #(.width(31), .enable("false")) multiplexer_33 (
    .in0(subtractor_10_out), .in1(adder_7_out), .out(multiplexer_33_out), .sel(not_8_out));
  Shifter #(.width(31), .shift("lr")) shifter_14 (
    .in(multiplexer_33_out), .\dist (subtractor_11_out), .out(shifter_14_out));
  assign pull_resistor_11_node = and_2_out ? {or_6_out[31], adder_6_out, bit_extender_15_out} : 32'bz;  // Controlled_Buffer controlled_buffer_11
  Multiplexer #(.width(32), .disabled(0), .enable("false")) multiplexer_34 (
    .in0(shifter_12_out), .in1(shifter_13_out), .out(multiplexer_34_out), .sel(controlled_buffer_10_out));
  Negator #(.width(32)) negator_11 (.in(multiplexer_34_out), .out(negator_11_out));
  // Probe on pull_resistor_11_node
  Multiplexer #(.width(32), .disabled(0), .enable("false")) multiplexer_35 (
    .in0(multiplexer_34_out), .in1(negator_11_out), .out(multiplexer_35_out), .sel(multiplexer_19_out[31]));
  // Probe on multiplexer_35_out
endmodule
module FPU (
  input  [31:0] in_1,
  input  [31:0] in_2,
  input  [5:0] in_3,
  output [31:0] out_4,
  output out_5,
  output out_6
);

  wire and_1_out, and_2_out, and_3_out, and_4_out, and_5_out, and_6_out, and_7_out, and_8_out, and_9_out,
       and_11_out, bitfinder_1_found, bitfinder_3_found, comparator_1_eq, comparator_1_lt, comparator_2_eq,
       comparator_2_gt, comparator_2_lt, comparator_3_eq, comparator_3_gt, comparator_3_lt, comparator_4_lt,
       controlled_buffer_4_out, decoder_1_out0, decoder_1_out1, decoder_1_out2, decoder_1_out3,
       decoder_1_out4, decoder_1_out5, decoder_1_out6, decoder_1_out7, decoder_1_out11, decoder_1_out12,
       decoder_1_out13, multiplexer_18_out, multiplexer_20_out, multiplexer_21_out, not_2_out, not_3_out,
       not_4_out, not_5_out, not_6_out, or_1_out, or_2_out, or_3_out, or_5_out, or_6_out, or_7_out, or_8_out,
       or_9_out, or_10_out, pull_resistor_3_node, subtractor_2_bout, subtractor_3_bout, subtractor_4_bout,
       xnor_1_out, xor_1_out, xor_3_out;
  wire [4:0] bit_extender_1_out, bit_extender_8_out, bitfinder_1_index, bitfinder_4_index, multiplexer_5_out,
       multiplexer_8_out, multiplexer_12_out, negator_2_out, negator_3_out, subtractor_2_out,
       subtractor_3_out, subtractor_7_out;
  wire [7:0] adder_1_out, adder_2_out, adder_3_out, adder_4_out, bit_extender_2_out, bit_extender_9_out,
       multiplexer_2_out, multiplexer_4_out, multiplexer_6_out, multiplexer_7_out, multiplexer_10_out,
       multiplexer_11_out, multiplexer_15_out, multiplexer_16_out, negator_4_out, subtractor_1_out,
       subtractor_4_out, subtractor_5_out;
  wire [22:0] bit_extender_5_out, bit_extender_6_out, bit_extender_10_out;
  wire [23:0] divider_1_out, multiplexer_9_out, multiplier_1_cout, shifter_1_out, shifter_2_out;
  wire [23:23] bitfinder_2_found;
  wire [30:0] adder_5_out, bit_extender_3_out, bit_extender_4_out, multiplexer_13_out, multiplexer_14_out,
       multiplexer_22_out, multiplexer_23_out, multiplexer_26_out, shifter_5_out, shifter_8_out,
       subtractor_6_out;
  wire [31:0] bit_extender_7_out, controlled_buffer_1_out, controlled_buffer_5_out, controlled_buffer_6_out,
       multiplexer_1_out, multiplexer_3_out, multiplexer_17_out, multiplexer_24_out, multiplexer_25_out,
       negator_1_out, negator_5_out, pull_resistor_1_node, shifter_3_out, shifter_4_out, shifter_6_out,
       shifter_7_out;
  wire [31:31] not_1_out, or_4_out, xor_2_out;

  assign controlled_buffer_1_out = in_3[5] ? in_1 : 32'bz;  // Controlled_Buffer controlled_buffer_1
  Pull_Resistor pull_resistor_1 (.node(pull_resistor_1_node));
  assign pull_resistor_1_node = in_3[5] ? in_2 : 32'bz;  // Controlled_Buffer controlled_buffer_2
  Pull_Resistor pull_resistor_2 (.node(controlled_buffer_1_out));
  Multiplexer #(.width(32), .enable("false")) multiplexer_1 (
    .in0(pull_resistor_1_node), .in1(32'h3f800000), .out(multiplexer_1_out), .sel(or_1_out));
  or or_1 (or_1_out, decoder_1_out11, decoder_1_out12);
  BitFinder #(.width(32), .\type ("high1")) bitfinder_1 (
    .in(multiplexer_3_out), .index(bitfinder_1_index), .found(bitfinder_1_found));
  Negator #(.width(32)) negator_1 (.in(controlled_buffer_1_out), .out(negator_1_out));
  Subtractor subtractor_1 (.a(controlled_buffer_1_out[30:23]), .b(8'h7f), .out(subtractor_1_out));  // open: bin, bout
  not not_1 (not_1_out[31], controlled_buffer_1_out[31]);
  Multiplexer #(.width(8), .enable("false")) multiplexer_2 (
    .in0(8'h1), .in1({8{1'b1}}), .out(multiplexer_2_out), .sel(decoder_1_out5));
  or or_2 (or_2_out, decoder_1_out1, decoder_1_out12);
  Subtractor #(.width(5)) subtractor_2 (
    .a(5'b10111), .b(bitfinder_1_index), .out(subtractor_2_out), .bout(subtractor_2_bout));  // open: bin
  Multiplexer #(.width(32), .disabled(0), .enable("false")) multiplexer_3 (
    .in0(controlled_buffer_1_out), .in1(negator_1_out), .out(multiplexer_3_out),
    .sel(controlled_buffer_1_out[31]));
  Bit_Extender #(.out_width(5)) bit_extender_1 (.in(subtractor_1_out), .out(bit_extender_1_out));
  Adder adder_1 (.a(controlled_buffer_1_out[30:23]), .b(multiplexer_2_out), .out(adder_1_out));  // open: cin, cout
  and and_1 (and_1_out, comparator_1_eq, not_3_out);
  xor xor_1 (xor_1_out, or_2_out, multiplexer_1_out[31]);
  Comparator #(.width(23)) comparator_1 (
    .a(controlled_buffer_1_out[22:0]), .b(multiplexer_1_out[22:0]), .eq(comparator_1_eq), .lt(comparator_1_lt));  // open: gt
  Multiplexer #(.width(8), .enable("false")) multiplexer_4 (
    .in0(controlled_buffer_1_out[30:23]), .in1(multiplexer_1_out[30:23]), .out(multiplexer_4_out),
    .sel(subtractor_4_bout));
  xor xor_2 (xor_2_out[31], controlled_buffer_1_out[31], pull_resistor_1_node[31]);
  Divider #(.width(24)) divider_1 (
    .a({24{1'b0}}), .b({1'b1, pull_resistor_1_node[22:0]}), .out(divider_1_out),
    .upper({1'b1, controlled_buffer_1_out[22:0]}));  // open: rem
  Multiplier #(.width(24)) multiplier_1 (
    .a({1'b1, controlled_buffer_1_out[22:0]}), .b({1'b1, pull_resistor_1_node[22:0]}),
    .cout(multiplier_1_cout));  // open: out, cin
  Multiplexer #(.width(5), .enable("false")) multiplexer_5 (
    .in0(5'b00001), .in1({5{1'b0}}), .out(multiplexer_5_out), .sel(multiplier_1_cout[23]));
  Multiplexer #(.width(8), .enable("false")) multiplexer_6 (
    .in0(controlled_buffer_1_out[30:23]), .in1(subtractor_5_out), .out(multiplexer_6_out),
    .sel(decoder_1_out3));
  Multiplexer #(.width(8), .enable("false")) multiplexer_7 (
    .in0(adder_2_out), .in1(controlled_buffer_1_out[30:23]), .out(multiplexer_7_out), .sel(decoder_1_out3));
  xnor xnor_1 (xnor_1_out, controlled_buffer_1_out[31], pull_resistor_1_node[31]);
  Comparator #(.width(23), .mode("unsigned")) comparator_2 (
    .a(controlled_buffer_1_out[22:0]), .b(pull_resistor_1_node[22:0]), .gt(comparator_2_gt),
    .eq(comparator_2_eq), .lt(comparator_2_lt));
  Comparator comparator_3 (
    .a(controlled_buffer_1_out[30:23]), .b(pull_resistor_1_node[30:23]), .gt(comparator_3_gt),
    .eq(comparator_3_eq), .lt(comparator_3_lt));
  and and_2 (and_2_out, pull_resistor_1_node[31], ~controlled_buffer_1_out[31]);  // AND_Gate
  Multiplexer #(.width(5), .disabled(0), .enable("false")) multiplexer_8 (
    .in0(subtractor_2_out), .in1(negator_2_out), .out(multiplexer_8_out), .sel(pull_resistor_3_node));
  Negator #(.width(5)) negator_2 (.in(subtractor_2_out), .out(negator_2_out));
  not not_2 (not_2_out, pull_resistor_3_node);
  Pull_Resistor pull_resistor_3 (.node(pull_resistor_3_node));
  assign pull_resistor_3_node = bitfinder_1_found ? subtractor_2_bout : 1'bz;  // Controlled_Buffer controlled_buffer_3
  assign bit_extender_2_out = {{3{1'b0}}, bitfinder_1_index};  // Bit_Extender bit_extender_2
  Subtractor #(.width(5)) subtractor_3 (
    .a(5'b10111), .b(bit_extender_1_out), .out(subtractor_3_out), .bout(subtractor_3_bout));  // open: bin
  assign controlled_buffer_4_out = bitfinder_2_found[23] ? subtractor_3_bout : 1'bz;  // Controlled_Buffer controlled_buffer_4
  BitFinder #(.width(32), .\type ("high1")) bitfinder_2 (
    .in(controlled_buffer_1_out), .found(bitfinder_2_found[23]));  // open: index
  and and_3 (and_3_out, xor_1_out, ~controlled_buffer_1_out[31], or_3_out);  // AND_Gate
  and and_4 (and_4_out, controlled_buffer_1_out[31], ~xor_1_out, ~or_3_out);  // AND_Gate
  or or_3 (or_3_out, and_5_out, subtractor_4_bout);
  and and_5 (and_5_out, comparator_1_lt, not_3_out);
  not not_3 (not_3_out, bitfinder_3_found);
  BitFinder #(.\type ("high1")) bitfinder_3 (.in(subtractor_4_out), .found(bitfinder_3_found));  // open: index
  Subtractor subtractor_4 (
    .a(controlled_buffer_1_out[30:23]), .b(multiplexer_1_out[30:23]), .out(subtractor_4_out),
    .bout(subtractor_4_bout));  // open: bin
  Shifter #(.width(24), .shift("lr")) shifter_1 (.in(divider_1_out), .\dist (5'b00001), .out(shifter_1_out));
  Multiplexer #(.width(24), .enable("false")) multiplexer_9 (
    .in0(shifter_1_out), .in1(shifter_2_out), .out(multiplexer_9_out), .sel(not_4_out));
  Shifter #(.width(24)) shifter_2 (.in(multiplier_1_cout), .\dist (multiplexer_5_out), .out(shifter_2_out));
  not not_4 (not_4_out, decoder_1_out3);
  Multiplexer #(.width(8), .enable("false")) multiplexer_10 (
    .in0(pull_resistor_1_node[30:23]), .in1(8'h7f), .out(multiplexer_10_out), .sel(decoder_1_out3));
  Adder adder_2 (.a(multiplexer_10_out), .b(multiplexer_6_out), .out(adder_2_out), .cin(not_4_out));  // open: cout
  Subtractor subtractor_5 (.a(multiplexer_7_out), .b(multiplexer_11_out), .out(subtractor_5_out));  // open: bin, bout
  Multiplexer #(.width(8), .enable("false")) multiplexer_11 (
    .in0(8'h7f), .in1(pull_resistor_1_node[30:23]), .out(multiplexer_11_out), .sel(decoder_1_out3));
  and and_6 (and_6_out, comparator_2_gt, comparator_3_eq);
  and and_7 (and_7_out, comparator_2_lt, comparator_3_eq);
  and and_8 (and_8_out, ~pull_resistor_1_node[31], controlled_buffer_1_out[31]);  // AND_Gate
  Shifter #(.width(32), .shift("lr")) shifter_3 (
    .in(multiplexer_3_out), .\dist (multiplexer_8_out), .out(shifter_3_out));
  Shifter #(.width(32)) shifter_4 (.in(multiplexer_3_out), .\dist (multiplexer_8_out), .out(shifter_4_out));
  Adder adder_3 (.a(8'h7f), .b(bit_extender_2_out), .out(adder_3_out));  // open: cin, cout
  Multiplexer #(.width(5), .disabled(0), .enable("false")) multiplexer_12 (
    .in0(subtractor_3_out), .in1(negator_3_out), .out(multiplexer_12_out), .sel(controlled_buffer_4_out));
  Negator #(.width(5)) negator_3 (.in(subtractor_3_out), .out(negator_3_out));
  or or_4 (or_4_out[31], and_3_out, and_4_out, and_9_out);
  and and_9 (and_9_out, controlled_buffer_1_out[31], xor_1_out);
  xor xor_3 (xor_3_out, controlled_buffer_1_out[31], xor_1_out);
  Multiplexer #(.width(31), .enable("false")) multiplexer_13 (
    .in0(bit_extender_3_out), .in1(bit_extender_4_out), .out(multiplexer_13_out), .sel(subtractor_4_bout));
  Multiplexer #(.width(31), .enable("false")) multiplexer_14 (
    .in0(bit_extender_4_out), .in1(bit_extender_3_out), .out(multiplexer_14_out), .sel(subtractor_4_bout));
  assign bit_extender_3_out = {{7{1'b0}}, {1'b1, controlled_buffer_1_out[22:0]}};  // Bit_Extender bit_extender_3
  assign bit_extender_4_out = {{7{1'b0}}, {1'b1, multiplexer_1_out[22:0]}};  // Bit_Extender bit_extender_4
  Multiplexer #(.width(8), .enable("false")) multiplexer_15 (
    .in0(subtractor_4_out), .in1(negator_4_out), .out(multiplexer_15_out), .sel(subtractor_4_bout));
  Negator negator_4 (.in(subtractor_4_out), .out(negator_4_out));
  Bit_Extender #(.in_width(24), .out_width(23)) bit_extender_5 (.in(multiplexer_9_out), .out(bit_extender_5_out));
  Multiplexer #(.width(8), .enable("false")) multiplexer_16 (
    .in0(adder_2_out), .in1(subtractor_5_out), .out(multiplexer_16_out), .sel(not_4_out));
  or or_5 (or_5_out, comparator_3_gt, and_6_out);
  not not_5 (not_5_out, xnor_1_out);
  and and_10 (out_6, comparator_2_eq, xnor_1_out, comparator_3_eq);
  or or_6 (or_6_out, and_7_out, comparator_3_lt);
  Multiplexer #(.width(32), .disabled(0), .enable("false")) multiplexer_17 (
    .in0(shifter_3_out), .in1(shifter_4_out), .out(multiplexer_17_out), .sel(not_2_out));
  Bit_Extender #(.in_width(32), .out_width(23)) bit_extender_6 (.in(multiplexer_17_out), .out(bit_extender_6_out));
  assign bit_extender_7_out = {{8{1'b0}}, {bitfinder_2_found[23], controlled_buffer_1_out[22:0]}};  // Bit_Extender bit_extender_7
  Pull_Resistor pull_resistor_4 (.node(controlled_buffer_4_out));
  not not_6 (not_6_out, xor_3_out);
  Comparator #(.width(31)) comparator_4 (
    .a(multiplexer_13_out), .b(shifter_5_out), .lt(comparator_4_lt));  // open: gt, eq
  Shifter #(.width(31), .shift("lr")) shifter_5 (
    .in(multiplexer_14_out), .\dist (bit_extender_8_out), .out(shifter_5_out));
  Bit_Extender #(.out_width(5)) bit_extender_8 (.in(multiplexer_15_out), .out(bit_extender_8_out));
  assign bit_extender_9_out = {{3{1'b0}}, subtractor_7_out};  // Bit_Extender bit_extender_9
  Multiplexer #(.enable("false")) multiplexer_18 (
    .in0(or_5_out), .in1(and_2_out), .out(multiplexer_18_out), .sel(not_5_out));
  Multiplexer #(.enable("false")) multiplexer_19 (
    .in0(multiplexer_18_out), .in1(multiplexer_20_out), .out(out_5), .sel(and_11_out));
  Multiplexer #(.enable("false")) multiplexer_20 (
    .in0(or_6_out), .in1(and_8_out), .out(multiplexer_20_out), .sel(not_5_out));
  Multiplexer #(.enable("false")) multiplexer_21 (
    .in0(multiplexer_20_out), .in1(multiplexer_18_out), .out(multiplexer_21_out), .sel(and_11_out));
  and and_11 (and_11_out, pull_resistor_1_node[31], controlled_buffer_1_out[31]);
  assign controlled_buffer_5_out = bitfinder_1_found ? {controlled_buffer_1_out[31], adder_3_out, bit_extender_6_out} : 32'bz;  // Controlled_Buffer controlled_buffer_5
  Shifter #(.width(32), .shift("lr")) shifter_6 (
    .in(bit_extender_7_out), .\dist (multiplexer_12_out), .out(shifter_6_out));
  Shifter #(.width(32)) shifter_7 (.in(bit_extender_7_out), .\dist (multiplexer_12_out), .out(shifter_7_out));
  Multiplexer #(.width(31), .enable("false")) multiplexer_22 (
    .in0(multiplexer_13_out), .in1(shifter_5_out), .out(multiplexer_22_out), .sel(comparator_4_lt));
  Multiplexer #(.width(31), .enable("false")) multiplexer_23 (
    .in0(shifter_5_out), .in1(multiplexer_13_out), .out(multiplexer_23_out), .sel(comparator_4_lt));
  BitFinder #(.width(31), .\type ("high1")) bitfinder_4 (
    .in(multiplexer_26_out), .index(bitfinder_4_index));  // open: found
  Bit_Extender #(.in_width(31), .out_width(23)) bit_extender_10 (.in(shifter_8_out), .out(bit_extender_10_out));
  Adder adder_4 (.a(bit_extender_9_out), .b(multiplexer_4_out), .out(adder_4_out));  // open: cin, cout
  or or_7 (or_7_out, or_9_out, decoder_1_out5);
  or or_8 (or_8_out, decoder_1_out2, decoder_1_out3);
  or or_9 (or_9_out, decoder_1_out0, decoder_1_out1);
  Decoder #(.select(4), .disabled(0)) decoder_1 (
    .out0(decoder_1_out0), .out1(decoder_1_out1), .out2(decoder_1_out2), .out3(decoder_1_out3),
    .out4(decoder_1_out4), .out5(decoder_1_out5), .out6(decoder_1_out6), .out7(decoder_1_out7),
    .out11(decoder_1_out11), .out12(decoder_1_out12), .out13(decoder_1_out13), .sel(in_3[3:0]), .en(in_3[4]));  // open: out8, out9, out10, out14, out15
  Multiplexer #(.width(32), .disabled(0), .enable("false")) multiplexer_24 (
    .in0(shifter_6_out), .in1(shifter_7_out), .out(multiplexer_24_out), .sel(controlled_buffer_4_out));
  Negator #(.width(32)) negator_5 (.in(multiplexer_24_out), .out(negator_5_out));
  Subtractor #(.width(31)) subtractor_6 (
    .a(multiplexer_22_out), .b(multiplexer_23_out), .out(subtractor_6_out));  // open: bin, bout
  Adder #(.width(31)) adder_5 (.a(multiplexer_22_out), .b(multiplexer_23_out), .out(adder_5_out));  // open: cin, cout
  Subtractor #(.width(5)) subtractor_7 (
    .a(bitfinder_4_index), .b(5'b10111), .out(subtractor_7_out));  // open: bin, bout
  or or_10 (or_10_out, decoder_1_out4, decoder_1_out5);
  or or_11 (decoder_1_out5, decoder_1_out11, decoder_1_out12);
  Multiplexer #(.width(32), .disabled(0), .enable("false")) multiplexer_25 (
    .in0(multiplexer_24_out), .in1(negator_5_out), .out(multiplexer_25_out), .sel(controlled_buffer_1_out[31]));
  Multiplexer #(.width(31), .enable("false")) multiplexer_26 (
    .in0(subtractor_6_out), .in1(adder_5_out), .out(multiplexer_26_out), .sel(not_6_out));
  Shifter #(.width(31), .shift("lr")) shifter_8 (
    .in(multiplexer_26_out), .\dist (subtractor_7_out), .out(shifter_8_out));
  assign controlled_buffer_6_out = and_1_out ? {or_4_out[31], adder_4_out, bit_extender_10_out} : 32'bz;  // Controlled_Buffer controlled_buffer_6
  assign out_4 = decoder_1_out6 ? controlled_buffer_5_out : 32'bz;  // Controlled_Buffer controlled_buffer_7
  assign out_4 = decoder_1_out7 ? multiplexer_25_out : 32'bz;  // Controlled_Buffer controlled_buffer_8
  assign out_4 = decoder_1_out13 ? {not_1_out[31], controlled_buffer_1_out[30:0]} : 32'bz;  // Controlled_Buffer controlled_buffer_9
  assign out_4 = or_10_out ? {controlled_buffer_1_out[31], adder_1_out, controlled_buffer_1_out[22:0]} : 32'bz;  // Controlled_Buffer controlled_buffer_10
  assign out_4 = or_7_out ? controlled_buffer_6_out : 32'bz;  // Controlled_Buffer controlled_buffer_11
  assign out_4 = or_8_out ? {xor_2_out[31], multiplexer_16_out, bit_extender_5_out} : 32'bz;  // Controlled_Buffer controlled_buffer_12

  // Notes on the sheet:
  //   INT TO FLOAT
  //   FLOAT TO INT
  //   SHIFT
  //   0-LEFT
  //   1-RIGHT
  //   0-ADD
  //   1-SUB
  //   NEGATE
  //   0-MULT
  //   1-DIV
  //   COMP
endmodule
